// Logisim project ym2610.circ as structural Verilog: 69 circuits, main circuit ym2610
module ym2610 (
  input  in_1
);

  wire clk_gen_1_clk1, clk_gen_1_clk2, clock_1_out, controlled_buffer_1_out, controlled_buffer_9_out,
       not_1_out, not_2_out, undriven;
  wire [8:0] write_data_1_nvalout, write_data_1_valout;

  Clock clock_1 (.out(clock_1_out));
  clk_gen clk_gen_1 (.MCLK(clock_1_out), .clk1(clk_gen_1_clk1), .clk2(clk_gen_1_clk2));
  // NOT_Gate not_1 has open pins: in=open, out=not_1_out
  not not_2 (not_2_out, not_1_out);
  assign controlled_buffer_1_out = not_2_out ? write_data_1_nvalout[0] : 1'bz;  // Controlled_Buffer controlled_buffer_1
  assign controlled_buffer_1_out = not_2_out ? write_data_1_nvalout[1] : 1'bz;  // Controlled_Buffer controlled_buffer_2
  assign controlled_buffer_1_out = not_2_out ? write_data_1_nvalout[2] : 1'bz;  // Controlled_Buffer controlled_buffer_3
  assign controlled_buffer_1_out = not_2_out ? write_data_1_nvalout[3] : 1'bz;  // Controlled_Buffer controlled_buffer_4
  Controlled_Buffer controlled_buffer_5 (.out(controlled_buffer_1_out), .en(not_2_out));  // open: in
  assign controlled_buffer_1_out = not_2_out ? write_data_1_nvalout[5] : 1'bz;  // Controlled_Buffer controlled_buffer_6
  Controlled_Buffer controlled_buffer_7 (.out(controlled_buffer_1_out), .en(not_2_out));  // open: in
  Controlled_Buffer controlled_buffer_8 (.out(controlled_buffer_1_out), .en(not_2_out));  // open: in
  clk_div clk_div_1 (
    .clk1(clk_gen_1_clk1), .clk2(clk_gen_1_clk2), .IC(in_1));  // open: fm_clk1, fm_clk2, res_latch1, res_latch2, out_8, out_9, out_10, out_11, out_12, out_13, out_14
  write_data write_data_1 (
    .valout(write_data_1_valout), .nvalout(write_data_1_nvalout));  // open: data_in, bank, write, oe
  assign controlled_buffer_9_out = undriven ? write_data_1_valout[0] : 1'bz;  // Controlled_Buffer controlled_buffer_9
  assign controlled_buffer_9_out = undriven ? write_data_1_valout[1] : 1'bz;  // Controlled_Buffer controlled_buffer_10
  assign controlled_buffer_9_out = undriven ? write_data_1_valout[2] : 1'bz;  // Controlled_Buffer controlled_buffer_11
  assign controlled_buffer_9_out = undriven ? write_data_1_valout[3] : 1'bz;  // Controlled_Buffer controlled_buffer_12
  assign controlled_buffer_9_out = undriven ? write_data_1_valout[4] : 1'bz;  // Controlled_Buffer controlled_buffer_13
  assign controlled_buffer_9_out = undriven ? write_data_1_valout[5] : 1'bz;  // Controlled_Buffer controlled_buffer_14
  assign controlled_buffer_9_out = undriven ? write_data_1_valout[6] : 1'bz;  // Controlled_Buffer controlled_buffer_15
  assign controlled_buffer_9_out = undriven ? write_data_1_valout[7] : 1'bz;  // Controlled_Buffer controlled_buffer_16
  reg_glob reg_glob_1 ();  // open: clk1, clk2, write_data, write_data_neg, addr_wr, data_wr, IC, sync, ch3_sel, sync_timer, data, write40, write70, write50, write60, write80, write30, write90, writeB0, writeAC, writeA0, writeA4, writeA8, writeB4, sel, busy, op_reg_bank, kon, kon_csm, timer_a_status, timer_b_status, test1, lfo, lfo_en, ch3_ext, test2, reg_1c_0, reg_1c_7
  fsm fsm_1 ();  // open: clk1, clk2, fsm_reset, algorithm, op1_sel, op2_mod, last_op_2, last_op_1, op2_sel, op1_1, op_output, do_feedback, sync_eg, sync_timers, sync_dbg, sync_accm, sync23, ch3_sel, out_19, out_20, out_21
  reg_op reg_op_1 ();  // open: clk1, clk2, data, eg_state, ic, out_sel, wr_sel, write90, write30, write40, write50, write60, write70, write80, ssg_enable, ssg_inv, ssg_b0, ssg_0_or_4, ssg_2_or_6, ssg_3_or_7, ssg_3_or_5, detune, multi, tl, ks, rate, am, sl
  reg_chan reg_chan_1 ();  // open: clk1, clk2, data, IC, writeA0, writeA8, writeA4, writeAC, writeB0, writeB4, sync, ch3ext, am, fnum, blk, note, algorithm, fb, pms, ams, pan
  // also tied to GND on the sheet: {controlled_buffer_1_out, controlled_buffer_9_out}
endmodule

module ym2612 (
  input  in_1,
  output out_2,
  output out_3
);

  wire clk_gen_1_clk1, clk_gen_1_clk2, clock_1_out, controlled_buffer_1_out, undriven;
  wire [8:0] write_data_1_valout;

  Clock clock_1 (.out(clock_1_out));
  clk_gen clk_gen_1 (.MCLK(clock_1_out), .clk1(clk_gen_1_clk1), .clk2(clk_gen_1_clk2));
  clk_div_2612 clk_div_2612_1 (
    .clk1(clk_gen_1_clk1), .clk2(clk_gen_1_clk2), .IC(in_1), .fm_clk1(out_2), .fm_clk2(out_3));  // open: res_latch1
  write_data write_data_1 (.valout(write_data_1_valout));  // open: data_in, bank, write, oe, nvalout
  assign controlled_buffer_1_out = undriven ? write_data_1_valout[0] : 1'bz;  // Controlled_Buffer controlled_buffer_1
  assign controlled_buffer_1_out = undriven ? write_data_1_valout[1] : 1'bz;  // Controlled_Buffer controlled_buffer_2
  assign controlled_buffer_1_out = undriven ? write_data_1_valout[2] : 1'bz;  // Controlled_Buffer controlled_buffer_3
  assign controlled_buffer_1_out = undriven ? write_data_1_valout[3] : 1'bz;  // Controlled_Buffer controlled_buffer_4
  assign controlled_buffer_1_out = undriven ? write_data_1_valout[4] : 1'bz;  // Controlled_Buffer controlled_buffer_5
  assign controlled_buffer_1_out = undriven ? write_data_1_valout[5] : 1'bz;  // Controlled_Buffer controlled_buffer_6
  assign controlled_buffer_1_out = undriven ? write_data_1_valout[6] : 1'bz;  // Controlled_Buffer controlled_buffer_7
  assign controlled_buffer_1_out = undriven ? write_data_1_valout[7] : 1'bz;  // Controlled_Buffer controlled_buffer_8
  reg_glob_2612 reg_glob_2612_1 ();  // open: clk1, clk2, write_data, write_data_neg, addr_wr, data_wr, IC, sync, ch3_sel, sync_timer, data, write40, write70, write50, write60, write80, write30, write90, writeB0, writeAC, writeA0, writeA4, writeA8, writeB4, sel, busy, op_reg_bank, kon, kon_csm, timer_a_status, timer_b_status, test1, lfo, lfo_en, ch3_ext, test2, dac, dac_en
  fsm_2612 fsm_2612_1 ();  // open: clk1, clk2, fsm_reset, algorithm, op1_sel, op2_mod, last_op_2, last_op_1, op2_sel, op1_1, op_output, do_feedback, sync_eg, sync_timers, sync_dbg, sync23, ch3_sel, dac_ch6_sel, dac_load, dac_out_sel
  reg_op reg_op_1 ();  // open: clk1, clk2, data, eg_state, ic, out_sel, wr_sel, write90, write30, write40, write50, write60, write70, write80, ssg_enable, ssg_inv, ssg_b0, ssg_0_or_4, ssg_2_or_6, ssg_3_or_7, ssg_3_or_5, detune, multi, tl, ks, rate, am, sl
  reg_chan reg_chan_1 ();  // open: clk1, clk2, data, IC, writeA0, writeA8, writeA4, writeAC, writeB0, writeB4, sync, ch3ext, am, fnum, blk, note, algorithm, fb, pms, ams, pan
  // also tied to GND on the sheet: controlled_buffer_1_out
endmodule

module sr_bit (
  input  val,
  input  clk1,
  input  clk2,
  output valout,
  output nvalout
);

  wire d_ff_1_q;

  D_Flip_Flop #(.trigger("high")) d_ff_1 (.D(val), .clk(clk1), .Q(d_ff_1_q));  // open: Qn, preset, reset
  D_Flip_Flop #(.trigger("high")) d_ff_2 (.D(d_ff_1_q), .clk(clk2), .Q(valout), .Qn(nvalout));  // open: preset, reset
endmodule

module reg_bit_1 (
  input  oe,
  input  val,
  input  write,
  output nvalout,
  output valout
);

  wire d_ff_1_q, nor_1_out, nor_2_out;

  D_Flip_Flop #(.trigger("high")) d_ff_1 (.D(val), .clk(write), .Q(d_ff_1_q));  // open: Qn, preset, reset
  nor nor_1 (nor_1_out, oe, d_ff_1_q);
  nor nor_2 (nor_2_out, oe, nor_1_out);
  assign nvalout = nor_1_out ? 1'b1 : 1'bz;  // Controlled_Buffer controlled_buffer_1
  assign nvalout = nor_2_out ? 1'b0 : 1'bz;  // Controlled_Buffer controlled_buffer_2
  assign valout = nor_2_out ? 1'b1 : 1'bz;  // Controlled_Buffer controlled_buffer_3
  assign valout = nor_1_out ? 1'b0 : 1'bz;  // Controlled_Buffer controlled_buffer_4

  // Notes on the sheet:
  //   dynamic latch!!!
endmodule

module read_bus_1 (
  input  val,
  input  enable,
  output valout
);

  wire nor_1_out, nor_2_out;

  nor nor_1 (nor_1_out, val, enable);
  nor nor_2 (nor_2_out, nor_1_out, enable);
  assign valout = nor_2_out ? 1'b1 : 1'bz;  // Controlled_Buffer controlled_buffer_1
  assign valout = nor_1_out ? 1'b0 : 1'bz;  // Controlled_Buffer controlled_buffer_2
endmodule

module write_data (
  input  [7:0] data_in,
  input  bank,
  input  write,
  input  oe,
  output [8:0] valout,
  output [8:0] nvalout
);

  reg_bit_1 reg_bit_1_1 (.oe(oe), .val(data_in[0]), .write(write), .nvalout(nvalout[0]), .valout(valout[0]));
  reg_bit_1 reg_bit_1_2 (.oe(oe), .val(data_in[1]), .write(write), .nvalout(nvalout[1]), .valout(valout[1]));
  reg_bit_1 reg_bit_1_3 (.oe(oe), .val(data_in[2]), .write(write), .nvalout(nvalout[2]), .valout(valout[2]));
  reg_bit_1 reg_bit_1_4 (.oe(oe), .val(data_in[3]), .write(write), .nvalout(nvalout[3]), .valout(valout[3]));
  reg_bit_1 reg_bit_1_5 (.oe(oe), .val(data_in[4]), .write(write), .nvalout(nvalout[4]), .valout(valout[4]));
  reg_bit_1 reg_bit_1_6 (.oe(oe), .val(data_in[5]), .write(write), .nvalout(nvalout[5]), .valout(valout[5]));
  reg_bit_1 reg_bit_1_7 (.oe(oe), .val(data_in[6]), .write(write), .nvalout(nvalout[6]), .valout(valout[6]));
  reg_bit_1 reg_bit_1_8 (.oe(oe), .val(data_in[7]), .write(write), .nvalout(nvalout[7]), .valout(valout[7]));
  reg_bit_1 reg_bit_1_9 (.oe(oe), .val(bank), .write(write), .nvalout(nvalout[8]), .valout(valout[8]));
endmodule

module clk_gen (
  input  MCLK,
  output clk1,
  output clk2
);

  wire not_1_out, not_2_out, not_3_out, not_4_out, not_5_out, not_6_out, not_7_out;

  not not_1 (not_1_out, MCLK);
  not not_2 (not_2_out, not_1_out);
  not not_3 (not_3_out, not_2_out);
  nor nor_1 (clk1, not_2_out, not_7_out);
  nor nor_2 (clk2, not_3_out, not_6_out);
  not not_4 (not_4_out, clk1);
  not not_5 (not_5_out, clk2);
  not not_6 (not_6_out, not_4_out);
  not not_7 (not_7_out, not_5_out);
endmodule

module clk_div (
  input  clk1,
  input  clk2,
  input  IC,
  output fm_clk1,
  output fm_clk2,
  output res_latch1,
  output res_latch2,
  output out_8,
  output out_9,
  output out_10,
  output out_11,
  output out_12,
  output out_13,
  output out_14
);

  wire nor_1_out, nor_2_out, nor_3_out, nor_4_out, nor_5_out, nor_6_out, nor_7_out, nor_8_out, nor_9_out,
       nor_10_out, nor_11_out, not_1_out, not_2_out, not_3_out, not_6_out, not_9_out, not_12_out, not_13_out,
       not_14_out, not_15_out, not_16_out, not_17_out, not_18_out, not_19_out, not_20_out, sr_bit_1_valout,
       sr_bit_2_valout, sr_bit_3_valout, sr_bit_4_valout, sr_bit_5_valout, sr_bit_6_valout, sr_bit_7_valout,
       sr_bit_8_valout, sr_bit_9_valout, sr_bit_10_valout, sr_bit_11_valout, sr_bit_12_valout,
       sr_bit_13_valout, sr_bit_14_valout, sr_bit_15_valout, sr_bit_16_valout, sr_bit_17_valout,
       sr_bit_18_valout, sr_bit_19_valout, sr_bit_20_valout, sr_bit_21_valout, sr_bit_22_valout,
       sr_bit_23_valout, sr_bit_24_valout, sr_bit_25_valout, sr_bit_26_valout, sr_bit_27_valout,
       sr_bit_28_valout, sr_bit_29_valout, sr_bit_30_valout, sr_bit_31_valout, sr_bit_32_valout,
       sr_bit_33_valout, sr_bit_34_valout, sr_bit_35_valout, sr_bit_36_valout, sr_bit_37_valout,
       sr_bit_38_valout, sr_bit_39_valout, sr_bit_40_valout, sr_bit_41_valout, sr_bit_42_valout;

  sr_bit sr_bit_1 (.clk1(clk1), .clk2(clk2), .val(IC), .valout(sr_bit_1_valout));  // open: nvalout
  nor nor_1 (nor_1_out, not_3_out, not_20_out);
  sr_bit sr_bit_2 (.clk1(clk1), .clk2(clk2), .val(sr_bit_1_valout), .valout(sr_bit_2_valout));  // open: nvalout
  sr_bit sr_bit_3 (.clk1(clk1), .clk2(clk2), .val(nor_1_out), .valout(sr_bit_3_valout));  // open: nvalout
  sr_bit sr_bit_4 (.clk1(clk1), .clk2(clk2), .val(sr_bit_2_valout), .valout(sr_bit_4_valout));  // open: nvalout
  not not_1 (not_1_out, sr_bit_1_valout);
  sr_bit sr_bit_5 (.clk1(clk1), .clk2(clk2), .val(sr_bit_3_valout), .valout(sr_bit_5_valout));  // open: nvalout
  sr_bit sr_bit_6 (.clk1(clk1), .clk2(clk2), .val(sr_bit_4_valout), .valout(sr_bit_6_valout));  // open: nvalout
  sr_bit sr_bit_7 (.clk1(clk1), .clk2(clk2), .val(sr_bit_6_valout), .valout(sr_bit_7_valout));  // open: nvalout
  nor nor_2 (nor_2_out, sr_bit_42_valout, not_1_out);
  not not_2 (not_2_out, nor_2_out);
  sr_bit sr_bit_8 (.clk1(clk1), .clk2(clk2), .val(sr_bit_5_valout), .valout(sr_bit_8_valout));  // open: nvalout
  sr_bit sr_bit_9 (.clk1(clk1), .clk2(clk2), .val(sr_bit_8_valout), .valout(sr_bit_9_valout));  // open: nvalout
  sr_bit sr_bit_10 (.clk1(clk1), .clk2(clk2), .val(sr_bit_7_valout), .valout(sr_bit_10_valout));  // open: nvalout
  sr_bit sr_bit_11 (.clk1(clk1), .clk2(clk2), .val(not_2_out), .valout(sr_bit_11_valout));  // open: nvalout
  sr_bit sr_bit_12 (.clk1(clk1), .clk2(clk2), .val(sr_bit_9_valout), .valout(sr_bit_12_valout));  // open: nvalout
  sr_bit sr_bit_13 (.clk1(clk1), .clk2(clk2), .val(sr_bit_10_valout), .valout(sr_bit_13_valout));  // open: nvalout
  sr_bit sr_bit_14 (.clk1(clk1), .clk2(clk2), .val(sr_bit_11_valout), .valout(sr_bit_14_valout));  // open: nvalout
  sr_bit sr_bit_15 (.clk1(clk1), .clk2(clk2), .val(sr_bit_12_valout), .valout(sr_bit_15_valout));  // open: nvalout
  sr_bit sr_bit_16 (.clk1(clk1), .clk2(clk2), .val(sr_bit_13_valout), .valout(sr_bit_16_valout));  // open: nvalout
  not not_3 (not_3_out, not_2_out);
  sr_bit sr_bit_17 (.clk1(clk1), .clk2(clk2), .val(sr_bit_14_valout), .valout(sr_bit_17_valout));  // open: nvalout
  sr_bit sr_bit_18 (.clk1(clk1), .clk2(clk2), .val(sr_bit_16_valout), .valout(sr_bit_18_valout));  // open: nvalout
  not not_4 (res_latch2, sr_bit_17_valout);
  sr_bit sr_bit_19 (.clk1(clk1), .clk2(clk2), .val(sr_bit_15_valout), .valout(sr_bit_19_valout));  // open: nvalout
  sr_bit sr_bit_20 (.clk1(clk1), .clk2(clk2), .val(sr_bit_18_valout), .valout(sr_bit_20_valout));  // open: nvalout
  sr_bit sr_bit_21 (.clk1(clk1), .clk2(clk2), .val(sr_bit_17_valout), .valout(sr_bit_21_valout));  // open: nvalout
  sr_bit sr_bit_22 (.clk1(clk1), .clk2(clk2), .val(sr_bit_19_valout), .valout(sr_bit_22_valout));  // open: nvalout
  sr_bit sr_bit_23 (.clk1(clk1), .clk2(clk2), .val(sr_bit_20_valout), .valout(sr_bit_23_valout));  // open: nvalout
  not not_5 (res_latch1, sr_bit_21_valout);
  sr_bit sr_bit_24 (.clk1(clk1), .clk2(clk2), .val(sr_bit_22_valout), .valout(sr_bit_24_valout));  // open: nvalout
  sr_bit sr_bit_25 (.clk1(clk1), .clk2(clk2), .val(sr_bit_23_valout), .valout(sr_bit_25_valout));  // open: nvalout
  sr_bit sr_bit_26 (.clk1(clk1), .clk2(clk2), .val(sr_bit_24_valout), .valout(sr_bit_26_valout));  // open: nvalout
  sr_bit sr_bit_27 (.clk1(clk1), .clk2(clk2), .val(sr_bit_25_valout), .valout(sr_bit_27_valout));  // open: nvalout
  sr_bit sr_bit_28 (.clk1(clk1), .clk2(clk2), .val(sr_bit_26_valout), .valout(sr_bit_28_valout));  // open: nvalout
  sr_bit sr_bit_29 (.clk1(clk1), .clk2(clk2), .val(sr_bit_27_valout), .valout(sr_bit_29_valout));  // open: nvalout
  sr_bit sr_bit_30 (.clk1(clk1), .clk2(clk2), .val(sr_bit_28_valout), .valout(sr_bit_30_valout));  // open: nvalout
  sr_bit sr_bit_31 (.clk1(clk1), .clk2(clk2), .val(sr_bit_29_valout), .valout(sr_bit_31_valout));  // open: nvalout
  sr_bit sr_bit_32 (.clk1(clk1), .clk2(clk2), .val(sr_bit_31_valout), .valout(sr_bit_32_valout));  // open: nvalout
  nor nor_3 (nor_3_out, sr_bit_3_valout, sr_bit_8_valout, sr_bit_12_valout, sr_bit_19_valout, sr_bit_24_valout, sr_bit_28_valout);
  not not_6 (not_6_out, nor_4_out);
  nor nor_4 (nor_4_out, sr_bit_8_valout, sr_bit_9_valout, sr_bit_12_valout, sr_bit_15_valout, sr_bit_19_valout, sr_bit_22_valout, sr_bit_24_valout, sr_bit_26_valout, sr_bit_28_valout, sr_bit_30_valout);
  nor nor_5 (nor_5_out, sr_bit_8_valout, sr_bit_9_valout, sr_bit_24_valout, sr_bit_26_valout);
  nor nor_6 (nor_6_out, sr_bit_3_valout, sr_bit_15_valout, sr_bit_19_valout, sr_bit_30_valout);
  nor nor_7 (nor_7_out, sr_bit_24_valout, sr_bit_26_valout, sr_bit_28_valout, sr_bit_30_valout);
  nor nor_8 (nor_8_out, sr_bit_3_valout, sr_bit_5_valout, sr_bit_8_valout, sr_bit_9_valout, sr_bit_12_valout, sr_bit_15_valout, sr_bit_19_valout, sr_bit_22_valout, sr_bit_24_valout, sr_bit_26_valout, sr_bit_28_valout);
  nor nor_9 (nor_9_out, sr_bit_3_valout, sr_bit_9_valout, sr_bit_19_valout, sr_bit_26_valout);
  nor nor_10 (nor_10_out, sr_bit_8_valout, sr_bit_9_valout, sr_bit_12_valout, sr_bit_15_valout);
  nor nor_11 (nor_11_out, sr_bit_8_valout, sr_bit_15_valout, sr_bit_24_valout, sr_bit_30_valout);
  sr_bit sr_bit_33 (.clk1(clk1), .clk2(clk2), .val(sr_bit_32_valout), .valout(sr_bit_33_valout));  // open: nvalout
  sr_bit sr_bit_34 (.clk1(clk1), .clk2(clk2), .val(nor_3_out), .valout(sr_bit_34_valout));  // open: nvalout
  D_Flip_Flop #(.trigger("high")) d_ff_1 (.D(not_6_out), .clk(clk1), .Qn(out_14));  // open: Q, preset, reset
  sr_bit sr_bit_35 (.clk1(clk1), .clk2(clk2), .val(nor_5_out), .valout(sr_bit_35_valout));  // open: nvalout
  sr_bit sr_bit_36 (.clk1(clk1), .clk2(clk2), .val(nor_6_out), .valout(sr_bit_36_valout));  // open: nvalout
  sr_bit sr_bit_37 (.clk1(clk1), .clk2(clk2), .val(nor_7_out), .valout(sr_bit_37_valout));  // open: nvalout
  sr_bit sr_bit_38 (.clk1(clk1), .clk2(clk2), .val(nor_9_out), .valout(sr_bit_38_valout));  // open: nvalout
  sr_bit sr_bit_39 (.clk1(clk1), .clk2(clk2), .val(nor_10_out), .valout(sr_bit_39_valout));  // open: nvalout
  sr_bit sr_bit_40 (.clk1(clk1), .clk2(clk2), .val(nor_11_out), .valout(sr_bit_40_valout));  // open: nvalout
  sr_bit sr_bit_41 (.clk1(clk1), .clk2(clk2), .val(sr_bit_33_valout), .valout(sr_bit_41_valout));  // open: nvalout
  not not_7 (out_12, sr_bit_37_valout);
  not not_8 (out_13, sr_bit_39_valout);
  sr_bit sr_bit_42 (.clk1(clk1), .clk2(clk2), .val(sr_bit_41_valout), .valout(sr_bit_42_valout));  // open: nvalout
  not not_9 (not_9_out, sr_bit_34_valout);
  nor nor_12 (out_8, sr_bit_34_valout, not_15_out);
  nor nor_13 (out_9, not_9_out, not_13_out);
  nor nor_14 (out_10, sr_bit_38_valout, not_19_out);
  nor nor_15 (out_11, sr_bit_40_valout, not_17_out);
  not not_10 (fm_clk2, sr_bit_35_valout);
  not not_11 (fm_clk1, sr_bit_36_valout);
  not not_12 (not_12_out, out_8);
  not not_13 (not_13_out, not_12_out);
  not not_14 (not_14_out, out_9);
  not not_15 (not_15_out, not_14_out);
  not not_16 (not_16_out, out_10);
  not not_17 (not_17_out, not_16_out);
  not not_18 (not_18_out, out_11);
  not not_19 (not_19_out, not_18_out);
  not not_20 (not_20_out, nor_8_out);
endmodule

module clk_div_2612 (
  input  clk1,
  input  clk2,
  input  IC,
  output fm_clk1,
  output fm_clk2,
  output res_latch1
);

  wire nor_1_out, nor_2_out, nor_3_out, nor_4_out, nor_5_out, not_1_out, not_2_out, not_3_out, not_5_out,
       sr_bit_1_valout, sr_bit_2_valout, sr_bit_3_valout, sr_bit_4_valout, sr_bit_5_valout, sr_bit_6_valout,
       sr_bit_7_valout, sr_bit_8_valout, sr_bit_9_valout, sr_bit_10_valout, sr_bit_11_valout,
       sr_bit_12_valout, sr_bit_13_valout, sr_bit_14_valout, sr_bit_15_valout, sr_bit_16_valout,
       sr_bit_17_valout, sr_bit_18_valout, sr_bit_19_valout, sr_bit_20_valout, sr_bit_21_valout,
       sr_bit_22_valout, sr_bit_23_valout, sr_bit_24_valout;

  nor nor_1 (nor_1_out, not_3_out, not_5_out);
  sr_bit sr_bit_1 (.clk1(clk1), .clk2(clk2), .val(IC), .valout(sr_bit_1_valout));  // open: nvalout
  sr_bit sr_bit_2 (.clk1(clk1), .clk2(clk2), .val(nor_1_out), .valout(sr_bit_2_valout));  // open: nvalout
  sr_bit sr_bit_3 (.clk1(clk1), .clk2(clk2), .val(sr_bit_1_valout), .valout(sr_bit_3_valout));  // open: nvalout
  not not_1 (not_1_out, IC);
  sr_bit sr_bit_4 (.clk1(clk1), .clk2(clk2), .val(sr_bit_2_valout), .valout(sr_bit_4_valout));  // open: nvalout
  sr_bit sr_bit_5 (.clk1(clk1), .clk2(clk2), .val(sr_bit_3_valout), .valout(sr_bit_5_valout));  // open: nvalout
  sr_bit sr_bit_6 (.clk1(clk1), .clk2(clk2), .val(sr_bit_5_valout), .valout(sr_bit_6_valout));  // open: nvalout
  nor nor_2 (nor_2_out, sr_bit_24_valout, not_1_out);
  not not_2 (not_2_out, nor_2_out);
  sr_bit sr_bit_7 (.clk1(clk1), .clk2(clk2), .val(sr_bit_4_valout), .valout(sr_bit_7_valout));  // open: nvalout
  sr_bit sr_bit_8 (.clk1(clk1), .clk2(clk2), .val(sr_bit_7_valout), .valout(sr_bit_8_valout));  // open: nvalout
  sr_bit sr_bit_9 (.clk1(clk1), .clk2(clk2), .val(sr_bit_6_valout), .valout(sr_bit_9_valout));  // open: nvalout
  sr_bit sr_bit_10 (.clk1(clk1), .clk2(clk2), .val(not_2_out), .valout(sr_bit_10_valout));  // open: nvalout
  sr_bit sr_bit_11 (.clk1(clk1), .clk2(clk2), .val(sr_bit_8_valout), .valout(sr_bit_11_valout));  // open: nvalout
  sr_bit sr_bit_12 (.clk1(clk1), .clk2(clk2), .val(sr_bit_9_valout), .valout(sr_bit_12_valout));  // open: nvalout
  sr_bit sr_bit_13 (.clk1(clk1), .clk2(clk2), .val(sr_bit_10_valout), .valout(sr_bit_13_valout));  // open: nvalout
  sr_bit sr_bit_14 (.clk1(clk1), .clk2(clk2), .val(sr_bit_11_valout), .valout(sr_bit_14_valout));  // open: nvalout
  sr_bit sr_bit_15 (.clk1(clk1), .clk2(clk2), .val(sr_bit_12_valout), .valout(sr_bit_15_valout));  // open: nvalout
  not not_3 (not_3_out, not_2_out);
  sr_bit sr_bit_16 (.clk1(clk1), .clk2(clk2), .val(sr_bit_13_valout), .valout(sr_bit_16_valout));  // open: nvalout
  sr_bit sr_bit_17 (.clk1(clk1), .clk2(clk2), .val(sr_bit_15_valout), .valout(sr_bit_17_valout));  // open: nvalout
  nor nor_3 (nor_3_out, sr_bit_7_valout, sr_bit_8_valout);
  nor nor_4 (nor_4_out, sr_bit_2_valout, sr_bit_14_valout);
  sr_bit sr_bit_18 (.clk1(clk1), .clk2(clk2), .val(sr_bit_17_valout), .valout(sr_bit_18_valout));  // open: nvalout
  sr_bit sr_bit_19 (.clk1(clk1), .clk2(clk2), .val(sr_bit_16_valout), .valout(sr_bit_19_valout));  // open: nvalout
  nor nor_5 (nor_5_out, sr_bit_2_valout, sr_bit_4_valout, sr_bit_7_valout, sr_bit_8_valout, sr_bit_11_valout);
  sr_bit sr_bit_20 (.clk1(clk1), .clk2(clk2), .val(sr_bit_18_valout), .valout(sr_bit_20_valout));  // open: nvalout
  not not_4 (res_latch1, sr_bit_19_valout);
  sr_bit sr_bit_21 (.clk1(clk1), .clk2(clk2), .val(nor_3_out), .valout(sr_bit_21_valout));  // open: nvalout
  sr_bit sr_bit_22 (.clk1(clk1), .clk2(clk2), .val(nor_4_out), .valout(sr_bit_22_valout));  // open: nvalout
  not not_5 (not_5_out, nor_5_out);
  sr_bit sr_bit_23 (.clk1(clk1), .clk2(clk2), .val(sr_bit_20_valout), .valout(sr_bit_23_valout));  // open: nvalout
  sr_bit sr_bit_24 (.clk1(clk1), .clk2(clk2), .val(sr_bit_23_valout), .valout(sr_bit_24_valout));  // open: nvalout
  not not_6 (fm_clk2, sr_bit_21_valout);
  not not_7 (fm_clk1, sr_bit_22_valout);
endmodule

module reg_glob (
  input  clk1,
  input  clk2,
  input  [8:0] write_data,
  input  [8:0] write_data_neg,
  input  addr_wr,
  input  data_wr,
  input  IC,
  input  sync,
  input  ch3_sel,
  input  sync_timer,
  output [7:0] data,
  output write40,
  output write70,
  output write50,
  output write60,
  output write80,
  output write30,
  output write90,
  output writeB0,
  output writeAC,
  output writeA0,
  output writeA4,
  output writeA8,
  output writeB4,
  output sel,
  output busy,
  output op_reg_bank,
  output kon,
  output kon_csm,
  output timer_a_status,
  output timer_b_status,
  output [7:0] test1,
  output [2:0] lfo,
  output lfo_en,
  output ch3_ext,
  output [7:0] test2,
  output [5:0] reg_1c_0,
  output reg_1c_7
);

  wire d_ff_1_qn, reg_timer_ctrl_1_csm_enable, reg_timer_ctrl_1_enable_a, reg_timer_ctrl_1_enable_b,
       reg_timer_ctrl_1_load_a, reg_timer_ctrl_1_load_b, reg_timer_ctrl_1_reset_a, reg_timer_ctrl_1_reset_b;
  wire [2:0] reg_kon_1_chan;
  wire [3:0] reg_kon_1_operator;
  wire [7:0] reg_timerb_1_valout;
  wire [9:0] reg_timera_1_valout;

  D_Flip_Flop #(.trigger("high")) d_ff_1 (.D(IC), .clk(clk1), .Qn(d_ff_1_qn));  // open: Q, preset, reset
  reg_test1 reg_test1_1 (
    .clk1(clk1), .clk2(clk2), .write_data(write_data), .write_data_neg(write_data_neg), .addr_wr(addr_wr),
    .data_wr(data_wr), .IC(d_ff_1_qn), .valout(test1));
  reg_lfo reg_lfo_1 (
    .clk1(clk1), .clk2(clk2), .write_data(write_data), .write_data_neg(write_data_neg), .addr_wr(addr_wr),
    .data_wr(data_wr), .IC(d_ff_1_qn), .lfo(lfo), .lfo_en(lfo_en));
  reg_timera reg_timera_1 (
    .clk1(clk1), .clk2(clk2), .write_data(write_data), .write_data_neg(write_data_neg), .addr_wr(addr_wr),
    .data_wr(data_wr), .IC(d_ff_1_qn), .valout(reg_timera_1_valout));
  reg_timerb reg_timerb_1 (
    .clk1(clk1), .clk2(clk2), .write_data(write_data), .write_data_neg(write_data_neg), .addr_wr(addr_wr),
    .data_wr(data_wr), .IC(d_ff_1_qn), .valout(reg_timerb_1_valout));
  reg_timer_ctrl reg_timer_ctrl_1 (
    .clk1(clk1), .clk2(clk2), .write_data(write_data), .write_data_neg(write_data_neg), .addr_wr(addr_wr),
    .data_wr(data_wr), .IC(d_ff_1_qn), .load_a(reg_timer_ctrl_1_load_a), .load_b(reg_timer_ctrl_1_load_b),
    .enable_a(reg_timer_ctrl_1_enable_a), .enable_b(reg_timer_ctrl_1_enable_b), .ch3_ext(ch3_ext),
    .csm_enable(reg_timer_ctrl_1_csm_enable), .reset_a(reg_timer_ctrl_1_reset_a),
    .reset_b(reg_timer_ctrl_1_reset_b));
  reg_kon reg_kon_1 (
    .clk1(clk1), .clk2(clk2), .write_data(write_data), .write_data_neg(write_data_neg), .addr_wr(addr_wr),
    .data_wr(data_wr), .IC(d_ff_1_qn), .chan(reg_kon_1_chan), .operator(reg_kon_1_operator));
  reg_test2 reg_test2_1 (
    .clk1(clk1), .clk2(clk2), .write_data(write_data), .write_data_neg(write_data_neg), .addr_wr(addr_wr),
    .data_wr(data_wr), .IC(d_ff_1_qn), .valout(test2));
  reg_1c reg_1c_1 (
    .clk1(clk1), .clk2(clk2), .write_data(write_data), .write_data_neg(write_data_neg), .addr_wr(addr_wr),
    .data_wr(data_wr), .IC(d_ff_1_qn), .out_8(reg_1c_0), .out_9(reg_1c_7));
  busy_cnt busy_cnt_1 (.clk1(clk1), .clk2(clk2), .data_wr(data_wr), .IC(IC), .busy(busy));
  keyon keyon_1 (
    .clk1(clk1), .clk2(clk2), .IC(IC), .sync(sync), .chan(reg_kon_1_chan), .op(reg_kon_1_operator),
    .csm_kon(kon_csm), .op_reg_bank_sel(op_reg_bank), .keyon(kon));
  timers timers_1 (
    .clk1(clk1), .clk2(clk2), .IC(IC), .ch3_sel(ch3_sel), .csm_enable(reg_timer_ctrl_1_csm_enable),
    .clk_timers(sync_timer), .timer_test(test1[2]), .timer_a_load(reg_timer_ctrl_1_load_a),
    .timer_a_enable(reg_timer_ctrl_1_enable_a), .timer_a_reset(reg_timer_ctrl_1_reset_a),
    .timer_a_val(reg_timera_1_valout), .timer_b_load(reg_timer_ctrl_1_load_b),
    .timer_b_enable(reg_timer_ctrl_1_enable_b), .timer_b_reset(reg_timer_ctrl_1_reset_b),
    .timer_b_val(reg_timerb_1_valout), .keyon_csm(kon_csm), .timer_a_status(timer_a_status),
    .timer_b_status(timer_b_status));
  reg_ctrl reg_ctrl_1 (
    .clk1(clk1), .clk2(clk2), .write_data(write_data), .addr_wr(addr_wr), .data_wr(data_wr),
    .IC_l(d_ff_1_qn), .IC(IC), .sync(sync), .data(data), .write40(write40), .write70(write70),
    .write50(write50), .write60(write60), .write80(write80), .write30(write30), .write90(write90),
    .writeB0(writeB0), .writeAC(writeAC), .writeA0(writeA0), .writeA4(writeA4), .writeA8(writeA8),
    .writeB4(writeB4), .sel(sel));
endmodule

module io_ctrl (
  input  RD,
  input  WR,
  input  A0,
  input  A1,
  input  CS,
  input  IC,
  input  clk1,
  input  clk2,
  input  aclk1,
  input  aclk2,
  output addr_wr,
  output data_wr,
  output data_wr2,
  output read,
  output read0,
  output read1,
  output read2,
  output write,
  output write0,
  output write1,
  output out_21,
  output out_22
);

  wire and_1_out, and_2_out, and_3_out, and_4_out, and_5_out, and_6_out, d_ff_1_qn, d_ff_2_qn, d_ff_3_qn,
       nand_1_out, nor_1_out, nor_2_out, nor_3_out, nor_4_out, nor_5_out, nor_6_out, nor_7_out, nor_8_out,
       nor_9_out, nor_10_out, nor_11_out, nor_12_out, nor_13_out, nor_14_out, nor_15_out, nor_16_out,
       nor_17_out, nor_18_out, nor_19_out, nor_20_out, nor_21_out, nor_22_out, nor_23_out, nor_24_out,
       nor_25_out, nor_26_out, not_1_out, not_2_out, not_3_out, not_4_out, not_5_out, not_6_out, not_7_out,
       not_8_out, not_9_out, not_10_out, not_11_out, not_12_out, not_13_out, not_18_out, not_22_out,
       not_23_out, not_24_out, not_25_out, or_1_out, sr_bit_1_valout, sr_bit_2_valout, sr_bit_3_valout;

  not not_1 (not_1_out, RD);
  not not_2 (not_2_out, not_1_out);
  not not_3 (not_3_out, WR);
  not not_4 (not_4_out, not_3_out);
  not not_5 (not_5_out, A0);
  not not_6 (not_6_out, not_5_out);
  not not_7 (not_7_out, A1);
  not not_8 (not_8_out, not_7_out);
  not not_9 (not_9_out, CS);
  not not_10 (not_10_out, not_9_out);
  not not_11 (not_11_out, nor_22_out);
  not not_12 (not_12_out, not_18_out);
  not not_13 (not_13_out, not_18_out);
  nor nor_1 (nor_1_out, not_11_out, nor_2_out);
  nor nor_2 (nor_2_out, nor_1_out, d_ff_1_qn);
  nor nor_3 (nor_3_out, not_12_out, nor_4_out);
  nor nor_4 (nor_4_out, nor_3_out, d_ff_2_qn);
  nor nor_5 (nor_5_out, not_13_out, nor_6_out);
  nor nor_6 (nor_6_out, nor_5_out, d_ff_3_qn);
  and and_1 (and_1_out, clk1, nor_2_out);
  and and_2 (and_2_out, clk1, nor_1_out);
  and and_3 (and_3_out, clk1, nor_4_out);
  and and_4 (and_4_out, clk1, nor_3_out);
  and and_5 (and_5_out, aclk1, nor_6_out);
  and and_6 (and_6_out, aclk1, nor_5_out);
  nor nor_7 (nor_7_out, not_2_out, IC, not_10_out);
  nor nor_8 (nor_8_out, not_4_out, not_6_out, not_10_out);
  nor nor_9 (nor_9_out, not_2_out, IC, not_8_out, not_5_out, not_10_out);
  nor nor_10 (nor_10_out, not_4_out, IC, not_8_out, not_5_out, not_10_out);
  nor nor_11 (nor_11_out, not_4_out, IC, not_6_out, not_8_out, not_10_out);
  nor nor_12 (nor_12_out, not_4_out, IC, not_5_out, not_10_out);
  nor nor_13 (nor_13_out, not_2_out, IC, not_6_out, not_7_out, not_10_out);
  nor nor_14 (nor_14_out, not_2_out, IC, not_6_out, not_8_out, not_10_out);
  nor nor_15 (nor_15_out, not_4_out, not_10_out);
  nor nor_16 (nor_16_out, and_1_out, nor_17_out);
  nor nor_17 (nor_17_out, and_2_out, nor_16_out);
  nor nor_18 (nor_18_out, and_3_out, nor_19_out);
  nor nor_19 (nor_19_out, and_4_out, nor_18_out);
  nor nor_20 (nor_20_out, and_5_out, nor_21_out);
  nor nor_21 (nor_21_out, and_6_out, nor_20_out);
  not not_14 (read, nor_7_out);
  not not_15 (read1, nor_9_out);
  not not_16 (write1, nor_10_out);
  not not_17 (write0, nor_11_out);
  not not_18 (not_18_out, nor_12_out);
  not not_19 (read2, nor_13_out);
  not not_20 (read0, nor_14_out);
  not not_21 (write, nor_15_out);
  D_Flip_Flop #(.trigger("high")) d_ff_1 (.D(nor_16_out), .clk(clk2), .Qn(d_ff_1_qn));  // open: Q, preset, reset
  D_Flip_Flop #(.trigger("high")) d_ff_2 (.D(nor_18_out), .clk(clk2), .Qn(d_ff_2_qn));  // open: Q, preset, reset
  D_Flip_Flop #(.trigger("high")) d_ff_3 (.D(nor_20_out), .clk(aclk2), .Qn(d_ff_3_qn));  // open: Q, preset, reset
  nor nor_22 (nor_22_out, IC, nor_8_out);
  sr_bit sr_bit_1 (.clk1(clk1), .clk2(clk2), .val(d_ff_1_qn), .valout(sr_bit_1_valout));  // open: nvalout
  sr_bit sr_bit_2 (.clk1(clk1), .clk2(clk2), .val(d_ff_2_qn), .valout(sr_bit_2_valout));  // open: nvalout
  sr_bit sr_bit_3 (.clk1(aclk1), .clk2(aclk2), .val(d_ff_3_qn), .valout(sr_bit_3_valout));  // open: nvalout
  not not_22 (not_22_out, d_ff_1_qn);
  not not_23 (not_23_out, d_ff_2_qn);
  not not_24 (not_24_out, d_ff_3_qn);
  or or_1 (or_1_out, not_18_out, not_8_out);
  not not_25 (not_25_out, IC);
  nor nor_23 (nor_23_out, sr_bit_1_valout, not_22_out);
  nor nor_24 (nor_24_out, sr_bit_2_valout, not_23_out);
  nor nor_25 (nor_25_out, sr_bit_3_valout, not_24_out);
  not not_26 (out_21, nor_26_out);
  nor nor_26 (nor_26_out, nor_22_out, not_8_out);
  not not_27 (out_22, nand_1_out);
  nand nand_1 (nand_1_out, or_1_out, not_25_out);
  not not_28 (addr_wr, nor_23_out);
  not not_29 (data_wr, nor_24_out);
  not not_30 (data_wr2, nor_25_out);
endmodule

module io_ctrl_2612 (
  input  RD,
  input  WR,
  input  A0,
  input  A1,
  input  CS,
  input  IC,
  input  clk1,
  input  clk2,
  output addr_wr,
  output data_wr,
  output read,
  output read0,
  output write
);

  wire and_1_out, and_2_out, and_3_out, and_4_out, d_ff_1_qn, d_ff_2_qn, nor_1_out, nor_2_out, nor_3_out,
       nor_4_out, nor_5_out, nor_6_out, nor_7_out, nor_8_out, nor_9_out, nor_10_out, nor_11_out, nor_12_out,
       nor_13_out, nor_14_out, nor_15_out, nor_16_out, not_1_out, not_2_out, not_3_out, not_4_out, not_5_out,
       not_6_out, not_7_out, not_8_out, not_9_out, not_10_out, not_11_out, not_12_out, not_14_out,
       not_17_out, not_18_out, sr_bit_1_valout, sr_bit_2_valout;

  not not_1 (not_1_out, RD);
  not not_2 (not_2_out, not_1_out);
  not not_3 (not_3_out, WR);
  not not_4 (not_4_out, not_3_out);
  not not_5 (not_5_out, A0);
  not not_6 (not_6_out, not_5_out);
  not not_7 (not_7_out, A1);
  not not_8 (not_8_out, not_7_out);
  not not_9 (not_9_out, CS);
  not not_10 (not_10_out, not_9_out);
  not not_11 (not_11_out, nor_14_out);
  not not_12 (not_12_out, not_14_out);
  nor nor_1 (nor_1_out, not_11_out, nor_2_out);
  nor nor_2 (nor_2_out, nor_1_out, d_ff_1_qn);
  nor nor_3 (nor_3_out, not_12_out, nor_4_out);
  nor nor_4 (nor_4_out, nor_3_out, d_ff_2_qn);
  and and_1 (and_1_out, clk1, nor_2_out);
  and and_2 (and_2_out, clk1, nor_1_out);
  and and_3 (and_3_out, clk1, nor_4_out);
  and and_4 (and_4_out, clk1, nor_3_out);
  nor nor_5 (nor_5_out, not_2_out, IC, not_10_out);
  nor nor_6 (nor_6_out, not_4_out, not_6_out, not_10_out);
  nor nor_7 (nor_7_out, not_4_out, IC, not_5_out, not_10_out);
  nor nor_8 (nor_8_out, not_2_out, IC, not_6_out, not_8_out, not_10_out);
  nor nor_9 (nor_9_out, not_4_out, not_10_out);
  nor nor_10 (nor_10_out, and_1_out, nor_11_out);
  nor nor_11 (nor_11_out, and_2_out, nor_10_out);
  nor nor_12 (nor_12_out, and_3_out, nor_13_out);
  nor nor_13 (nor_13_out, and_4_out, nor_12_out);
  not not_13 (read, nor_5_out);
  not not_14 (not_14_out, nor_7_out);
  not not_15 (read0, nor_8_out);
  not not_16 (write, nor_9_out);
  D_Flip_Flop #(.trigger("high")) d_ff_1 (.D(nor_10_out), .clk(clk2), .Qn(d_ff_1_qn));  // open: Q, preset, reset
  D_Flip_Flop #(.trigger("high")) d_ff_2 (.D(nor_12_out), .clk(clk2), .Qn(d_ff_2_qn));  // open: Q, preset, reset
  nor nor_14 (nor_14_out, IC, nor_6_out);
  sr_bit sr_bit_1 (.clk1(clk1), .clk2(clk2), .val(d_ff_1_qn), .valout(sr_bit_1_valout));  // open: nvalout
  sr_bit sr_bit_2 (.clk1(clk1), .clk2(clk2), .val(d_ff_2_qn), .valout(sr_bit_2_valout));  // open: nvalout
  not not_17 (not_17_out, d_ff_1_qn);
  not not_18 (not_18_out, d_ff_2_qn);
  nor nor_15 (nor_15_out, sr_bit_1_valout, not_17_out);
  nor nor_16 (nor_16_out, sr_bit_2_valout, not_18_out);
  not not_19 (addr_wr, nor_15_out);
  not not_20 (data_wr, nor_16_out);
endmodule

module reg_bit_2 (
  input  clk1,
  input  clk2,
  input  val,
  input  load,
  input  nload,
  input  ic,
  output valout
);

  wire controlled_buffer_1_out, d_ff_1_q, d_ff_2_qn;

  assign controlled_buffer_1_out = load ? val : 1'bz;  // Controlled_Buffer controlled_buffer_1
  assign controlled_buffer_1_out = nload ? d_ff_2_qn : 1'bz;  // Controlled_Buffer controlled_buffer_2
  D_Flip_Flop #(.trigger("high")) d_ff_1 (
    .D(controlled_buffer_1_out), .clk(clk1), .Q(d_ff_1_q));  // open: Qn, preset, reset
  nand nand_1 (valout, d_ff_1_q, ic);
  D_Flip_Flop #(.trigger("high")) d_ff_2 (.D(valout), .clk(clk2), .Qn(d_ff_2_qn));  // open: Q, preset, reset
endmodule

module reg_bit_3 (
  input  clk1,
  input  clk2,
  input  val,
  input  load,
  input  nload,
  input  ic,
  output valout
);

  wire controlled_buffer_1_out, d_ff_1_q, d_ff_2_qn, nand_1_out;

  assign controlled_buffer_1_out = load ? val : 1'bz;  // Controlled_Buffer controlled_buffer_1
  assign controlled_buffer_1_out = nload ? d_ff_2_qn : 1'bz;  // Controlled_Buffer controlled_buffer_2
  D_Flip_Flop #(.trigger("high")) d_ff_1 (
    .D(controlled_buffer_1_out), .clk(clk1), .Q(d_ff_1_q));  // open: Qn, preset, reset
  nand nand_1 (nand_1_out, d_ff_1_q, ic);
  D_Flip_Flop #(.trigger("high")) d_ff_2 (.D(nand_1_out), .clk(clk2), .Qn(d_ff_2_qn));  // open: Q, preset, reset
  not not_1 (valout, d_ff_2_qn);
endmodule

module reg_bit_4 (
  input  clk1,
  input  clk2,
  input  val,
  input  load,
  input  nload,
  input  ic,
  output valout
);

  wire controlled_buffer_1_out, d_ff_1_q, nand_1_out;

  assign controlled_buffer_1_out = load ? val : 1'bz;  // Controlled_Buffer controlled_buffer_1
  assign controlled_buffer_1_out = nload ? valout : 1'bz;  // Controlled_Buffer controlled_buffer_2
  D_Flip_Flop #(.trigger("high")) d_ff_1 (
    .D(controlled_buffer_1_out), .clk(clk1), .Q(d_ff_1_q));  // open: Qn, preset, reset
  nand nand_1 (nand_1_out, d_ff_1_q, ic);
  D_Flip_Flop #(.trigger("high")) d_ff_2 (.D(nand_1_out), .clk(clk2), .Qn(valout));  // open: Q, preset, reset
endmodule

module cnt_bit (
  input  cin,
  input  ic,
  input  clk1,
  input  clk2,
  output cout,
  output valout
);

  wire and_1_out, d_ff_2_q, nor_2_out, not_1_out;

  not not_1 (not_1_out, cin);
  and and_1 (and_1_out, not_1_out, d_ff_2_q);
  nor nor_1 (cout, not_1_out, d_ff_2_q);
  nor nor_2 (nor_2_out, cout, ic, and_1_out);
  D_Flip_Flop #(.trigger("high")) d_ff_1 (.D(nor_2_out), .clk(clk1), .Qn(valout));  // open: Q, preset, reset
  D_Flip_Flop #(.trigger("high")) d_ff_2 (.D(valout), .clk(clk2), .Q(d_ff_2_q));  // open: Qn, preset, reset
endmodule

module timer_bit (
  input  cin,
  input  ic,
  input  load,
  input  value,
  input  clk1,
  input  clk2,
  output out_7
);

  wire and_1_out, and_2_out, d_ff_1_q, d_ff_2_q, d_ff_3_q, d_ff_4_q, nor_2_out, nor_3_out, not_1_out;

  not not_1 (not_1_out, cin);
  nor nor_1 (out_7, d_ff_4_q, not_1_out);
  and and_1 (and_1_out, not_1_out, d_ff_4_q);
  D_Flip_Flop #(.trigger("high")) d_ff_1 (.D(nor_2_out), .clk(clk1), .Q(d_ff_1_q));  // open: Qn, preset, reset
  nor nor_2 (nor_2_out, out_7, and_1_out, ic, load);
  D_Flip_Flop #(.trigger("high")) d_ff_2 (.D(load), .clk(clk1), .Q(d_ff_2_q));  // open: Qn, preset, reset
  D_Flip_Flop #(.trigger("high")) d_ff_3 (.D(value), .clk(clk1), .Q(d_ff_3_q));  // open: Qn, preset, reset
  nor nor_3 (nor_3_out, d_ff_1_q, and_2_out);
  and and_2 (and_2_out, d_ff_2_q, d_ff_3_q);
  D_Flip_Flop #(.trigger("high")) d_ff_4 (.D(nor_3_out), .clk(clk2), .Q(d_ff_4_q));  // open: Qn, preset, reset
endmodule

module reg_timera (
  input  clk1,
  input  clk2,
  input  [8:0] write_data,
  input  [8:0] write_data_neg,
  input  addr_wr,
  input  data_wr,
  input  IC,
  output [9:0] valout
);

  wire and_1_out, and_2_out, nor_1_out, nor_2_out, nor_3_out, nor_4_out, nor_5_out, nor_6_out, not_1_out,
       not_2_out, sr_bit_1_nvalout, sr_bit_1_valout, sr_bit_2_nvalout, sr_bit_2_valout;

  nor nor_1 (nor_1_out, write_data[8], write_data[7], write_data[6], write_data_neg[5], write_data[4], write_data[3], write_data_neg[2], write_data[1], write_data_neg[0], addr_wr);
  nor nor_2 (nor_2_out, write_data[8], write_data[7], write_data[6], write_data_neg[5], write_data[4], write_data[3], write_data_neg[2], write_data[1], write_data[0], addr_wr);
  and and_1 (and_1_out, addr_wr, sr_bit_1_nvalout);
  and and_2 (and_2_out, addr_wr, sr_bit_2_nvalout);
  nor nor_3 (nor_3_out, nor_1_out, and_1_out);
  nor nor_4 (nor_4_out, nor_2_out, and_2_out);
  sr_bit sr_bit_1 (.clk1(clk1), .clk2(clk2), .val(nor_3_out), .nvalout(sr_bit_1_nvalout), .valout(sr_bit_1_valout));
  sr_bit sr_bit_2 (.clk1(clk1), .clk2(clk2), .val(nor_4_out), .nvalout(sr_bit_2_nvalout), .valout(sr_bit_2_valout));
  nor nor_5 (nor_5_out, sr_bit_1_valout, write_data[8], data_wr);
  nor nor_6 (nor_6_out, sr_bit_2_valout, write_data[8], data_wr);
  not not_1 (not_1_out, nor_5_out);
  not not_2 (not_2_out, nor_6_out);
  reg_bit_4 reg_bit_4_1 (
    .clk1(clk1), .clk2(clk2), .val(write_data[0]), .load(nor_5_out), .nload(not_1_out), .ic(IC),
    .valout(valout[0]));
  reg_bit_4 reg_bit_4_2 (
    .clk1(clk1), .clk2(clk2), .val(write_data[1]), .load(nor_5_out), .nload(not_1_out), .ic(IC),
    .valout(valout[1]));
  reg_bit_4 reg_bit_4_3 (
    .clk1(clk1), .clk2(clk2), .val(write_data[0]), .load(nor_6_out), .nload(not_2_out), .ic(IC),
    .valout(valout[2]));
  reg_bit_4 reg_bit_4_4 (
    .clk1(clk1), .clk2(clk2), .val(write_data[1]), .load(nor_6_out), .nload(not_2_out), .ic(IC),
    .valout(valout[3]));
  reg_bit_4 reg_bit_4_5 (
    .clk1(clk1), .clk2(clk2), .val(write_data[2]), .load(nor_6_out), .nload(not_2_out), .ic(IC),
    .valout(valout[4]));
  reg_bit_4 reg_bit_4_6 (
    .clk1(clk1), .clk2(clk2), .val(write_data[3]), .load(nor_6_out), .nload(not_2_out), .ic(IC),
    .valout(valout[5]));
  reg_bit_4 reg_bit_4_7 (
    .clk1(clk1), .clk2(clk2), .val(write_data[4]), .load(nor_6_out), .nload(not_2_out), .ic(IC),
    .valout(valout[6]));
  reg_bit_4 reg_bit_4_8 (
    .clk1(clk1), .clk2(clk2), .val(write_data[5]), .load(nor_6_out), .nload(not_2_out), .ic(IC),
    .valout(valout[7]));
  reg_bit_4 reg_bit_4_9 (
    .clk1(clk1), .clk2(clk2), .val(write_data[6]), .load(nor_6_out), .nload(not_2_out), .ic(IC),
    .valout(valout[8]));
  reg_bit_4 reg_bit_4_10 (
    .clk1(clk1), .clk2(clk2), .val(write_data[7]), .load(nor_6_out), .nload(not_2_out), .ic(IC),
    .valout(valout[9]));
endmodule

module reg_timer_ctrl (
  input  clk1,
  input  clk2,
  input  [8:0] write_data,
  input  [8:0] write_data_neg,
  input  addr_wr,
  input  data_wr,
  input  IC,
  output load_a,
  output load_b,
  output enable_a,
  output enable_b,
  output ch3_ext,
  output csm_enable,
  output reset_a,
  output reset_b
);

  wire and_1_out, nand_1_out, nand_2_out, nor_1_out, nor_2_out, nor_3_out, not_1_out, not_2_out, not_3_out,
       reg_bit_2_1_valout, reg_bit_2_2_valout, sr_bit_1_nvalout, sr_bit_1_valout;

  nor nor_1 (nor_1_out, write_data[8], write_data[7], write_data[6], write_data_neg[5], write_data[4], write_data[3], write_data_neg[2], write_data_neg[1], write_data_neg[0], addr_wr);
  and and_1 (and_1_out, addr_wr, sr_bit_1_nvalout);
  nor nor_2 (nor_2_out, nor_1_out, and_1_out);
  sr_bit sr_bit_1 (.clk1(clk1), .clk2(clk2), .val(nor_2_out), .nvalout(sr_bit_1_nvalout), .valout(sr_bit_1_valout));
  nor nor_3 (nor_3_out, sr_bit_1_valout, write_data[8], data_wr);
  not not_1 (not_1_out, nor_3_out);
  nand nand_1 (nand_1_out, nor_3_out, write_data[4]);
  nand nand_2 (nand_2_out, nor_3_out, write_data[5]);
  sr_bit sr_bit_2 (.clk1(clk1), .clk2(clk2), .val(nand_1_out), .valout(reset_a));  // open: nvalout
  sr_bit sr_bit_3 (.clk1(clk1), .clk2(clk2), .val(nand_2_out), .valout(reset_b));  // open: nvalout
  reg_bit_4 reg_bit_4_1 (
    .clk1(clk1), .clk2(clk2), .val(write_data[0]), .load(nor_3_out), .nload(not_1_out), .ic(IC),
    .valout(load_a));
  reg_bit_4 reg_bit_4_2 (
    .clk1(clk1), .clk2(clk2), .val(write_data[1]), .load(nor_3_out), .nload(not_1_out), .ic(IC),
    .valout(load_b));
  reg_bit_4 reg_bit_4_3 (
    .clk1(clk1), .clk2(clk2), .val(write_data[2]), .load(nor_3_out), .nload(not_1_out), .ic(IC),
    .valout(enable_a));
  reg_bit_4 reg_bit_4_4 (
    .clk1(clk1), .clk2(clk2), .val(write_data[3]), .load(nor_3_out), .nload(not_1_out), .ic(IC),
    .valout(enable_b));
  reg_bit_2 reg_bit_2_1 (
    .clk1(clk1), .clk2(clk2), .val(write_data[6]), .load(nor_3_out), .nload(not_1_out), .ic(IC),
    .valout(reg_bit_2_1_valout));
  reg_bit_2 reg_bit_2_2 (
    .clk1(clk1), .clk2(clk2), .val(write_data[7]), .load(nor_3_out), .nload(not_1_out), .ic(IC),
    .valout(reg_bit_2_2_valout));
  not not_2 (not_2_out, reg_bit_2_1_valout);
  or or_1 (ch3_ext, not_2_out, not_3_out);
  not not_3 (not_3_out, reg_bit_2_2_valout);
  nor nor_4 (csm_enable, not_2_out, reg_bit_2_2_valout);
endmodule

module reg_timerb (
  input  clk1,
  input  clk2,
  input  [8:0] write_data,
  input  [8:0] write_data_neg,
  input  addr_wr,
  input  data_wr,
  input  IC,
  output [7:0] valout
);

  wire and_1_out, nor_1_out, nor_2_out, nor_3_out, not_1_out, sr_bit_1_nvalout, sr_bit_1_valout;

  nor nor_1 (nor_1_out, write_data[8], write_data[7], write_data[6], write_data_neg[5], write_data[4], write_data[3], write_data_neg[2], write_data_neg[1], write_data[0], addr_wr);
  and and_1 (and_1_out, addr_wr, sr_bit_1_nvalout);
  nor nor_2 (nor_2_out, nor_1_out, and_1_out);
  sr_bit sr_bit_1 (.clk1(clk1), .clk2(clk2), .val(nor_2_out), .nvalout(sr_bit_1_nvalout), .valout(sr_bit_1_valout));
  nor nor_3 (nor_3_out, sr_bit_1_valout, write_data[8], data_wr);
  not not_1 (not_1_out, nor_3_out);
  reg_bit_4 reg_bit_4_1 (
    .clk1(clk1), .clk2(clk2), .val(write_data[0]), .load(nor_3_out), .nload(not_1_out), .ic(IC),
    .valout(valout[0]));
  reg_bit_4 reg_bit_4_2 (
    .clk1(clk1), .clk2(clk2), .val(write_data[1]), .load(nor_3_out), .nload(not_1_out), .ic(IC),
    .valout(valout[1]));
  reg_bit_4 reg_bit_4_3 (
    .clk1(clk1), .clk2(clk2), .val(write_data[2]), .load(nor_3_out), .nload(not_1_out), .ic(IC),
    .valout(valout[2]));
  reg_bit_4 reg_bit_4_4 (
    .clk1(clk1), .clk2(clk2), .val(write_data[3]), .load(nor_3_out), .nload(not_1_out), .ic(IC),
    .valout(valout[3]));
  reg_bit_4 reg_bit_4_5 (
    .clk1(clk1), .clk2(clk2), .val(write_data[4]), .load(nor_3_out), .nload(not_1_out), .ic(IC),
    .valout(valout[4]));
  reg_bit_4 reg_bit_4_6 (
    .clk1(clk1), .clk2(clk2), .val(write_data[5]), .load(nor_3_out), .nload(not_1_out), .ic(IC),
    .valout(valout[5]));
  reg_bit_4 reg_bit_4_7 (
    .clk1(clk1), .clk2(clk2), .val(write_data[6]), .load(nor_3_out), .nload(not_1_out), .ic(IC),
    .valout(valout[6]));
  reg_bit_4 reg_bit_4_8 (
    .clk1(clk1), .clk2(clk2), .val(write_data[7]), .load(nor_3_out), .nload(not_1_out), .ic(IC),
    .valout(valout[7]));
endmodule

module reg_1c (
  input  clk1,
  input  clk2,
  input  [8:0] write_data,
  input  [8:0] write_data_neg,
  input  addr_wr,
  input  data_wr,
  input  IC,
  output [5:0] out_8,
  output out_9
);

  wire and_1_out, nor_1_out, nor_2_out, nor_3_out, not_1_out, sr_bit_1_nvalout, sr_bit_1_valout;

  nor nor_1 (nor_1_out, write_data[8], write_data[7], write_data[6], write_data[5], write_data_neg[4], write_data_neg[3], write_data_neg[2], write_data[1], write_data[0], addr_wr);
  and and_1 (and_1_out, addr_wr, sr_bit_1_nvalout);
  nor nor_2 (nor_2_out, nor_1_out, and_1_out);
  sr_bit sr_bit_1 (.clk1(clk1), .clk2(clk2), .val(nor_2_out), .nvalout(sr_bit_1_nvalout), .valout(sr_bit_1_valout));
  nor nor_3 (nor_3_out, sr_bit_1_valout, write_data[8], data_wr);
  not not_1 (not_1_out, nor_3_out);
  reg_bit_3 reg_bit_3_1 (
    .clk1(clk1), .clk2(clk2), .val(write_data[0]), .load(nor_3_out), .nload(not_1_out), .ic(IC),
    .valout(out_8[0]));
  reg_bit_3 reg_bit_3_2 (
    .clk1(clk1), .clk2(clk2), .val(write_data[1]), .load(nor_3_out), .nload(not_1_out), .ic(IC),
    .valout(out_8[1]));
  reg_bit_3 reg_bit_3_3 (
    .clk1(clk1), .clk2(clk2), .val(write_data[2]), .load(nor_3_out), .nload(not_1_out), .ic(IC),
    .valout(out_8[2]));
  reg_bit_3 reg_bit_3_4 (
    .clk1(clk1), .clk2(clk2), .val(write_data[3]), .load(nor_3_out), .nload(not_1_out), .ic(IC),
    .valout(out_8[3]));
  reg_bit_3 reg_bit_3_5 (
    .clk1(clk1), .clk2(clk2), .val(write_data[4]), .load(nor_3_out), .nload(not_1_out), .ic(IC),
    .valout(out_8[4]));
  reg_bit_3 reg_bit_3_6 (
    .clk1(clk1), .clk2(clk2), .val(write_data[5]), .load(nor_3_out), .nload(not_1_out), .ic(IC),
    .valout(out_8[5]));
  reg_bit_3 reg_bit_3_7 (
    .clk1(clk1), .clk2(clk2), .val(write_data[7]), .load(nor_3_out), .nload(not_1_out), .ic(IC),
    .valout(out_9));
endmodule

module reg_test2 (
  input  clk1,
  input  clk2,
  input  [8:0] write_data,
  input  [8:0] write_data_neg,
  input  addr_wr,
  input  data_wr,
  input  IC,
  output [7:0] valout
);

  wire and_1_out, nor_1_out, nor_2_out, nor_3_out, not_1_out, not_2_out, reg_bit_4_1_valout,
       reg_bit_4_2_valout, reg_bit_4_3_valout, reg_bit_4_4_valout, sr_bit_1_nvalout, sr_bit_1_valout;

  not not_1 (not_1_out, write_data[8]);
  nor nor_1 (nor_1_out, not_1_out, write_data[7], write_data[6], write_data[5], write_data[4], write_data[3], write_data[2], write_data_neg[1], write_data[0], addr_wr);
  and and_1 (and_1_out, addr_wr, sr_bit_1_nvalout);
  nor nor_2 (nor_2_out, nor_1_out, and_1_out);
  sr_bit sr_bit_1 (.clk1(clk1), .clk2(clk2), .val(nor_2_out), .nvalout(sr_bit_1_nvalout), .valout(sr_bit_1_valout));
  nor nor_3 (nor_3_out, sr_bit_1_valout, not_1_out, data_wr);
  not not_2 (not_2_out, nor_3_out);
  reg_bit_4 reg_bit_4_1 (
    .clk1(clk1), .clk2(clk2), .val(write_data[3]), .load(nor_3_out), .nload(not_2_out), .ic(IC),
    .valout(reg_bit_4_1_valout));
  reg_bit_4 reg_bit_4_2 (
    .clk1(clk1), .clk2(clk2), .val(write_data[4]), .load(nor_3_out), .nload(not_2_out), .ic(IC),
    .valout(reg_bit_4_2_valout));
  reg_bit_4 reg_bit_4_3 (
    .clk1(clk1), .clk2(clk2), .val(write_data[5]), .load(nor_3_out), .nload(not_2_out), .ic(IC),
    .valout(reg_bit_4_3_valout));
  reg_bit_4 reg_bit_4_4 (
    .clk1(clk1), .clk2(clk2), .val(write_data[7]), .load(nor_3_out), .nload(not_2_out), .ic(IC),
    .valout(reg_bit_4_4_valout));
  not not_3 (valout[3], reg_bit_4_1_valout);
  not not_4 (valout[4], reg_bit_4_2_valout);
  not not_5 (valout[5], reg_bit_4_3_valout);
  not not_6 (valout[7], reg_bit_4_4_valout);
endmodule

module reg_lfo (
  input  clk1,
  input  clk2,
  input  [8:0] write_data,
  input  [8:0] write_data_neg,
  input  addr_wr,
  input  data_wr,
  input  IC,
  output [2:0] lfo,
  output lfo_en
);

  wire and_1_out, nor_1_out, nor_2_out, nor_3_out, not_1_out, sr_bit_1_nvalout, sr_bit_1_valout;

  nor nor_1 (nor_1_out, write_data[8], write_data[7], write_data[6], write_data_neg[5], write_data[4], write_data[3], write_data[2], write_data_neg[1], write_data[0], addr_wr);
  and and_1 (and_1_out, addr_wr, sr_bit_1_nvalout);
  nor nor_2 (nor_2_out, nor_1_out, and_1_out);
  sr_bit sr_bit_1 (.clk1(clk1), .clk2(clk2), .val(nor_2_out), .nvalout(sr_bit_1_nvalout), .valout(sr_bit_1_valout));
  nor nor_3 (nor_3_out, sr_bit_1_valout, write_data[8], data_wr);
  not not_1 (not_1_out, nor_3_out);
  reg_bit_2 reg_bit_2_1 (
    .clk1(clk1), .clk2(clk2), .val(write_data[0]), .load(nor_3_out), .nload(not_1_out), .ic(IC),
    .valout(lfo[0]));
  reg_bit_2 reg_bit_2_2 (
    .clk1(clk1), .clk2(clk2), .val(write_data[1]), .load(nor_3_out), .nload(not_1_out), .ic(IC),
    .valout(lfo[1]));
  reg_bit_2 reg_bit_2_3 (
    .clk1(clk1), .clk2(clk2), .val(write_data[2]), .load(nor_3_out), .nload(not_1_out), .ic(IC),
    .valout(lfo[2]));
  reg_bit_4 reg_bit_4_1 (
    .clk1(clk1), .clk2(clk2), .val(write_data[3]), .load(nor_3_out), .nload(not_1_out), .ic(IC),
    .valout(lfo_en));
endmodule

module reg_kon (
  input  clk1,
  input  clk2,
  input  [8:0] write_data,
  input  [8:0] write_data_neg,
  input  addr_wr,
  input  data_wr,
  input  IC,
  output [2:0] chan,
  output [3:0] operator
);

  wire and_1_out, nor_1_out, nor_2_out, nor_3_out, not_1_out, sr_bit_1_nvalout, sr_bit_1_valout;

  nor nor_1 (nor_1_out, write_data[8], write_data[7], write_data[6], write_data_neg[5], write_data[4], write_data_neg[3], write_data[2], write_data[1], write_data[0], addr_wr);
  nor nor_2 (nor_2_out, nor_1_out, and_1_out);
  and and_1 (and_1_out, addr_wr, sr_bit_1_nvalout);
  sr_bit sr_bit_1 (.clk1(clk1), .clk2(clk2), .val(nor_2_out), .nvalout(sr_bit_1_nvalout), .valout(sr_bit_1_valout));
  nor nor_3 (nor_3_out, sr_bit_1_valout, write_data[8], data_wr);
  not not_1 (not_1_out, nor_3_out);
  reg_bit_2 reg_bit_2_1 (
    .clk1(clk1), .clk2(clk2), .val(write_data[0]), .load(nor_3_out), .nload(not_1_out), .ic(IC),
    .valout(chan[0]));
  reg_bit_2 reg_bit_2_2 (
    .clk1(clk1), .clk2(clk2), .val(write_data[1]), .load(nor_3_out), .nload(not_1_out), .ic(IC),
    .valout(chan[1]));
  reg_bit_2 reg_bit_2_3 (
    .clk1(clk1), .clk2(clk2), .val(write_data[2]), .load(nor_3_out), .nload(not_1_out), .ic(IC),
    .valout(chan[2]));
  reg_bit_4 reg_bit_4_1 (
    .clk1(clk1), .clk2(clk2), .val(write_data[4]), .load(nor_3_out), .nload(not_1_out), .ic(IC),
    .valout(operator[0]));
  reg_bit_4 reg_bit_4_2 (
    .clk1(clk1), .clk2(clk2), .val(write_data[5]), .load(nor_3_out), .nload(not_1_out), .ic(IC),
    .valout(operator[1]));
  reg_bit_4 reg_bit_4_3 (
    .clk1(clk1), .clk2(clk2), .val(write_data[6]), .load(nor_3_out), .nload(not_1_out), .ic(IC),
    .valout(operator[2]));
  reg_bit_4 reg_bit_4_4 (
    .clk1(clk1), .clk2(clk2), .val(write_data[7]), .load(nor_3_out), .nload(not_1_out), .ic(IC),
    .valout(operator[3]));
endmodule

module reg_test1 (
  input  clk1,
  input  clk2,
  input  [8:0] write_data,
  input  [8:0] write_data_neg,
  input  addr_wr,
  input  data_wr,
  input  IC,
  output [7:0] valout
);

  wire and_1_out, nor_1_out, nor_2_out, nor_3_out, not_1_out, sr_bit_1_nvalout, sr_bit_1_valout;

  nor nor_1 (nor_1_out, write_data[8], write_data[7], write_data[6], write_data_neg[5], write_data[4], write_data[3], write_data[2], write_data[1], write_data_neg[0], addr_wr);
  and and_1 (and_1_out, addr_wr, sr_bit_1_nvalout);
  nor nor_2 (nor_2_out, nor_1_out, and_1_out);
  sr_bit sr_bit_1 (.clk1(clk1), .clk2(clk2), .val(nor_2_out), .nvalout(sr_bit_1_nvalout), .valout(sr_bit_1_valout));
  nor nor_3 (nor_3_out, sr_bit_1_valout, write_data[8], data_wr);
  not not_1 (not_1_out, nor_3_out);
  reg_bit_2 reg_bit_2_1 (
    .clk1(clk1), .clk2(clk2), .val(write_data[0]), .load(nor_3_out), .nload(not_1_out), .ic(IC),
    .valout(valout[0]));
  reg_bit_4 reg_bit_4_1 (
    .clk1(clk1), .clk2(clk2), .val(write_data[2]), .load(nor_3_out), .nload(not_1_out), .ic(IC),
    .valout(valout[2]));
  reg_bit_2 reg_bit_2_2 (
    .clk1(clk1), .clk2(clk2), .val(write_data[3]), .load(nor_3_out), .nload(not_1_out), .ic(IC),
    .valout(valout[3]));
  reg_bit_4 reg_bit_4_2 (
    .clk1(clk1), .clk2(clk2), .val(write_data[4]), .load(nor_3_out), .nload(not_1_out), .ic(IC),
    .valout(valout[4]));
  reg_bit_2 reg_bit_2_3 (
    .clk1(clk1), .clk2(clk2), .val(write_data[5]), .load(nor_3_out), .nload(not_1_out), .ic(IC),
    .valout(valout[5]));
  reg_bit_2 reg_bit_2_4 (
    .clk1(clk1), .clk2(clk2), .val(write_data[6]), .load(nor_3_out), .nload(not_1_out), .ic(IC),
    .valout(valout[6]));
  reg_bit_2 reg_bit_2_5 (
    .clk1(clk1), .clk2(clk2), .val(write_data[7]), .load(nor_3_out), .nload(not_1_out), .ic(IC),
    .valout(valout[7]));
endmodule

module reg_ctrl (
  input  clk1,
  input  clk2,
  input  [8:0] write_data,
  input  addr_wr,
  input  data_wr,
  input  IC_l,
  input  IC,
  input  sync,
  output [7:0] data,
  output write40,
  output write70,
  output write50,
  output write60,
  output write80,
  output write30,
  output write90,
  output writeB0,
  output writeAC,
  output writeA0,
  output writeA4,
  output writeA8,
  output writeB4,
  output sel
);

  wire and_1_out, and_2_out, and_3_out, and_4_out, and_5_out, and_6_out, and_7_out, and_8_out, and_9_out,
       cnt_bit_1_cout, cnt_bit_1_valout, cnt_bit_2_valout, cnt_bit_3_cout, cnt_bit_3_valout,
       cnt_bit_4_valout, d_ff_1_qn, d_ff_2_qn, d_ff_3_q, d_ff_4_qn, nor_1_out, nor_2_out, nor_3_out,
       nor_4_out, nor_5_out, nor_6_out, nor_7_out, nor_8_out, nor_9_out, nor_10_out, nor_11_out, nor_12_out,
       nor_13_out, nor_14_out, nor_15_out, nor_16_out, nor_17_out, nor_18_out, nor_19_out, nor_20_out,
       nor_21_out, nor_22_out, not_1_out, not_2_out, not_3_out, not_4_out, not_5_out, not_6_out, not_7_out,
       or_1_out, or_2_out, or_3_out, or_4_out, sr_bit_1_nvalout, sr_bit_1_valout;
  wire [8:0] not_8_out, reg_bit_2_1_valout;

  or or_1 (or_1_out, or_2_out, d_ff_4_qn);
  D_Flip_Flop #(.trigger("high")) d_ff_1 (.D(sync), .clk(clk2), .Qn(d_ff_1_qn));  // open: Q, preset, reset
  nor nor_1 (nor_1_out, write_data[4], write_data[5], write_data[6], write_data[7]);
  cnt_bit cnt_bit_1 (
    .cin(1'b1), .ic(or_1_out), .clk1(clk1), .clk2(clk2), .cout(cnt_bit_1_cout), .valout(cnt_bit_1_valout));
  nor nor_2 (nor_2_out, cnt_bit_1_valout, not_4_out);
  nor nor_3 (nor_3_out, cnt_bit_2_valout, not_5_out);
  nor nor_4 (nor_4_out, cnt_bit_3_valout, not_6_out);
  nor nor_5 (nor_5_out, cnt_bit_4_valout, not_7_out);
  or or_2 (or_2_out, d_ff_1_qn, IC);
  nor nor_6 (nor_6_out, nor_1_out, addr_wr);
  not not_1 (not_1_out, d_ff_2_qn);
  and and_1 (and_1_out, addr_wr, sr_bit_1_nvalout);
  and and_2 (and_2_out, addr_wr, d_ff_3_q);
  nor nor_7 (nor_7_out, nor_6_out, and_1_out);
  nor nor_8 (nor_8_out, nor_9_out, and_2_out);
  and and_3 (and_3_out, cnt_bit_1_valout, not_4_out);
  and and_4 (and_4_out, cnt_bit_2_valout, not_5_out);
  and and_5 (and_5_out, cnt_bit_3_valout, not_6_out);
  and and_6 (and_6_out, cnt_bit_4_valout, not_7_out);
  and and_7 (and_7_out, cnt_bit_1_valout, not_4_out);
  and and_8 (and_8_out, cnt_bit_2_valout, not_5_out);
  and and_9 (and_9_out, cnt_bit_3_valout, not_6_out);
  sr_bit sr_bit_1 (.clk1(clk1), .clk2(clk2), .val(nor_7_out), .nvalout(sr_bit_1_nvalout), .valout(sr_bit_1_valout));
  D_Flip_Flop #(.trigger("high")) d_ff_2 (.D(nor_8_out), .clk(clk1), .Qn(d_ff_2_qn));  // open: Q, preset, reset
  cnt_bit cnt_bit_2 (
    .cin(cnt_bit_1_cout), .ic(or_1_out), .clk1(clk1), .clk2(clk2), .valout(cnt_bit_2_valout));  // open: cout
  D_Flip_Flop #(.trigger("high")) d_ff_3 (.D(d_ff_2_qn), .clk(clk2), .Q(d_ff_3_q));  // open: Qn, preset, reset
  or or_3 (or_3_out, and_3_out, nor_2_out, and_4_out, nor_3_out, and_5_out, nor_4_out, and_6_out, nor_5_out, not_1_out);
  or or_4 (or_4_out, and_7_out, nor_2_out, and_8_out, nor_3_out, and_9_out, nor_4_out, not_1_out);
  nor nor_9 (nor_9_out, sr_bit_1_valout, data_wr);
  D_Flip_Flop #(.trigger("high")) d_ff_4 (.D(cnt_bit_2_valout), .clk(clk2), .Qn(d_ff_4_qn));  // open: Q, preset, reset
  cnt_bit cnt_bit_3 (
    .cin(d_ff_4_qn), .ic(or_2_out), .clk1(clk1), .clk2(clk2), .cout(cnt_bit_3_cout), .valout(cnt_bit_3_valout));
  cnt_bit cnt_bit_4 (
    .cin(cnt_bit_3_cout), .ic(or_2_out), .clk1(clk1), .clk2(clk2), .valout(cnt_bit_4_valout));  // open: cout
  not not_2 (not_2_out, nor_6_out);
  reg_bit_2 reg_bit_2_1 (
    .clk1(clk1), .clk2(clk2), .val(write_data[0]), .load(nor_6_out), .nload(not_2_out), .ic(IC_l),
    .valout(reg_bit_2_1_valout[0]));
  reg_bit_2 reg_bit_2_2 (
    .clk1(clk1), .clk2(clk2), .val(write_data[1]), .load(nor_6_out), .nload(not_2_out), .ic(IC_l),
    .valout(reg_bit_2_1_valout[1]));
  reg_bit_2 reg_bit_2_3 (
    .clk1(clk1), .clk2(clk2), .val(write_data[2]), .load(nor_6_out), .nload(not_2_out), .ic(IC_l),
    .valout(reg_bit_2_1_valout[2]));
  reg_bit_2 reg_bit_2_4 (
    .clk1(clk1), .clk2(clk2), .val(write_data[3]), .load(nor_6_out), .nload(not_2_out), .ic(IC_l),
    .valout(reg_bit_2_1_valout[3]));
  reg_bit_2 reg_bit_2_5 (
    .clk1(clk1), .clk2(clk2), .val(write_data[4]), .load(nor_6_out), .nload(not_2_out), .ic(IC_l),
    .valout(reg_bit_2_1_valout[4]));
  reg_bit_2 reg_bit_2_6 (
    .clk1(clk1), .clk2(clk2), .val(write_data[5]), .load(nor_6_out), .nload(not_2_out), .ic(IC_l),
    .valout(reg_bit_2_1_valout[5]));
  reg_bit_2 reg_bit_2_7 (
    .clk1(clk1), .clk2(clk2), .val(write_data[6]), .load(nor_6_out), .nload(not_2_out), .ic(IC_l),
    .valout(reg_bit_2_1_valout[6]));
  reg_bit_2 reg_bit_2_8 (
    .clk1(clk1), .clk2(clk2), .val(write_data[7]), .load(nor_6_out), .nload(not_2_out), .ic(IC_l),
    .valout(reg_bit_2_1_valout[7]));
  reg_bit_2 reg_bit_2_9 (
    .clk1(clk1), .clk2(clk2), .val(write_data[8]), .load(nor_6_out), .nload(not_2_out), .ic(IC_l),
    .valout(reg_bit_2_1_valout[8]));
  not not_3 (not_3_out, nor_9_out);
  reg_bit_4 reg_bit_4_1 (
    .clk1(clk1), .clk2(clk2), .val(write_data[0]), .load(nor_9_out), .nload(not_3_out), .ic(IC_l),
    .valout(data[0]));
  reg_bit_4 reg_bit_4_2 (
    .clk1(clk1), .clk2(clk2), .val(write_data[1]), .load(nor_9_out), .nload(not_3_out), .ic(IC_l),
    .valout(data[1]));
  reg_bit_4 reg_bit_4_3 (
    .clk1(clk1), .clk2(clk2), .val(write_data[2]), .load(nor_9_out), .nload(not_3_out), .ic(IC_l),
    .valout(data[2]));
  reg_bit_4 reg_bit_4_4 (
    .clk1(clk1), .clk2(clk2), .val(write_data[3]), .load(nor_9_out), .nload(not_3_out), .ic(IC_l),
    .valout(data[3]));
  reg_bit_4 reg_bit_4_5 (
    .clk1(clk1), .clk2(clk2), .val(write_data[4]), .load(nor_9_out), .nload(not_3_out), .ic(IC_l),
    .valout(data[4]));
  reg_bit_4 reg_bit_4_6 (
    .clk1(clk1), .clk2(clk2), .val(write_data[5]), .load(nor_9_out), .nload(not_3_out), .ic(IC_l),
    .valout(data[5]));
  reg_bit_4 reg_bit_4_7 (
    .clk1(clk1), .clk2(clk2), .val(write_data[6]), .load(nor_9_out), .nload(not_3_out), .ic(IC_l),
    .valout(data[6]));
  reg_bit_4 reg_bit_4_8 (
    .clk1(clk1), .clk2(clk2), .val(write_data[7]), .load(nor_9_out), .nload(not_3_out), .ic(IC_l),
    .valout(data[7]));
  not not_4 (not_4_out, reg_bit_2_1_valout[0]);
  not not_5 (not_5_out, reg_bit_2_1_valout[1]);
  not not_6 (not_6_out, reg_bit_2_1_valout[8]);
  not not_7 (not_7_out, reg_bit_2_1_valout[2]);
  assign not_8_out = ~reg_bit_2_1_valout;  // NOT_Gate not_8, 9 bits wide
  D_Flip_Flop #(.trigger("high")) d_ff_5 (.D(nor_10_out), .clk(clk2), .Qn(write40));  // open: Q, preset, reset
  nor nor_10 (nor_10_out, not_8_out[7], reg_bit_2_1_valout[6], not_8_out[5], not_8_out[4], or_3_out);
  D_Flip_Flop #(.trigger("high")) d_ff_6 (.D(nor_11_out), .clk(clk2), .Qn(write70));  // open: Q, preset, reset
  nor nor_11 (nor_11_out, not_8_out[7], reg_bit_2_1_valout[6], reg_bit_2_1_valout[5], reg_bit_2_1_valout[4], or_3_out);
  D_Flip_Flop #(.trigger("high")) d_ff_7 (.D(nor_12_out), .clk(clk2), .Qn(write50));  // open: Q, preset, reset
  nor nor_12 (nor_12_out, not_8_out[7], reg_bit_2_1_valout[6], not_8_out[5], reg_bit_2_1_valout[4], or_3_out);
  D_Flip_Flop #(.trigger("high")) d_ff_8 (.D(nor_13_out), .clk(clk2), .Qn(write60));  // open: Q, preset, reset
  nor nor_13 (nor_13_out, not_8_out[7], reg_bit_2_1_valout[6], reg_bit_2_1_valout[5], not_8_out[4], or_3_out);
  D_Flip_Flop #(.trigger("high")) d_ff_9 (.D(nor_14_out), .clk(clk2), .Qn(write80));  // open: Q, preset, reset
  nor nor_14 (nor_14_out, reg_bit_2_1_valout[7], not_8_out[6], not_8_out[5], not_8_out[4], or_3_out);
  D_Flip_Flop #(.trigger("high")) d_ff_10 (.D(nor_15_out), .clk(clk2), .Qn(write30));  // open: Q, preset, reset
  nor nor_15 (nor_15_out, not_8_out[7], not_8_out[6], reg_bit_2_1_valout[5], reg_bit_2_1_valout[4], or_3_out);
  D_Flip_Flop #(.trigger("high")) d_ff_11 (.D(nor_16_out), .clk(clk2), .Qn(write90));  // open: Q, preset, reset
  nor nor_16 (nor_16_out, reg_bit_2_1_valout[7], not_8_out[6], not_8_out[5], reg_bit_2_1_valout[4], or_3_out);
  D_Flip_Flop #(.trigger("high")) d_ff_12 (.D(nor_17_out), .clk(clk2), .Qn(writeB0));  // open: Q, preset, reset
  nor nor_17 (nor_17_out, reg_bit_2_1_valout[7], not_8_out[6], reg_bit_2_1_valout[5], reg_bit_2_1_valout[4], not_8_out[3], not_8_out[2], or_4_out);
  D_Flip_Flop #(.trigger("high")) d_ff_13 (.D(nor_18_out), .clk(clk2), .Qn(writeAC));  // open: Q, preset, reset
  nor nor_18 (nor_18_out, reg_bit_2_1_valout[7], not_8_out[6], reg_bit_2_1_valout[5], not_8_out[4], reg_bit_2_1_valout[3], reg_bit_2_1_valout[2], or_4_out);
  D_Flip_Flop #(.trigger("high")) d_ff_14 (.D(nor_19_out), .clk(clk2), .Qn(writeA0));  // open: Q, preset, reset
  nor nor_19 (nor_19_out, reg_bit_2_1_valout[7], not_8_out[6], reg_bit_2_1_valout[5], not_8_out[4], not_8_out[3], not_8_out[2], or_4_out);
  D_Flip_Flop #(.trigger("high")) d_ff_15 (.D(nor_20_out), .clk(clk2), .Qn(writeA4));  // open: Q, preset, reset
  nor nor_20 (nor_20_out, reg_bit_2_1_valout[7], not_8_out[6], reg_bit_2_1_valout[5], not_8_out[4], not_8_out[3], reg_bit_2_1_valout[2], or_4_out);
  D_Flip_Flop #(.trigger("high")) d_ff_16 (.D(nor_21_out), .clk(clk2), .Qn(writeA8));  // open: Q, preset, reset
  nor nor_21 (nor_21_out, reg_bit_2_1_valout[7], not_8_out[6], reg_bit_2_1_valout[5], not_8_out[4], reg_bit_2_1_valout[3], not_8_out[2], or_4_out);
  D_Flip_Flop #(.trigger("high")) d_ff_17 (.D(nor_22_out), .clk(clk2), .Qn(writeB4));  // open: Q, preset, reset
  nor nor_22 (nor_22_out, reg_bit_2_1_valout[7], not_8_out[6], reg_bit_2_1_valout[5], reg_bit_2_1_valout[4], not_8_out[3], reg_bit_2_1_valout[2], or_4_out);
  D_Flip_Flop #(.trigger("high")) d_ff_18 (.D(reg_bit_2_1_valout[3]), .clk(clk2), .Qn(sel));  // open: Q, preset, reset
endmodule

module busy_cnt (
  input  clk1,
  input  clk2,
  input  data_wr,
  input  IC,
  output busy
);

  wire and_1_out, cnt_bit_1_cout, cnt_bit_2_cout, cnt_bit_3_cout, cnt_bit_4_cout, cnt_bit_5_cout, d_ff_1_qn,
       d_ff_2_q, d_ff_3_q, nor_1_out, nor_2_out, not_1_out;

  cnt_bit cnt_bit_1 (.cin(d_ff_3_q), .ic(IC), .clk1(clk1), .clk2(clk2), .cout(cnt_bit_1_cout));  // open: valout
  not not_1 (not_1_out, data_wr);
  nor nor_1 (nor_1_out, IC, cnt_bit_5_cout);
  and and_1 (and_1_out, nor_1_out, d_ff_2_q);
  cnt_bit cnt_bit_2 (.cin(cnt_bit_1_cout), .ic(IC), .clk1(clk1), .clk2(clk2), .cout(cnt_bit_2_cout));  // open: valout
  D_Flip_Flop #(.trigger("high")) d_ff_1 (.D(nor_2_out), .clk(clk1), .Qn(d_ff_1_qn));  // open: Q, preset, reset
  nor nor_2 (nor_2_out, not_1_out, and_1_out);
  D_Flip_Flop #(.trigger("high")) d_ff_2 (.D(d_ff_1_qn), .clk(clk2), .Q(d_ff_2_q));  // open: Qn, preset, reset
  not not_2 (busy, d_ff_1_qn);
  D_Flip_Flop #(.trigger("high")) d_ff_3 (.D(d_ff_1_qn), .clk(clk2), .Q(d_ff_3_q));  // open: Qn, preset, reset
  cnt_bit cnt_bit_3 (.cin(cnt_bit_2_cout), .ic(IC), .clk1(clk1), .clk2(clk2), .cout(cnt_bit_3_cout));  // open: valout
  cnt_bit cnt_bit_4 (.cin(cnt_bit_3_cout), .ic(IC), .clk1(clk1), .clk2(clk2), .cout(cnt_bit_4_cout));  // open: valout
  cnt_bit cnt_bit_5 (.cin(cnt_bit_4_cout), .ic(IC), .clk1(clk1), .clk2(clk2), .cout(cnt_bit_5_cout));  // open: valout
endmodule

module timers (
  input  clk1,
  input  clk2,
  input  IC,
  input  ch3_sel,
  input  csm_enable,
  input  clk_timers,
  input  timer_test,
  input  timer_a_load,
  input  timer_a_enable,
  input  timer_a_reset,
  input  [9:0] timer_a_val,
  input  timer_b_load,
  input  timer_b_enable,
  input  timer_b_reset,
  input  [7:0] timer_b_val,
  output keyon_csm,
  output timer_a_status,
  output timer_b_status
);

  wire and_1_out, and_2_out, and_3_out, and_4_out, cnt_bit_1_cout, cnt_bit_2_cout, cnt_bit_3_cout,
       cnt_bit_4_cout, d_ff_1_q, d_ff_1_qn, d_ff_2_qn, d_ff_3_qn, d_ff_4_qn, d_ff_5_q, d_ff_6_qn, d_ff_7_q,
       d_ff_8_q, d_ff_10_q, d_ff_12_q, nand_1_out, nand_2_out, nor_1_out, nor_2_out, nor_3_out, nor_4_out,
       nor_5_out, nor_6_out, not_1_out, not_2_out, not_3_out, not_4_out, not_5_out, not_6_out, not_7_out,
       not_8_out, not_9_out, not_10_out, or_1_out, or_2_out, or_3_out, or_4_out, sr_bit_1_nvalout,
       sr_bit_2_nvalout, sr_bit_3_nvalout, sr_bit_4_nvalout, sr_bit_5_valout, timer_bit_1_out_7,
       timer_bit_2_out_7, timer_bit_3_out_7, timer_bit_4_out_7, timer_bit_5_out_7, timer_bit_6_out_7,
       timer_bit_7_out_7, timer_bit_8_out_7, timer_bit_9_out_7, timer_bit_10_out_7, timer_bit_11_out_7,
       timer_bit_12_out_7, timer_bit_13_out_7, timer_bit_14_out_7, timer_bit_15_out_7, timer_bit_16_out_7,
       timer_bit_17_out_7, timer_bit_18_out_7;

  not not_1 (not_1_out, d_ff_3_qn);
  D_Flip_Flop #(.trigger("high")) d_ff_1 (
    .D(timer_b_load), .clk(nor_1_out), .Q(d_ff_1_q), .Qn(d_ff_1_qn));  // open: preset, reset
  not not_2 (not_2_out, d_ff_1_qn);
  and and_1 (and_1_out, not_2_out, sr_bit_5_valout);
  and and_2 (and_2_out, not_1_out, d_ff_2_qn);
  or or_1 (or_1_out, and_2_out, timer_test);
  or or_2 (or_2_out, and_1_out, timer_test);
  D_Flip_Flop #(.trigger("high")) d_ff_2 (.D(clk_timers), .clk(clk2), .Qn(d_ff_2_qn));  // open: Q, preset, reset
  cnt_bit cnt_bit_1 (.cin(d_ff_2_qn), .ic(IC), .clk1(clk1), .clk2(clk2), .cout(cnt_bit_1_cout));  // open: valout
  D_Flip_Flop #(.trigger("high")) d_ff_3 (.D(timer_a_load), .clk(nor_1_out), .Qn(d_ff_3_qn));  // open: Q, preset, reset
  D_Flip_Flop #(.trigger("high")) d_ff_4 (.D(d_ff_2_qn), .clk(clk1), .Qn(d_ff_4_qn));  // open: Q, preset, reset
  sr_bit sr_bit_1 (.clk1(clk1), .clk2(clk2), .val(d_ff_1_q), .nvalout(sr_bit_1_nvalout));  // open: valout
  timer_bit timer_bit_1 (
    .cin(or_1_out), .ic(d_ff_3_qn), .load(nand_2_out), .value(timer_a_val[0]), .clk1(clk1), .clk2(clk2),
    .out_7(timer_bit_1_out_7));
  timer_bit timer_bit_2 (
    .cin(timer_bit_17_out_7), .ic(d_ff_3_qn), .load(nand_2_out), .value(timer_a_val[5]), .clk1(clk1),
    .clk2(clk2), .out_7(timer_bit_2_out_7));
  timer_bit timer_bit_3 (
    .cin(or_2_out), .ic(d_ff_1_qn), .load(nand_1_out), .value(timer_b_val[0]), .clk1(clk1), .clk2(clk2),
    .out_7(timer_bit_3_out_7));
  timer_bit timer_bit_4 (
    .cin(timer_bit_15_out_7), .ic(d_ff_1_qn), .load(nand_1_out), .value(timer_b_val[4]), .clk1(clk1),
    .clk2(clk2), .out_7(timer_bit_4_out_7));
  sr_bit sr_bit_2 (.clk1(clk1), .clk2(clk2), .val(d_ff_3_qn), .nvalout(sr_bit_2_nvalout));  // open: valout
  D_Flip_Flop #(.trigger("high")) d_ff_5 (.D(d_ff_4_qn), .clk(clk2), .Q(d_ff_5_q));  // open: Qn, preset, reset
  sr_bit sr_bit_3 (.clk1(clk1), .clk2(clk2), .val(timer_bit_16_out_7), .nvalout(sr_bit_3_nvalout));  // open: valout
  or or_3 (or_3_out, sr_bit_2_nvalout, d_ff_3_qn);
  nor nor_1 (nor_1_out, d_ff_4_qn, d_ff_5_q);
  or or_4 (or_4_out, sr_bit_1_nvalout, d_ff_1_qn);
  not not_3 (not_3_out, timer_b_reset);
  cnt_bit cnt_bit_2 (.cin(cnt_bit_1_cout), .ic(IC), .clk1(clk1), .clk2(clk2), .cout(cnt_bit_2_cout));  // open: valout
  nand nand_1 (nand_1_out, or_4_out, sr_bit_3_nvalout);
  not not_4 (not_4_out, timer_b_enable);
  not not_5 (not_5_out, not_3_out);
  sr_bit sr_bit_4 (.clk1(clk1), .clk2(clk2), .val(timer_bit_18_out_7), .nvalout(sr_bit_4_nvalout));  // open: valout
  timer_bit timer_bit_5 (
    .cin(timer_bit_1_out_7), .ic(d_ff_3_qn), .load(nand_2_out), .value(timer_a_val[1]), .clk1(clk1),
    .clk2(clk2), .out_7(timer_bit_5_out_7));
  timer_bit timer_bit_6 (
    .cin(timer_bit_2_out_7), .ic(d_ff_3_qn), .load(nand_2_out), .value(timer_a_val[6]), .clk1(clk1),
    .clk2(clk2), .out_7(timer_bit_6_out_7));
  nor nor_2 (nor_2_out, not_4_out, not_3_out, sr_bit_3_nvalout);
  timer_bit timer_bit_7 (
    .cin(timer_bit_3_out_7), .ic(d_ff_1_qn), .load(nand_1_out), .value(timer_b_val[1]), .clk1(clk1),
    .clk2(clk2), .out_7(timer_bit_7_out_7));
  timer_bit timer_bit_8 (
    .cin(timer_bit_4_out_7), .ic(d_ff_1_qn), .load(nand_1_out), .value(timer_b_val[5]), .clk1(clk1),
    .clk2(clk2), .out_7(timer_bit_8_out_7));
  nand nand_2 (nand_2_out, or_3_out, sr_bit_4_nvalout);
  D_Flip_Flop #(.trigger("high")) d_ff_6 (.D(ch3_sel), .clk(clk2), .Qn(d_ff_6_qn));  // open: Q, preset, reset
  not not_6 (not_6_out, nand_2_out);
  D_Flip_Flop #(.trigger("high")) d_ff_7 (.D(csm_enable), .clk(clk2), .Q(d_ff_7_q));  // open: Qn, preset, reset
  not not_7 (not_7_out, sr_bit_4_nvalout);
  not not_8 (not_8_out, timer_a_reset);
  and and_3 (and_3_out, not_5_out, d_ff_10_q);
  cnt_bit cnt_bit_3 (.cin(cnt_bit_2_cout), .ic(IC), .clk1(clk1), .clk2(clk2), .cout(cnt_bit_3_cout));  // open: valout
  not not_9 (not_9_out, not_7_out);
  not not_10 (not_10_out, timer_a_enable);
  nor nor_3 (nor_3_out, nor_2_out, and_3_out);
  nor nor_4 (nor_4_out, not_6_out, d_ff_7_q);
  D_Flip_Flop #(.trigger("high")) d_ff_8 (.D(nor_4_out), .clk(nor_1_out), .Q(d_ff_8_q));  // open: Qn, preset, reset
  nor nor_5 (nor_5_out, not_9_out, not_8_out, not_10_out);
  timer_bit timer_bit_9 (
    .cin(timer_bit_5_out_7), .ic(d_ff_3_qn), .load(nand_2_out), .value(timer_a_val[2]), .clk1(clk1),
    .clk2(clk2), .out_7(timer_bit_9_out_7));
  timer_bit timer_bit_10 (
    .cin(timer_bit_6_out_7), .ic(d_ff_3_qn), .load(nand_2_out), .value(timer_a_val[7]), .clk1(clk1),
    .clk2(clk2), .out_7(timer_bit_10_out_7));
  D_Flip_Flop #(.trigger("high")) d_ff_9 (.D(nor_3_out), .clk(clk1), .Qn(timer_b_status));  // open: Q, preset, reset
  timer_bit timer_bit_11 (
    .cin(timer_bit_7_out_7), .ic(d_ff_1_qn), .load(nand_1_out), .value(timer_b_val[2]), .clk1(clk1),
    .clk2(clk2), .out_7(timer_bit_11_out_7));
  timer_bit timer_bit_12 (
    .cin(timer_bit_8_out_7), .ic(d_ff_1_qn), .load(nand_1_out), .value(timer_b_val[6]), .clk1(clk1),
    .clk2(clk2), .out_7(timer_bit_12_out_7));
  and and_4 (and_4_out, not_8_out, d_ff_12_q);
  D_Flip_Flop #(.trigger("high")) d_ff_10 (.D(timer_b_status), .clk(clk2), .Q(d_ff_10_q));  // open: Qn, preset, reset
  nand nand_3 (keyon_csm, d_ff_6_qn, d_ff_8_q);
  nor nor_6 (nor_6_out, nor_5_out, and_4_out);
  cnt_bit cnt_bit_4 (.cin(cnt_bit_3_cout), .ic(IC), .clk1(clk1), .clk2(clk2), .cout(cnt_bit_4_cout));  // open: valout
  D_Flip_Flop #(.trigger("high")) d_ff_11 (.D(nor_6_out), .clk(clk1), .Qn(timer_a_status));  // open: Q, preset, reset
  sr_bit sr_bit_5 (.clk1(clk1), .clk2(clk2), .val(cnt_bit_4_cout), .valout(sr_bit_5_valout));  // open: nvalout
  timer_bit timer_bit_13 (
    .cin(timer_bit_9_out_7), .ic(d_ff_3_qn), .load(nand_2_out), .value(timer_a_val[3]), .clk1(clk1),
    .clk2(clk2), .out_7(timer_bit_13_out_7));
  timer_bit timer_bit_14 (
    .cin(timer_bit_10_out_7), .ic(d_ff_3_qn), .load(nand_2_out), .value(timer_a_val[8]), .clk1(clk1),
    .clk2(clk2), .out_7(timer_bit_14_out_7));
  timer_bit timer_bit_15 (
    .cin(timer_bit_11_out_7), .ic(d_ff_1_qn), .load(nand_1_out), .value(timer_b_val[3]), .clk1(clk1),
    .clk2(clk2), .out_7(timer_bit_15_out_7));
  timer_bit timer_bit_16 (
    .cin(timer_bit_12_out_7), .ic(d_ff_1_qn), .load(nand_1_out), .value(timer_b_val[7]), .clk1(clk1),
    .clk2(clk2), .out_7(timer_bit_16_out_7));
  D_Flip_Flop #(.trigger("high")) d_ff_12 (.D(timer_a_status), .clk(clk2), .Q(d_ff_12_q));  // open: Qn, preset, reset
  timer_bit timer_bit_17 (
    .cin(timer_bit_13_out_7), .ic(d_ff_3_qn), .load(nand_2_out), .value(timer_a_val[4]), .clk1(clk1),
    .clk2(clk2), .out_7(timer_bit_17_out_7));
  timer_bit timer_bit_18 (
    .cin(timer_bit_14_out_7), .ic(d_ff_3_qn), .load(nand_2_out), .value(timer_a_val[9]), .clk1(clk1),
    .clk2(clk2), .out_7(timer_bit_18_out_7));
endmodule

module keyon (
  input  clk1,
  input  clk2,
  input  IC,
  input  sync,
  input  [2:0] chan,
  input  [3:0] op,
  input  csm_kon,
  output op_reg_bank_sel,
  output keyon
);

  wire and_1_out, and_2_out, and_3_out, and_4_out, and_5_out, and_6_out, and_7_out, cnt_bit_1_cout,
       cnt_bit_1_valout, cnt_bit_2_valout, cnt_bit_3_cout, cnt_bit_3_valout, cnt_bit_4_cout,
       cnt_bit_4_valout, controlled_buffer_1_out, controlled_buffer_3_out, controlled_buffer_5_out,
       d_ff_1_qn, d_ff_2_q, d_ff_2_qn, d_ff_3_qn, d_ff_4_qn, d_ff_5_qn, d_ff_6_q, nor_1_out, nor_2_out,
       nor_3_out, nor_4_out, nor_5_out, nor_6_out, nor_7_out, not_1_out, not_2_out, not_3_out, not_4_out,
       or_1_out, or_2_out, or_3_out, sr_bit_1_valout, sr_bit_2_valout, sr_bit_3_valout, sr_bit_4_valout,
       sr_bit_5_valout, sr_bit_6_valout, sr_bit_7_valout, sr_bit_8_valout, sr_bit_9_valout, sr_bit_10_valout,
       sr_bit_11_valout, sr_bit_12_valout, sr_bit_13_valout, sr_bit_14_valout, sr_bit_15_valout,
       sr_bit_16_valout, sr_bit_17_valout, sr_bit_18_valout, sr_bit_19_valout, sr_bit_20_valout,
       sr_bit_21_valout, sr_bit_22_valout, sr_bit_23_valout;

  D_Flip_Flop #(.trigger("high")) d_ff_1 (.D(sync), .clk(clk2), .Qn(d_ff_1_qn));  // open: Q, preset, reset
  not not_1 (not_1_out, chan[1]);
  not not_2 (not_2_out, chan[2]);
  not not_3 (not_3_out, chan[0]);
  or or_1 (or_1_out, IC, d_ff_1_qn);
  or or_2 (or_2_out, or_1_out, d_ff_3_qn);
  and and_1 (and_1_out, cnt_bit_1_valout, not_3_out);
  nor nor_1 (nor_1_out, cnt_bit_1_valout, not_3_out);
  and and_2 (and_2_out, cnt_bit_2_valout, not_1_out);
  nor nor_2 (nor_2_out, cnt_bit_2_valout, not_1_out);
  and and_3 (and_3_out, cnt_bit_3_valout, not_2_out);
  nor nor_3 (nor_3_out, cnt_bit_3_valout, not_2_out);
  and and_4 (and_4_out, cnt_bit_4_valout, 1'b0);
  nor nor_4 (nor_4_out, cnt_bit_4_valout, 1'b0);
  and and_5 (and_5_out, op_reg_bank_sel, 1'b0);
  nor nor_5 (nor_5_out, op_reg_bank_sel, 1'b0);
  nor nor_6 (nor_6_out, not_3_out, not_1_out);
  cnt_bit cnt_bit_1 (
    .cin(1'b1), .ic(or_2_out), .clk1(clk1), .clk2(clk2), .cout(cnt_bit_1_cout), .valout(cnt_bit_1_valout));
  sr_bit sr_bit_1 (.clk1(clk1), .clk2(clk2), .val(or_3_out), .valout(sr_bit_1_valout));  // open: nvalout
  sr_bit sr_bit_2 (.clk1(clk1), .clk2(clk2), .val(controlled_buffer_1_out), .valout(sr_bit_2_valout));  // open: nvalout
  sr_bit sr_bit_3 (.clk1(clk1), .clk2(clk2), .val(controlled_buffer_3_out), .valout(sr_bit_3_valout));  // open: nvalout
  sr_bit sr_bit_4 (.clk1(clk1), .clk2(clk2), .val(controlled_buffer_5_out), .valout(sr_bit_4_valout));  // open: nvalout
  nor nor_7 (nor_7_out, and_1_out, nor_1_out, and_2_out, nor_2_out, and_3_out, nor_3_out, and_4_out, nor_4_out, and_5_out, nor_5_out, nor_6_out);
  sr_bit sr_bit_5 (.clk1(clk1), .clk2(clk2), .val(sr_bit_1_valout), .valout(sr_bit_5_valout));  // open: nvalout
  sr_bit sr_bit_6 (.clk1(clk1), .clk2(clk2), .val(sr_bit_2_valout), .valout(sr_bit_6_valout));  // open: nvalout
  sr_bit sr_bit_7 (.clk1(clk1), .clk2(clk2), .val(sr_bit_3_valout), .valout(sr_bit_7_valout));  // open: nvalout
  sr_bit sr_bit_8 (.clk1(clk1), .clk2(clk2), .val(sr_bit_4_valout), .valout(sr_bit_8_valout));  // open: nvalout
  D_Flip_Flop #(.trigger("high")) d_ff_2 (
    .D(nor_7_out), .clk(clk2), .Q(d_ff_2_q), .Qn(d_ff_2_qn));  // open: preset, reset
  cnt_bit cnt_bit_2 (
    .cin(cnt_bit_1_cout), .ic(or_2_out), .clk1(clk1), .clk2(clk2), .valout(cnt_bit_2_valout));  // open: cout
  sr_bit sr_bit_9 (.clk1(clk1), .clk2(clk2), .val(sr_bit_5_valout), .valout(sr_bit_9_valout));  // open: nvalout
  sr_bit sr_bit_10 (.clk1(clk1), .clk2(clk2), .val(sr_bit_6_valout), .valout(sr_bit_10_valout));  // open: nvalout
  sr_bit sr_bit_11 (.clk1(clk1), .clk2(clk2), .val(sr_bit_7_valout), .valout(sr_bit_11_valout));  // open: nvalout
  sr_bit sr_bit_12 (.clk1(clk1), .clk2(clk2), .val(sr_bit_8_valout), .valout(sr_bit_12_valout));  // open: nvalout
  D_Flip_Flop #(.trigger("high")) d_ff_3 (.D(cnt_bit_2_valout), .Qn(d_ff_3_qn));  // open: clk, Q, preset, reset
  sr_bit sr_bit_13 (.clk1(clk1), .clk2(clk2), .val(sr_bit_9_valout), .valout(sr_bit_13_valout));  // open: nvalout
  sr_bit sr_bit_14 (.clk1(clk1), .clk2(clk2), .val(sr_bit_10_valout), .valout(sr_bit_14_valout));  // open: nvalout
  sr_bit sr_bit_15 (.clk1(clk1), .clk2(clk2), .val(sr_bit_11_valout), .valout(sr_bit_15_valout));  // open: nvalout
  sr_bit sr_bit_16 (.clk1(clk1), .clk2(clk2), .val(sr_bit_12_valout), .valout(sr_bit_16_valout));  // open: nvalout
  sr_bit sr_bit_17 (.clk1(clk1), .clk2(clk2), .val(sr_bit_13_valout), .valout(sr_bit_17_valout));  // open: nvalout
  sr_bit sr_bit_18 (.clk1(clk1), .clk2(clk2), .val(sr_bit_14_valout), .valout(sr_bit_18_valout));  // open: nvalout
  sr_bit sr_bit_19 (.clk1(clk1), .clk2(clk2), .val(sr_bit_15_valout), .valout(sr_bit_19_valout));  // open: nvalout
  sr_bit sr_bit_20 (.clk1(clk1), .clk2(clk2), .val(sr_bit_16_valout), .valout(sr_bit_20_valout));  // open: nvalout
  sr_bit sr_bit_21 (.clk1(clk1), .clk2(clk2), .val(sr_bit_17_valout), .valout(sr_bit_21_valout));  // open: nvalout
  sr_bit sr_bit_22 (.clk1(clk1), .clk2(clk2), .val(sr_bit_18_valout), .valout(sr_bit_22_valout));  // open: nvalout
  sr_bit sr_bit_23 (.clk1(clk1), .clk2(clk2), .val(sr_bit_19_valout), .valout(sr_bit_23_valout));  // open: nvalout
  D_Flip_Flop #(.trigger("high")) d_ff_4 (.D(sr_bit_20_valout), .clk(clk1), .Qn(d_ff_4_qn));  // open: Q, preset, reset
  D_Flip_Flop #(.trigger("high")) d_ff_5 (.D(d_ff_4_qn), .clk(clk2), .Qn(d_ff_5_qn));  // open: Q, preset, reset
  D_Flip_Flop #(.trigger("high")) d_ff_6 (.D(d_ff_4_qn), .clk(clk2), .Q(d_ff_6_q));  // open: Qn, preset, reset
  cnt_bit cnt_bit_3 (
    .cin(d_ff_3_qn), .ic(or_1_out), .clk1(clk1), .clk2(clk2), .cout(cnt_bit_3_cout), .valout(cnt_bit_3_valout));
  assign controlled_buffer_1_out = d_ff_2_qn ? sr_bit_21_valout : 1'bz;  // Controlled_Buffer controlled_buffer_1
  assign controlled_buffer_1_out = d_ff_2_q ? op[3] : 1'bz;  // Controlled_Buffer controlled_buffer_2
  assign controlled_buffer_3_out = d_ff_2_qn ? sr_bit_22_valout : 1'bz;  // Controlled_Buffer controlled_buffer_3
  assign controlled_buffer_3_out = d_ff_2_q ? op[1] : 1'bz;  // Controlled_Buffer controlled_buffer_4
  assign controlled_buffer_5_out = d_ff_2_qn ? sr_bit_23_valout : 1'bz;  // Controlled_Buffer controlled_buffer_5
  assign controlled_buffer_5_out = d_ff_2_q ? op[2] : 1'bz;  // Controlled_Buffer controlled_buffer_6
  and and_6 (and_6_out, d_ff_2_q, op[0]);
  not not_4 (not_4_out, IC);
  and and_7 (and_7_out, d_ff_2_qn, not_4_out, d_ff_5_qn);
  or or_3 (or_3_out, and_6_out, and_7_out);
  cnt_bit cnt_bit_4 (
    .cin(cnt_bit_3_cout), .ic(or_1_out), .clk1(clk1), .clk2(clk2), .cout(cnt_bit_4_cout),
    .valout(cnt_bit_4_valout));
  cnt_bit cnt_bit_5 (
    .cin(cnt_bit_4_cout), .ic(or_1_out), .clk1(clk1), .clk2(clk2), .valout(op_reg_bank_sel));  // open: cout
  nand nand_1 (keyon, d_ff_6_q, csm_kon);
endmodule

module keyon_2612 (
  input  clk1,
  input  clk2,
  input  IC,
  input  sync,
  input  [2:0] chan,
  input  [3:0] op,
  input  csm_kon,
  output op_reg_bank_sel,
  output keyon
);

  wire and_1_out, and_2_out, and_3_out, and_4_out, and_5_out, and_6_out, and_7_out, cnt_bit_1_cout,
       cnt_bit_1_valout, cnt_bit_2_valout, cnt_bit_3_cout, cnt_bit_3_valout, cnt_bit_4_cout,
       cnt_bit_4_valout, controlled_buffer_1_out, controlled_buffer_3_out, controlled_buffer_5_out,
       d_ff_1_qn, d_ff_2_q, d_ff_2_qn, d_ff_3_qn, d_ff_4_qn, d_ff_5_qn, d_ff_6_q, nor_1_out, nor_2_out,
       nor_3_out, nor_4_out, nor_5_out, nor_6_out, not_1_out, not_2_out, not_3_out, not_4_out, or_1_out,
       or_2_out, or_3_out, sr_bit_1_valout, sr_bit_2_valout, sr_bit_3_valout, sr_bit_4_valout,
       sr_bit_5_valout, sr_bit_6_valout, sr_bit_7_valout, sr_bit_8_valout, sr_bit_9_valout, sr_bit_10_valout,
       sr_bit_11_valout, sr_bit_12_valout, sr_bit_13_valout, sr_bit_14_valout, sr_bit_15_valout,
       sr_bit_16_valout, sr_bit_17_valout, sr_bit_18_valout, sr_bit_19_valout, sr_bit_20_valout,
       sr_bit_21_valout, sr_bit_22_valout, sr_bit_23_valout;

  D_Flip_Flop #(.trigger("high")) d_ff_1 (.D(sync), .clk(clk2), .Qn(d_ff_1_qn));  // open: Q, preset, reset
  not not_1 (not_1_out, chan[1]);
  not not_2 (not_2_out, chan[2]);
  not not_3 (not_3_out, chan[0]);
  or or_1 (or_1_out, IC, d_ff_1_qn);
  or or_2 (or_2_out, or_1_out, d_ff_3_qn);
  and and_1 (and_1_out, cnt_bit_1_valout, not_3_out);
  nor nor_1 (nor_1_out, cnt_bit_1_valout, not_3_out);
  and and_2 (and_2_out, cnt_bit_2_valout, not_1_out);
  nor nor_2 (nor_2_out, cnt_bit_2_valout, not_1_out);
  and and_3 (and_3_out, cnt_bit_3_valout, not_2_out);
  nor nor_3 (nor_3_out, cnt_bit_3_valout, not_2_out);
  and and_4 (and_4_out, cnt_bit_4_valout, 1'b0);
  nor nor_4 (nor_4_out, cnt_bit_4_valout, 1'b0);
  and and_5 (and_5_out, op_reg_bank_sel, 1'b0);
  nor nor_5 (nor_5_out, op_reg_bank_sel, 1'b0);
  cnt_bit cnt_bit_1 (
    .cin(1'b1), .ic(or_2_out), .clk1(clk1), .clk2(clk2), .cout(cnt_bit_1_cout), .valout(cnt_bit_1_valout));
  sr_bit sr_bit_1 (.clk1(clk1), .clk2(clk2), .val(or_3_out), .valout(sr_bit_1_valout));  // open: nvalout
  sr_bit sr_bit_2 (.clk1(clk1), .clk2(clk2), .val(controlled_buffer_1_out), .valout(sr_bit_2_valout));  // open: nvalout
  sr_bit sr_bit_3 (.clk1(clk1), .clk2(clk2), .val(controlled_buffer_3_out), .valout(sr_bit_3_valout));  // open: nvalout
  sr_bit sr_bit_4 (.clk1(clk1), .clk2(clk2), .val(controlled_buffer_5_out), .valout(sr_bit_4_valout));  // open: nvalout
  nor nor_6 (nor_6_out, and_1_out, nor_1_out, and_2_out, nor_2_out, and_3_out, nor_3_out, and_4_out, nor_4_out, and_5_out, nor_5_out);
  sr_bit sr_bit_5 (.clk1(clk1), .clk2(clk2), .val(sr_bit_1_valout), .valout(sr_bit_5_valout));  // open: nvalout
  sr_bit sr_bit_6 (.clk1(clk1), .clk2(clk2), .val(sr_bit_2_valout), .valout(sr_bit_6_valout));  // open: nvalout
  sr_bit sr_bit_7 (.clk1(clk1), .clk2(clk2), .val(sr_bit_3_valout), .valout(sr_bit_7_valout));  // open: nvalout
  sr_bit sr_bit_8 (.clk1(clk1), .clk2(clk2), .val(sr_bit_4_valout), .valout(sr_bit_8_valout));  // open: nvalout
  D_Flip_Flop #(.trigger("high")) d_ff_2 (
    .D(nor_6_out), .clk(clk2), .Q(d_ff_2_q), .Qn(d_ff_2_qn));  // open: preset, reset
  cnt_bit cnt_bit_2 (
    .cin(cnt_bit_1_cout), .ic(or_2_out), .clk1(clk1), .clk2(clk2), .valout(cnt_bit_2_valout));  // open: cout
  sr_bit sr_bit_9 (.clk1(clk1), .clk2(clk2), .val(sr_bit_5_valout), .valout(sr_bit_9_valout));  // open: nvalout
  sr_bit sr_bit_10 (.clk1(clk1), .clk2(clk2), .val(sr_bit_6_valout), .valout(sr_bit_10_valout));  // open: nvalout
  sr_bit sr_bit_11 (.clk1(clk1), .clk2(clk2), .val(sr_bit_7_valout), .valout(sr_bit_11_valout));  // open: nvalout
  sr_bit sr_bit_12 (.clk1(clk1), .clk2(clk2), .val(sr_bit_8_valout), .valout(sr_bit_12_valout));  // open: nvalout
  D_Flip_Flop #(.trigger("high")) d_ff_3 (.D(cnt_bit_2_valout), .Qn(d_ff_3_qn));  // open: clk, Q, preset, reset
  sr_bit sr_bit_13 (.clk1(clk1), .clk2(clk2), .val(sr_bit_9_valout), .valout(sr_bit_13_valout));  // open: nvalout
  sr_bit sr_bit_14 (.clk1(clk1), .clk2(clk2), .val(sr_bit_10_valout), .valout(sr_bit_14_valout));  // open: nvalout
  sr_bit sr_bit_15 (.clk1(clk1), .clk2(clk2), .val(sr_bit_11_valout), .valout(sr_bit_15_valout));  // open: nvalout
  sr_bit sr_bit_16 (.clk1(clk1), .clk2(clk2), .val(sr_bit_12_valout), .valout(sr_bit_16_valout));  // open: nvalout
  sr_bit sr_bit_17 (.clk1(clk1), .clk2(clk2), .val(sr_bit_13_valout), .valout(sr_bit_17_valout));  // open: nvalout
  sr_bit sr_bit_18 (.clk1(clk1), .clk2(clk2), .val(sr_bit_14_valout), .valout(sr_bit_18_valout));  // open: nvalout
  sr_bit sr_bit_19 (.clk1(clk1), .clk2(clk2), .val(sr_bit_15_valout), .valout(sr_bit_19_valout));  // open: nvalout
  sr_bit sr_bit_20 (.clk1(clk1), .clk2(clk2), .val(sr_bit_16_valout), .valout(sr_bit_20_valout));  // open: nvalout
  sr_bit sr_bit_21 (.clk1(clk1), .clk2(clk2), .val(sr_bit_17_valout), .valout(sr_bit_21_valout));  // open: nvalout
  sr_bit sr_bit_22 (.clk1(clk1), .clk2(clk2), .val(sr_bit_18_valout), .valout(sr_bit_22_valout));  // open: nvalout
  sr_bit sr_bit_23 (.clk1(clk1), .clk2(clk2), .val(sr_bit_19_valout), .valout(sr_bit_23_valout));  // open: nvalout
  D_Flip_Flop #(.trigger("high")) d_ff_4 (.D(sr_bit_20_valout), .clk(clk1), .Qn(d_ff_4_qn));  // open: Q, preset, reset
  D_Flip_Flop #(.trigger("high")) d_ff_5 (.D(d_ff_4_qn), .clk(clk2), .Qn(d_ff_5_qn));  // open: Q, preset, reset
  D_Flip_Flop #(.trigger("high")) d_ff_6 (.D(d_ff_4_qn), .clk(clk2), .Q(d_ff_6_q));  // open: Qn, preset, reset
  cnt_bit cnt_bit_3 (
    .cin(d_ff_3_qn), .ic(or_1_out), .clk1(clk1), .clk2(clk2), .cout(cnt_bit_3_cout), .valout(cnt_bit_3_valout));
  assign controlled_buffer_1_out = d_ff_2_qn ? sr_bit_21_valout : 1'bz;  // Controlled_Buffer controlled_buffer_1
  assign controlled_buffer_1_out = d_ff_2_q ? op[3] : 1'bz;  // Controlled_Buffer controlled_buffer_2
  assign controlled_buffer_3_out = d_ff_2_qn ? sr_bit_22_valout : 1'bz;  // Controlled_Buffer controlled_buffer_3
  assign controlled_buffer_3_out = d_ff_2_q ? op[1] : 1'bz;  // Controlled_Buffer controlled_buffer_4
  assign controlled_buffer_5_out = d_ff_2_qn ? sr_bit_23_valout : 1'bz;  // Controlled_Buffer controlled_buffer_5
  assign controlled_buffer_5_out = d_ff_2_q ? op[2] : 1'bz;  // Controlled_Buffer controlled_buffer_6
  and and_6 (and_6_out, d_ff_2_q, op[0]);
  not not_4 (not_4_out, IC);
  and and_7 (and_7_out, d_ff_2_qn, not_4_out, d_ff_5_qn);
  or or_3 (or_3_out, and_6_out, and_7_out);
  cnt_bit cnt_bit_4 (
    .cin(cnt_bit_3_cout), .ic(or_1_out), .clk1(clk1), .clk2(clk2), .cout(cnt_bit_4_cout),
    .valout(cnt_bit_4_valout));
  cnt_bit cnt_bit_5 (
    .cin(cnt_bit_4_cout), .ic(or_1_out), .clk1(clk1), .clk2(clk2), .valout(op_reg_bank_sel));  // open: cout
  nand nand_1 (keyon, d_ff_6_q, csm_kon);
endmodule

module reg_glob_2612 (
  input  clk1,
  input  clk2,
  input  [8:0] write_data,
  input  [8:0] write_data_neg,
  input  addr_wr,
  input  data_wr,
  input  IC,
  input  sync,
  input  ch3_sel,
  input  sync_timer,
  output [7:0] data,
  output write40,
  output write70,
  output write50,
  output write60,
  output write80,
  output write30,
  output write90,
  output writeB0,
  output writeAC,
  output writeA0,
  output writeA4,
  output writeA8,
  output writeB4,
  output sel,
  output busy,
  output op_reg_bank,
  output kon,
  output kon_csm,
  output timer_a_status,
  output timer_b_status,
  output [7:0] test1,
  output [2:0] lfo,
  output lfo_en,
  output ch3_ext,
  output [7:0] test2,
  output [7:0] dac,
  output dac_en
);

  wire d_ff_1_qn, reg_timer_ctrl_1_csm_enable, reg_timer_ctrl_1_enable_a, reg_timer_ctrl_1_enable_b,
       reg_timer_ctrl_1_load_a, reg_timer_ctrl_1_load_b, reg_timer_ctrl_1_reset_a, reg_timer_ctrl_1_reset_b;
  wire [2:0] reg_kon_1_chan;
  wire [3:0] reg_kon_1_operator;
  wire [7:0] reg_timerb_1_valout;
  wire [9:0] reg_timera_1_valout;

  D_Flip_Flop #(.trigger("high")) d_ff_1 (.D(IC), .clk(clk1), .Qn(d_ff_1_qn));  // open: Q, preset, reset
  reg_test1_2612 reg_test1_2612_1 (
    .clk1(clk1), .clk2(clk2), .write_data(write_data), .write_data_neg(write_data_neg), .addr_wr(addr_wr),
    .data_wr(data_wr), .IC(d_ff_1_qn), .valout(test1));
  reg_lfo reg_lfo_1 (
    .clk1(clk1), .clk2(clk2), .write_data(write_data), .write_data_neg(write_data_neg), .addr_wr(addr_wr),
    .data_wr(data_wr), .IC(d_ff_1_qn), .lfo(lfo), .lfo_en(lfo_en));
  reg_timera reg_timera_1 (
    .clk1(clk1), .clk2(clk2), .write_data(write_data), .write_data_neg(write_data_neg), .addr_wr(addr_wr),
    .data_wr(data_wr), .IC(d_ff_1_qn), .valout(reg_timera_1_valout));
  reg_timerb reg_timerb_1 (
    .clk1(clk1), .clk2(clk2), .write_data(write_data), .write_data_neg(write_data_neg), .addr_wr(addr_wr),
    .data_wr(data_wr), .IC(d_ff_1_qn), .valout(reg_timerb_1_valout));
  reg_timer_ctrl reg_timer_ctrl_1 (
    .clk1(clk1), .clk2(clk2), .write_data(write_data), .write_data_neg(write_data_neg), .addr_wr(addr_wr),
    .data_wr(data_wr), .IC(d_ff_1_qn), .load_a(reg_timer_ctrl_1_load_a), .load_b(reg_timer_ctrl_1_load_b),
    .enable_a(reg_timer_ctrl_1_enable_a), .enable_b(reg_timer_ctrl_1_enable_b), .ch3_ext(ch3_ext),
    .csm_enable(reg_timer_ctrl_1_csm_enable), .reset_a(reg_timer_ctrl_1_reset_a),
    .reset_b(reg_timer_ctrl_1_reset_b));
  reg_kon reg_kon_1 (
    .clk1(clk1), .clk2(clk2), .write_data(write_data), .write_data_neg(write_data_neg), .addr_wr(addr_wr),
    .data_wr(data_wr), .IC(d_ff_1_qn), .chan(reg_kon_1_chan), .operator(reg_kon_1_operator));
  reg_test2_2612 reg_test2_2612_1 (
    .clk1(clk1), .clk2(clk2), .write_data(write_data), .write_data_neg(write_data_neg), .addr_wr(addr_wr),
    .data_wr(data_wr), .IC(d_ff_1_qn), .valout(test2));
  reg_dac_2612 reg_dac_2612_1 (
    .clk1(clk1), .clk2(clk2), .write_data(write_data), .write_data_neg(write_data_neg), .addr_wr(addr_wr),
    .data_wr(data_wr), .IC(d_ff_1_qn), .valout(dac));
  reg_dac_en_2612 reg_dac_en_2612_1 (
    .clk1(clk1), .clk2(clk2), .write_data(write_data), .write_data_neg(write_data_neg), .addr_wr(addr_wr),
    .data_wr(data_wr), .IC(d_ff_1_qn), .valout(dac_en));
  busy_cnt busy_cnt_1 (.clk1(clk1), .clk2(clk2), .data_wr(data_wr), .IC(IC), .busy(busy));
  keyon_2612 keyon_2612_1 (
    .clk1(clk1), .clk2(clk2), .IC(IC), .sync(sync), .chan(reg_kon_1_chan), .op(reg_kon_1_operator),
    .csm_kon(kon_csm), .op_reg_bank_sel(op_reg_bank), .keyon(kon));
  timers timers_1 (
    .clk1(clk1), .clk2(clk2), .IC(IC), .ch3_sel(ch3_sel), .csm_enable(reg_timer_ctrl_1_csm_enable),
    .clk_timers(sync_timer), .timer_test(test1[2]), .timer_a_load(reg_timer_ctrl_1_load_a),
    .timer_a_enable(reg_timer_ctrl_1_enable_a), .timer_a_reset(reg_timer_ctrl_1_reset_a),
    .timer_a_val(reg_timera_1_valout), .timer_b_load(reg_timer_ctrl_1_load_b),
    .timer_b_enable(reg_timer_ctrl_1_enable_b), .timer_b_reset(reg_timer_ctrl_1_reset_b),
    .timer_b_val(reg_timerb_1_valout), .keyon_csm(kon_csm), .timer_a_status(timer_a_status),
    .timer_b_status(timer_b_status));
  reg_ctrl reg_ctrl_1 (
    .clk1(clk1), .clk2(clk2), .write_data(write_data), .addr_wr(addr_wr), .data_wr(data_wr),
    .IC_l(d_ff_1_qn), .IC(IC), .sync(sync), .data(data), .write40(write40), .write70(write70),
    .write50(write50), .write60(write60), .write80(write80), .write30(write30), .write90(write90),
    .writeB0(writeB0), .writeAC(writeAC), .writeA0(writeA0), .writeA4(writeA4), .writeA8(writeA8),
    .writeB4(writeB4), .sel(sel));
endmodule

module reg_test1_2612 (
  input  clk1,
  input  clk2,
  input  [8:0] write_data,
  input  [8:0] write_data_neg,
  input  addr_wr,
  input  data_wr,
  input  IC,
  output [7:0] valout
);

  wire and_1_out, nor_1_out, nor_2_out, nor_3_out, not_1_out, sr_bit_1_nvalout, sr_bit_1_valout;

  nor nor_1 (nor_1_out, write_data[8], write_data[7], write_data[6], write_data_neg[5], write_data[4], write_data[3], write_data[2], write_data[1], write_data_neg[0], addr_wr);
  and and_1 (and_1_out, addr_wr, sr_bit_1_nvalout);
  nor nor_2 (nor_2_out, nor_1_out, and_1_out);
  sr_bit sr_bit_1 (.clk1(clk1), .clk2(clk2), .val(nor_2_out), .nvalout(sr_bit_1_nvalout), .valout(sr_bit_1_valout));
  nor nor_3 (nor_3_out, sr_bit_1_valout, write_data[8], data_wr);
  not not_1 (not_1_out, nor_3_out);
  reg_bit_2 reg_bit_2_1 (
    .clk1(clk1), .clk2(clk2), .val(write_data[0]), .load(nor_3_out), .nload(not_1_out), .ic(IC),
    .valout(valout[0]));
  reg_bit_2 reg_bit_2_2 (
    .clk1(clk1), .clk2(clk2), .val(write_data[1]), .load(nor_3_out), .nload(not_1_out), .ic(IC),
    .valout(valout[1]));
  reg_bit_4 reg_bit_4_1 (
    .clk1(clk1), .clk2(clk2), .val(write_data[2]), .load(nor_3_out), .nload(not_1_out), .ic(IC),
    .valout(valout[2]));
  reg_bit_2 reg_bit_2_3 (
    .clk1(clk1), .clk2(clk2), .val(write_data[3]), .load(nor_3_out), .nload(not_1_out), .ic(IC),
    .valout(valout[3]));
  reg_bit_4 reg_bit_4_2 (
    .clk1(clk1), .clk2(clk2), .val(write_data[4]), .load(nor_3_out), .nload(not_1_out), .ic(IC),
    .valout(valout[4]));
  reg_bit_2 reg_bit_2_4 (
    .clk1(clk1), .clk2(clk2), .val(write_data[5]), .load(nor_3_out), .nload(not_1_out), .ic(IC),
    .valout(valout[5]));
  reg_bit_2 reg_bit_2_5 (
    .clk1(clk1), .clk2(clk2), .val(write_data[6]), .load(nor_3_out), .nload(not_1_out), .ic(IC),
    .valout(valout[6]));
  reg_bit_2 reg_bit_2_6 (
    .clk1(clk1), .clk2(clk2), .val(write_data[7]), .load(nor_3_out), .nload(not_1_out), .ic(IC),
    .valout(valout[7]));
endmodule

module reg_test2_2612 (
  input  clk1,
  input  clk2,
  input  [8:0] write_data,
  input  [8:0] write_data_neg,
  input  addr_wr,
  input  data_wr,
  input  IC,
  output [7:0] valout
);

  wire and_1_out, nor_1_out, nor_2_out, nor_3_out, not_1_out, sr_bit_1_nvalout, sr_bit_1_valout;

  nor nor_1 (nor_1_out, write_data[8], write_data[7], write_data[6], write_data_neg[5], write_data[4], write_data_neg[3], write_data_neg[2], write_data[1], write_data[0], addr_wr);
  and and_1 (and_1_out, addr_wr, sr_bit_1_nvalout);
  nor nor_2 (nor_2_out, nor_1_out, and_1_out);
  sr_bit sr_bit_1 (.clk1(clk1), .clk2(clk2), .val(nor_2_out), .nvalout(sr_bit_1_nvalout), .valout(sr_bit_1_valout));
  nor nor_3 (nor_3_out, sr_bit_1_valout, write_data[8], data_wr);
  not not_1 (not_1_out, nor_3_out);
  reg_bit_2 reg_bit_2_1 (
    .clk1(clk1), .clk2(clk2), .val(write_data[3]), .load(nor_3_out), .nload(not_1_out), .ic(IC),
    .valout(valout[3]));
  reg_bit_2 reg_bit_2_2 (
    .clk1(clk1), .clk2(clk2), .val(write_data[4]), .load(nor_3_out), .nload(not_1_out), .ic(IC),
    .valout(valout[4]));
  reg_bit_2 reg_bit_2_3 (
    .clk1(clk1), .clk2(clk2), .val(write_data[5]), .load(nor_3_out), .nload(not_1_out), .ic(IC),
    .valout(valout[5]));
  reg_bit_2 reg_bit_2_4 (
    .clk1(clk1), .clk2(clk2), .val(write_data[6]), .load(nor_3_out), .nload(not_1_out), .ic(IC),
    .valout(valout[6]));
  reg_bit_2 reg_bit_2_5 (
    .clk1(clk1), .clk2(clk2), .val(write_data[7]), .load(nor_3_out), .nload(not_1_out), .ic(IC),
    .valout(valout[7]));
endmodule

module reg_dac_2612 (
  input  clk1,
  input  clk2,
  input  [8:0] write_data,
  input  [8:0] write_data_neg,
  input  addr_wr,
  input  data_wr,
  input  IC,
  output [7:0] valout
);

  wire and_1_out, nor_1_out, nor_2_out, nor_3_out, not_1_out, sr_bit_1_nvalout, sr_bit_1_valout;

  nor nor_1 (nor_1_out, write_data[8], write_data[7], write_data[6], write_data_neg[5], write_data[4], write_data_neg[3], write_data[2], write_data_neg[1], write_data[0], addr_wr);
  and and_1 (and_1_out, addr_wr, sr_bit_1_nvalout);
  nor nor_2 (nor_2_out, nor_1_out, and_1_out);
  sr_bit sr_bit_1 (.clk1(clk1), .clk2(clk2), .val(nor_2_out), .nvalout(sr_bit_1_nvalout), .valout(sr_bit_1_valout));
  nor nor_3 (nor_3_out, sr_bit_1_valout, write_data[8], data_wr);
  not not_1 (not_1_out, nor_3_out);
  reg_bit_2 reg_bit_2_1 (
    .clk1(clk1), .clk2(clk2), .val(write_data[0]), .load(nor_3_out), .nload(not_1_out), .ic(IC),
    .valout(valout[0]));
  reg_bit_2 reg_bit_2_2 (
    .clk1(clk1), .clk2(clk2), .val(write_data[1]), .load(nor_3_out), .nload(not_1_out), .ic(IC),
    .valout(valout[1]));
  reg_bit_2 reg_bit_2_3 (
    .clk1(clk1), .clk2(clk2), .val(write_data[2]), .load(nor_3_out), .nload(not_1_out), .ic(IC),
    .valout(valout[2]));
  reg_bit_2 reg_bit_2_4 (
    .clk1(clk1), .clk2(clk2), .val(write_data[3]), .load(nor_3_out), .nload(not_1_out), .ic(IC),
    .valout(valout[3]));
  reg_bit_2 reg_bit_2_5 (
    .clk1(clk1), .clk2(clk2), .val(write_data[4]), .load(nor_3_out), .nload(not_1_out), .ic(IC),
    .valout(valout[4]));
  reg_bit_2 reg_bit_2_6 (
    .clk1(clk1), .clk2(clk2), .val(write_data[5]), .load(nor_3_out), .nload(not_1_out), .ic(IC),
    .valout(valout[5]));
  reg_bit_3 reg_bit_3_1 (
    .clk1(clk1), .clk2(clk2), .val(write_data[6]), .load(nor_3_out), .nload(not_1_out), .ic(IC),
    .valout(valout[6]));
  reg_bit_5 reg_bit_5_1 (
    .clk1(clk1), .clk2(clk2), .val(write_data[7]), .load(nor_3_out), .nload(not_1_out), .ic(IC),
    .valout(valout[7]));
endmodule

module reg_bit_5 (
  input  clk1,
  input  clk2,
  input  val,
  input  load,
  input  nload,
  input  ic,
  output valout
);

  wire controlled_buffer_1_out, d_ff_1_qn, d_ff_2_qn;

  assign controlled_buffer_1_out = load ? val : 1'bz;  // Controlled_Buffer controlled_buffer_1
  assign controlled_buffer_1_out = nload ? d_ff_2_qn : 1'bz;  // Controlled_Buffer controlled_buffer_2
  D_Flip_Flop #(.trigger("high")) d_ff_1 (
    .D(controlled_buffer_1_out), .clk(clk1), .Qn(d_ff_1_qn));  // open: Q, preset, reset
  and and_1 (valout, d_ff_1_qn, ic);
  D_Flip_Flop #(.trigger("high")) d_ff_2 (.D(valout), .clk(clk2), .Qn(d_ff_2_qn));  // open: Q, preset, reset
endmodule

module reg_dac_en_2612 (
  input  clk1,
  input  clk2,
  input  [8:0] write_data,
  input  [8:0] write_data_neg,
  input  addr_wr,
  input  data_wr,
  input  IC,
  output valout
);

  wire and_1_out, nor_1_out, nor_2_out, nor_3_out, not_1_out, sr_bit_1_nvalout, sr_bit_1_valout;

  nor nor_1 (nor_1_out, write_data[8], write_data[7], write_data[6], write_data_neg[5], write_data[4], write_data_neg[3], write_data[2], write_data_neg[1], write_data_neg[0], addr_wr);
  and and_1 (and_1_out, addr_wr, sr_bit_1_nvalout);
  nor nor_2 (nor_2_out, nor_1_out, and_1_out);
  sr_bit sr_bit_1 (.clk1(clk1), .clk2(clk2), .val(nor_2_out), .nvalout(sr_bit_1_nvalout), .valout(sr_bit_1_valout));
  nor nor_3 (nor_3_out, sr_bit_1_valout, write_data[8], data_wr);
  not not_1 (not_1_out, nor_3_out);
  reg_bit_2 reg_bit_2_1 (
    .clk1(clk1), .clk2(clk2), .val(write_data[7]), .load(nor_3_out), .nload(not_1_out), .ic(IC),
    .valout(valout));
endmodule

module fsm_counter (
  input  clk1,
  input  clk2,
  input  reset,
  output [4:0] cnt
);

  wire cnt_bit_1_cout, cnt_bit_3_cout, cnt_bit_4_cout, d_ff_1_qn, or_1_out;

  or or_1 (or_1_out, reset, d_ff_1_qn);
  cnt_bit cnt_bit_1 (.cin(1'b1), .ic(or_1_out), .clk1(clk1), .clk2(clk2), .cout(cnt_bit_1_cout), .valout(cnt[0]));
  cnt_bit cnt_bit_2 (.cin(cnt_bit_1_cout), .ic(or_1_out), .clk1(clk1), .clk2(clk2), .valout(cnt[1]));  // open: cout
  D_Flip_Flop #(.trigger("high")) d_ff_1 (.D(cnt[1]), .clk(clk2), .Qn(d_ff_1_qn));  // open: Q, preset, reset
  cnt_bit cnt_bit_3 (.cin(d_ff_1_qn), .ic(reset), .clk1(clk1), .clk2(clk2), .cout(cnt_bit_3_cout), .valout(cnt[2]));
  cnt_bit cnt_bit_4 (
    .cin(cnt_bit_3_cout), .ic(reset), .clk1(clk1), .clk2(clk2), .cout(cnt_bit_4_cout), .valout(cnt[3]));
  cnt_bit cnt_bit_5 (.cin(cnt_bit_4_cout), .ic(reset), .clk1(clk1), .clk2(clk2), .valout(cnt[4]));  // open: cout
endmodule
module op_ctrl (
  input  sel1,
  input  sel2,
  input  sel3,
  input  sel4,
  input  [2:0] algorithm,
  input  clk1,
  input  clk2,
  output op1_sel,
  output op2_mod,
  output last_op_2,
  output last_op_1,
  output op2_sel,
  output op1_1,
  output op_output,
  output do_feedback
);

  wire and_1_out, and_2_out, and_3_out, and_4_out, and_5_out, and_6_out, and_7_out, and_8_out, and_9_out,
       and_10_out, d_ff_1_qn, d_ff_2_qn, d_ff_3_qn, d_ff_4_qn, d_ff_5_q, d_ff_5_qn, d_ff_6_q, d_ff_6_qn,
       d_ff_7_q, d_ff_7_qn, d_ff_15_qn, nor_1_out, nor_2_out, nor_3_out, nor_4_out, nor_5_out, nor_6_out,
       nor_7_out, nor_8_out, or_1_out, or_2_out, or_3_out, or_4_out, or_5_out, or_6_out, or_7_out, or_8_out,
       or_9_out, or_10_out, or_11_out;

  D_Flip_Flop #(.trigger("high")) d_ff_1 (.D(sel1), .clk(clk2), .Qn(d_ff_1_qn));  // open: Q, preset, reset
  D_Flip_Flop #(.trigger("high")) d_ff_2 (.D(sel2), .clk(clk2), .Qn(d_ff_2_qn));  // open: Q, preset, reset
  D_Flip_Flop #(.trigger("high")) d_ff_3 (.D(sel3), .clk(clk2), .Qn(d_ff_3_qn));  // open: Q, preset, reset
  D_Flip_Flop #(.trigger("high")) d_ff_4 (.D(sel4), .clk(clk2), .Qn(d_ff_4_qn));  // open: Q, preset, reset
  D_Flip_Flop #(.trigger("high")) d_ff_5 (
    .D(algorithm[0]), .clk(clk2), .Q(d_ff_5_q), .Qn(d_ff_5_qn));  // open: preset, reset
  D_Flip_Flop #(.trigger("high")) d_ff_6 (
    .D(algorithm[1]), .clk(clk2), .Q(d_ff_6_q), .Qn(d_ff_6_qn));  // open: preset, reset
  D_Flip_Flop #(.trigger("high")) d_ff_7 (
    .D(algorithm[2]), .clk(clk2), .Q(d_ff_7_q), .Qn(d_ff_7_qn));  // open: preset, reset
  nor nor_1 (nor_1_out, d_ff_5_qn, d_ff_6_qn, d_ff_7_qn);
  nor nor_2 (nor_2_out, d_ff_5_q, d_ff_6_qn, d_ff_7_qn);
  nor nor_3 (nor_3_out, d_ff_5_qn, d_ff_6_q, d_ff_7_qn);
  nor nor_4 (nor_4_out, d_ff_5_q, d_ff_6_q, d_ff_7_qn);
  nor nor_5 (nor_5_out, d_ff_5_qn, d_ff_6_qn, d_ff_7_q);
  nor nor_6 (nor_6_out, d_ff_5_q, d_ff_6_qn, d_ff_7_q);
  nor nor_7 (nor_7_out, d_ff_5_qn, d_ff_6_q, d_ff_7_q);
  nor nor_8 (nor_8_out, d_ff_5_q, d_ff_6_q, d_ff_7_q);
  or or_1 (or_1_out, nor_1_out, nor_2_out, nor_3_out);
  or or_2 (or_2_out, nor_1_out, nor_2_out, nor_4_out, nor_5_out);
  or or_3 (or_3_out, nor_1_out, nor_4_out, nor_5_out, nor_6_out, nor_7_out);
  or or_4 (or_4_out, nor_2_out, nor_6_out);
  or or_5 (or_5_out, nor_3_out, nor_6_out);
  or or_6 (or_6_out, nor_5_out, nor_6_out, nor_7_out, nor_8_out);
  or or_7 (or_7_out, nor_6_out, nor_7_out, nor_8_out);
  and and_1 (and_1_out, d_ff_1_qn, or_1_out);
  or or_8 (or_8_out, and_1_out, and_2_out);
  and and_2 (and_2_out, d_ff_3_qn, nor_4_out);
  and and_3 (and_3_out, d_ff_3_qn, nor_3_out);
  and and_4 (and_4_out, d_ff_3_qn, or_2_out);
  or or_9 (or_9_out, and_4_out, and_5_out);
  and and_5 (and_5_out, d_ff_4_qn, or_3_out);
  and and_6 (and_6_out, d_ff_1_qn, or_4_out);
  or or_10 (or_10_out, and_6_out, and_7_out, d_ff_2_qn);
  and and_7 (and_7_out, d_ff_3_qn, or_5_out);
  and and_8 (and_8_out, d_ff_2_qn, or_6_out);
  and and_9 (and_9_out, d_ff_3_qn, or_7_out);
  or or_11 (or_11_out, and_8_out, and_9_out, and_10_out, d_ff_1_qn);
  and and_10 (and_10_out, d_ff_4_qn, nor_8_out);
  D_Flip_Flop #(.trigger("high")) d_ff_8 (.D(d_ff_4_qn), .clk(clk1), .Qn(op1_sel));  // open: Q, preset, reset
  D_Flip_Flop #(.trigger("high")) d_ff_9 (.D(or_8_out), .clk(clk1), .Qn(op2_mod));  // open: Q, preset, reset
  D_Flip_Flop #(.trigger("high")) d_ff_10 (.D(and_3_out), .clk(clk1), .Qn(last_op_2));  // open: Q, preset, reset
  D_Flip_Flop #(.trigger("high")) d_ff_11 (.D(or_9_out), .clk(clk1), .Qn(last_op_1));  // open: Q, preset, reset
  D_Flip_Flop #(.trigger("high")) d_ff_12 (.D(d_ff_2_qn), .clk(clk1), .Qn(op2_sel));  // open: Q, preset, reset
  D_Flip_Flop #(.trigger("high")) d_ff_13 (.D(or_10_out), .clk(clk1), .Qn(op1_1));  // open: Q, preset, reset
  D_Flip_Flop #(.trigger("high")) d_ff_14 (.D(or_11_out), .clk(clk1), .Qn(op_output));  // open: Q, preset, reset
  D_Flip_Flop #(.trigger("high")) d_ff_15 (.D(op2_sel), .clk(clk2), .Qn(d_ff_15_qn));  // open: Q, preset, reset
  D_Flip_Flop #(.trigger("high")) d_ff_16 (.D(d_ff_15_qn), .clk(clk1), .Qn(do_feedback));  // open: Q, preset, reset
endmodule

module fsm (
  input  clk1,
  input  clk2,
  input  fsm_reset,
  input  [2:0] algorithm,
  output op1_sel,
  output op2_mod,
  output last_op_2,
  output last_op_1,
  output op2_sel,
  output op1_1,
  output op_output,
  output do_feedback,
  output sync_eg,
  output sync_timers,
  output sync_dbg,
  output sync_accm,
  output sync23,
  output ch3_sel,
  output out_19,
  output out_20,
  output out_21
);

  wire fsm_table_1_sel1, fsm_table_1_sel2, fsm_table_1_sel3, fsm_table_1_sel4;
  wire [4:0] fsm_counter_1_cnt;

  fsm_counter fsm_counter_1 (.clk1(clk1), .clk2(clk2), .reset(fsm_reset), .cnt(fsm_counter_1_cnt));
  fsm_table fsm_table_1 (
    .counter(fsm_counter_1_cnt), .clk1(clk1), .clk2(clk2), .sel1(fsm_table_1_sel1), .sel2(fsm_table_1_sel2),
    .sel3(fsm_table_1_sel3), .sel4(fsm_table_1_sel4), .sync_eg(sync_eg), .sync_timers(sync_timers),
    .sync_dbg(sync_dbg), .sync_accm(sync_accm), .sync23(sync23), .ch3_sel(ch3_sel), .out_14(out_19),
    .out_15(out_20), .out_16(out_21));
  op_ctrl op_ctrl_1 (
    .sel1(fsm_table_1_sel1), .sel2(fsm_table_1_sel2), .sel3(fsm_table_1_sel3), .sel4(fsm_table_1_sel4),
    .algorithm(algorithm), .clk1(clk1), .clk2(clk2), .op1_sel(op1_sel), .op2_mod(op2_mod),
    .last_op_2(last_op_2), .last_op_1(last_op_1), .op2_sel(op2_sel), .op1_1(op1_1), .op_output(op_output),
    .do_feedback(do_feedback));
endmodule

module fsm_table (
  input  [4:0] counter,
  input  clk1,
  input  clk2,
  output sel1,
  output sel2,
  output sel3,
  output sel4,
  output sync_eg,
  output sync_timers,
  output sync_dbg,
  output sync_accm,
  output sync23,
  output ch3_sel,
  output out_14,
  output out_15,
  output out_16
);

  wire d_ff_1_qn, d_ff_2_qn, d_ff_3_qn, d_ff_4_qn, d_ff_5_qn, d_ff_6_qn, d_ff_7_qn, d_ff_8_qn, nor_1_out,
       nor_2_out, nor_3_out, nor_4_out, nor_5_out, nor_6_out, nor_7_out, nor_8_out, nor_9_out, nor_10_out,
       nor_11_out, nor_12_out, nor_13_out, nor_14_out, nor_15_out, nor_16_out, nor_17_out, nor_18_out,
       nor_19_out, nor_20_out, nor_21_out, nor_22_out, nor_23_out, nor_24_out, not_2_out, not_3_out,
       not_4_out, not_5_out, not_6_out, not_7_out;
  wire [4:0] not_1_out;

  assign not_1_out = ~counter;  // NOT_Gate not_1, 5 bits wide
  nor nor_1 (nor_1_out, counter[1], counter[2], counter[3], counter[4]);
  nor nor_2 (nor_2_out, not_1_out[4], not_1_out[3], not_1_out[2]);
  nor nor_3 (nor_3_out, not_1_out[4], not_1_out[3], counter[2], not_1_out[1]);
  nor nor_4 (nor_4_out, counter[4], not_1_out[3], counter[2], counter[1]);
  nor nor_5 (nor_5_out, counter[4], counter[3], not_1_out[2]);
  nor nor_6 (nor_6_out, counter[4], counter[3], counter[2], not_1_out[1]);
  nor nor_7 (nor_7_out, not_1_out[4], counter[3], counter[2]);
  nor nor_8 (nor_8_out, counter[4], not_1_out[3], not_1_out[2], counter[1]);
  nor nor_9 (nor_9_out, counter[4], not_1_out[3], counter[2], not_1_out[1]);
  nor nor_10 (nor_10_out, not_1_out[4], not_1_out[3], counter[2]);
  nor nor_11 (nor_11_out, not_1_out[4], counter[3], not_1_out[2]);
  nor nor_12 (nor_12_out, not_1_out[4], counter[3], counter[2], not_1_out[1]);
  nor nor_13 (nor_13_out, counter[4], counter[3], counter[2], counter[1]);
  nor nor_14 (nor_14_out, not_1_out[4], not_1_out[3], not_1_out[2], not_1_out[1], not_1_out[0]);
  nor nor_15 (nor_15_out, not_1_out[4], not_1_out[3], not_1_out[2], not_1_out[1], counter[0]);
  nor nor_16 (nor_16_out, not_1_out[4], counter[3], counter[2], not_1_out[1], counter[0]);
  nor nor_17 (nor_17_out, counter[4], counter[3], counter[2], not_1_out[1], counter[0]);
  nor nor_18 (nor_18_out, not_1_out[2], not_1_out[1], counter[0]);
  nor nor_19 (nor_19_out, not_1_out[4], not_1_out[3], counter[2]);
  nor nor_20 (nor_20_out, not_1_out[4], counter[3], not_1_out[2], not_1_out[1], not_1_out[0]);
  nor nor_21 (nor_21_out, counter[4], not_1_out[3], counter[2]);
  nor nor_22 (nor_22_out, counter[4], counter[3], not_1_out[2], not_1_out[1], not_1_out[0]);
  not not_2 (not_2_out, nor_13_out);
  not not_3 (not_3_out, nor_14_out);
  not not_4 (not_4_out, nor_15_out);
  not not_5 (not_5_out, nor_16_out);
  not not_6 (not_6_out, nor_17_out);
  not not_7 (not_7_out, nor_18_out);
  nor nor_23 (nor_23_out, nor_19_out, nor_20_out);
  nor nor_24 (nor_24_out, nor_21_out, nor_22_out);
  nor nor_25 (sel1, nor_1_out, nor_2_out, nor_3_out);
  nor nor_26 (sel2, nor_4_out, nor_5_out, nor_6_out);
  nor nor_27 (sel3, nor_7_out, nor_8_out, nor_9_out);
  nor nor_28 (sel4, nor_10_out, nor_11_out, nor_12_out);
  D_Flip_Flop #(.trigger("high")) d_ff_1 (.D(not_2_out), .clk(clk2), .Qn(d_ff_1_qn));  // open: Q, preset, reset
  D_Flip_Flop #(.trigger("high")) d_ff_2 (.D(not_3_out), .clk(clk2), .Qn(d_ff_2_qn));  // open: Q, preset, reset
  D_Flip_Flop #(.trigger("high")) d_ff_3 (.D(not_4_out), .clk(clk2), .Qn(d_ff_3_qn));  // open: Q, preset, reset
  D_Flip_Flop #(.trigger("high")) d_ff_4 (.D(not_5_out), .clk(clk2), .Qn(d_ff_4_qn));  // open: Q, preset, reset
  D_Flip_Flop #(.trigger("high")) d_ff_5 (.D(not_6_out), .clk(clk2), .Qn(d_ff_5_qn));  // open: Q, preset, reset
  D_Flip_Flop #(.trigger("high")) d_ff_6 (.D(not_7_out), .clk(clk2), .Qn(d_ff_6_qn));  // open: Q, preset, reset
  D_Flip_Flop #(.trigger("high")) d_ff_7 (.D(nor_23_out), .clk(clk2), .Qn(d_ff_7_qn));  // open: Q, preset, reset
  D_Flip_Flop #(.trigger("high")) d_ff_8 (.D(nor_24_out), .clk(clk2), .Qn(d_ff_8_qn));  // open: Q, preset, reset
  D_Flip_Flop #(.trigger("high")) d_ff_9 (.D(counter[4]), .clk(clk2), .Qn(out_16));  // open: Q, preset, reset
  D_Flip_Flop #(.trigger("high")) d_ff_10 (.D(d_ff_1_qn), .clk(clk1), .Qn(sync_eg));  // open: Q, preset, reset
  D_Flip_Flop #(.trigger("high")) d_ff_11 (.D(d_ff_2_qn), .clk(clk1), .Qn(sync_timers));  // open: Q, preset, reset
  D_Flip_Flop #(.trigger("high")) d_ff_12 (.D(d_ff_3_qn), .clk(clk1), .Qn(sync_dbg));  // open: Q, preset, reset
  D_Flip_Flop #(.trigger("high")) d_ff_13 (.D(d_ff_4_qn), .clk(clk1), .Qn(sync_accm));  // open: Q, preset, reset
  D_Flip_Flop #(.trigger("high")) d_ff_14 (.D(d_ff_5_qn), .clk(clk1), .Qn(sync23));  // open: Q, preset, reset
  D_Flip_Flop #(.trigger("high")) d_ff_15 (.D(d_ff_6_qn), .clk(clk1), .Qn(ch3_sel));  // open: Q, preset, reset
  D_Flip_Flop #(.trigger("high")) d_ff_16 (.D(d_ff_7_qn), .clk(clk1), .Qn(out_14));  // open: Q, preset, reset
  D_Flip_Flop #(.trigger("high")) d_ff_17 (.D(d_ff_8_qn), .clk(clk1), .Qn(out_15));  // open: Q, preset, reset
endmodule

module fsm_table_2612 (
  input  [4:0] counter,
  input  clk1,
  input  clk2,
  output sel1,
  output sel2,
  output sel3,
  output sel4,
  output sync_eg,
  output sync_timers,
  output sync_dbg,
  output sync23,
  output ch3_sel,
  output dac_ch6_sel,
  output dac_load,
  output dac_out_sel
);

  wire d_ff_1_qn, d_ff_2_qn, d_ff_3_qn, d_ff_4_qn, d_ff_5_qn, d_ff_6_qn, d_ff_7_qn, d_ff_8_qn, nor_1_out,
       nor_2_out, nor_3_out, nor_4_out, nor_5_out, nor_6_out, nor_7_out, nor_8_out, nor_9_out, nor_10_out,
       nor_11_out, nor_12_out, nor_13_out, nor_14_out, nor_15_out, nor_16_out, nor_17_out, nor_18_out,
       nor_19_out, nor_20_out, nor_21_out, nor_22_out, nor_23_out, nor_24_out, nor_25_out, nor_26_out,
       nor_27_out, nor_28_out, nor_29_out, not_2_out, not_3_out, not_4_out, not_5_out, not_6_out;
  wire [4:0] not_1_out;

  assign not_1_out = ~counter;  // NOT_Gate not_1, 5 bits wide
  nor nor_1 (nor_1_out, counter[1], counter[2], counter[3], counter[4]);
  nor nor_2 (nor_2_out, not_1_out[4], not_1_out[3], not_1_out[2]);
  nor nor_3 (nor_3_out, not_1_out[4], not_1_out[3], counter[2], not_1_out[1]);
  nor nor_4 (nor_4_out, counter[4], not_1_out[3], counter[2], counter[1]);
  nor nor_5 (nor_5_out, counter[4], counter[3], not_1_out[2]);
  nor nor_6 (nor_6_out, counter[4], counter[3], counter[2], not_1_out[1]);
  nor nor_7 (nor_7_out, not_1_out[4], counter[3], counter[2]);
  nor nor_8 (nor_8_out, counter[4], not_1_out[3], not_1_out[2], counter[1]);
  nor nor_9 (nor_9_out, counter[4], not_1_out[3], counter[2], not_1_out[1]);
  nor nor_10 (nor_10_out, not_1_out[4], not_1_out[3], counter[2]);
  nor nor_11 (nor_11_out, not_1_out[4], counter[3], not_1_out[2]);
  nor nor_12 (nor_12_out, not_1_out[4], counter[3], counter[2], not_1_out[1]);
  nor nor_13 (nor_13_out, counter[4], counter[3], counter[2], counter[1]);
  nor nor_14 (nor_14_out, not_1_out[4], not_1_out[3], not_1_out[2], not_1_out[1], not_1_out[0]);
  nor nor_15 (nor_15_out, not_1_out[4], not_1_out[3], not_1_out[2], not_1_out[1], counter[0]);
  nor nor_16 (nor_16_out, counter[4], counter[3], counter[2], not_1_out[1], counter[0]);
  nor nor_17 (nor_17_out, not_1_out[2], not_1_out[1], counter[0]);
  nor nor_18 (nor_18_out, not_1_out[4], not_1_out[3], counter[2]);
  nor nor_19 (nor_19_out, not_1_out[4], counter[3], not_1_out[2], not_1_out[1], not_1_out[0]);
  nor nor_20 (nor_20_out, counter[3], counter[2], counter[1], not_1_out[0]);
  nor nor_21 (nor_21_out, not_1_out[3], counter[2], not_1_out[1], not_1_out[0]);
  nor nor_22 (nor_22_out, counter[3], not_1_out[2], not_1_out[1], counter[0]);
  nor nor_23 (nor_23_out, not_1_out[4], counter[3], counter[2], counter[1], not_1_out[0]);
  nor nor_24 (nor_24_out, counter[4], not_1_out[3]);
  nor nor_25 (nor_25_out, counter[4], counter[3], not_1_out[2]);
  nor nor_26 (nor_26_out, counter[4], counter[3], counter[2], not_1_out[1]);
  not not_2 (not_2_out, nor_13_out);
  not not_3 (not_3_out, nor_14_out);
  not not_4 (not_4_out, nor_15_out);
  not not_5 (not_5_out, nor_16_out);
  not not_6 (not_6_out, nor_17_out);
  nor nor_27 (nor_27_out, nor_18_out, nor_19_out);
  nor nor_28 (nor_28_out, nor_20_out, nor_21_out, nor_22_out);
  nor nor_29 (nor_29_out, nor_23_out, nor_24_out, nor_25_out, nor_26_out);
  nor nor_30 (sel1, nor_1_out, nor_2_out, nor_3_out);
  nor nor_31 (sel2, nor_4_out, nor_5_out, nor_6_out);
  nor nor_32 (sel3, nor_7_out, nor_8_out, nor_9_out);
  nor nor_33 (sel4, nor_10_out, nor_11_out, nor_12_out);
  D_Flip_Flop #(.trigger("high")) d_ff_1 (.D(not_2_out), .clk(clk2), .Qn(d_ff_1_qn));  // open: Q, preset, reset
  D_Flip_Flop #(.trigger("high")) d_ff_2 (.D(not_3_out), .clk(clk2), .Qn(d_ff_2_qn));  // open: Q, preset, reset
  D_Flip_Flop #(.trigger("high")) d_ff_3 (.D(not_4_out), .clk(clk2), .Qn(d_ff_3_qn));  // open: Q, preset, reset
  D_Flip_Flop #(.trigger("high")) d_ff_4 (.D(not_5_out), .clk(clk2), .Qn(d_ff_4_qn));  // open: Q, preset, reset
  D_Flip_Flop #(.trigger("high")) d_ff_5 (.D(not_6_out), .clk(clk2), .Qn(d_ff_5_qn));  // open: Q, preset, reset
  D_Flip_Flop #(.trigger("high")) d_ff_6 (.D(nor_27_out), .clk(clk2), .Qn(d_ff_6_qn));  // open: Q, preset, reset
  D_Flip_Flop #(.trigger("high")) d_ff_7 (.D(nor_28_out), .clk(clk2), .Qn(d_ff_7_qn));  // open: Q, preset, reset
  D_Flip_Flop #(.trigger("high")) d_ff_8 (.D(nor_29_out), .clk(clk2), .Qn(d_ff_8_qn));  // open: Q, preset, reset
  D_Flip_Flop #(.trigger("high")) d_ff_9 (.D(d_ff_1_qn), .clk(clk1), .Qn(sync_eg));  // open: Q, preset, reset
  D_Flip_Flop #(.trigger("high")) d_ff_10 (.D(d_ff_2_qn), .clk(clk1), .Qn(sync_timers));  // open: Q, preset, reset
  D_Flip_Flop #(.trigger("high")) d_ff_11 (.D(d_ff_3_qn), .clk(clk1), .Qn(sync_dbg));  // open: Q, preset, reset
  D_Flip_Flop #(.trigger("high")) d_ff_12 (.D(d_ff_4_qn), .clk(clk1), .Qn(sync23));  // open: Q, preset, reset
  D_Flip_Flop #(.trigger("high")) d_ff_13 (.D(d_ff_5_qn), .clk(clk1), .Qn(ch3_sel));  // open: Q, preset, reset
  D_Flip_Flop #(.trigger("high")) d_ff_14 (.D(d_ff_6_qn), .clk(clk1), .Qn(dac_ch6_sel));  // open: Q, preset, reset
  D_Flip_Flop #(.trigger("high")) d_ff_15 (.D(d_ff_7_qn), .clk(clk1), .Qn(dac_load));  // open: Q, preset, reset
  D_Flip_Flop #(.trigger("high")) d_ff_16 (.D(d_ff_8_qn), .clk(clk1), .Qn(dac_out_sel));  // open: Q, preset, reset
endmodule

module fsm_2612 (
  input  clk1,
  input  clk2,
  input  fsm_reset,
  input  [2:0] algorithm,
  output op1_sel,
  output op2_mod,
  output last_op_2,
  output last_op_1,
  output op2_sel,
  output op1_1,
  output op_output,
  output do_feedback,
  output sync_eg,
  output sync_timers,
  output sync_dbg,
  output sync23,
  output ch3_sel,
  output dac_ch6_sel,
  output dac_load,
  output dac_out_sel
);

  wire fsm_table_2612_1_sel1, fsm_table_2612_1_sel2, fsm_table_2612_1_sel3, fsm_table_2612_1_sel4;
  wire [4:0] fsm_counter_1_cnt;

  fsm_counter fsm_counter_1 (.clk1(clk1), .clk2(clk2), .reset(fsm_reset), .cnt(fsm_counter_1_cnt));
  fsm_table_2612 fsm_table_2612_1 (
    .counter(fsm_counter_1_cnt), .clk1(clk1), .clk2(clk2), .sel1(fsm_table_2612_1_sel1),
    .sel2(fsm_table_2612_1_sel2), .sel3(fsm_table_2612_1_sel3), .sel4(fsm_table_2612_1_sel4),
    .sync_eg(sync_eg), .sync_timers(sync_timers), .sync_dbg(sync_dbg), .sync23(sync23), .ch3_sel(ch3_sel),
    .dac_ch6_sel(dac_ch6_sel), .dac_load(dac_load), .dac_out_sel(dac_out_sel));
  op_ctrl op_ctrl_1 (
    .sel1(fsm_table_2612_1_sel1), .sel2(fsm_table_2612_1_sel2), .sel3(fsm_table_2612_1_sel3),
    .sel4(fsm_table_2612_1_sel4), .algorithm(algorithm), .clk1(clk1), .clk2(clk2), .op1_sel(op1_sel),
    .op2_mod(op2_mod), .last_op_2(last_op_2), .last_op_1(last_op_1), .op2_sel(op2_sel), .op1_1(op1_1),
    .op_output(op_output), .do_feedback(do_feedback));
endmodule

module reg_chan (
  input  clk1,
  input  clk2,
  input  [7:0] data,
  input  IC,
  input  writeA0,
  input  writeA8,
  input  writeA4,
  input  writeAC,
  input  writeB0,
  input  writeB4,
  input  sync,
  input  ch3ext,
  input  am,
  output [10:0] fnum,
  output [2:0] blk,
  output [1:0] note,
  output [2:0] algorithm,
  output [2:0] fb,
  output [2:0] pms,
  output [1:0] ams,
  output [1:0] pan
);

  wire cnt_bit_1_cout, cnt_bit_1_valout, cnt_bit_2_valout, cnt_bit_3_cout, cnt_bit_3_valout, cnt_bit_4_cout,
       cnt_bit_4_valout, cnt_bit_5_valout, controlled_buffer_35_out, d_ff_1_qn, d_ff_2_q, d_ff_2_qn,
       d_ff_3_q, d_ff_4_q, d_ff_5_qn, d_ff_6_qn, d_ff_7_q, d_ff_7_qn, d_ff_8_q, d_ff_8_qn, nand_1_out,
       nand_2_out, nor_12_out, nor_13_out, nor_14_out, nor_15_out, nor_16_out, nor_17_out, not_1_out,
       not_2_out, not_3_out, not_4_out, not_5_out, not_6_out, not_7_out, not_8_out, not_20_out, not_21_out,
       not_22_out, not_23_out, not_24_out, not_25_out;
  wire [1:0] bit_extender_1_out, bit_extender_11_out, bit_extender_12_out, controlled_buffer_19_out,
       controlled_buffer_21_out, nor_1_out, nor_11_out, not_18_out, not_19_out, sr_bit_2_1_valout,
       sr_bit_2_2_valout, sr_bit_2_3_valout, sr_bit_2_4_valout, sr_bit_2_5_valout, sr_bit_2_6_valout,
       sr_bit_2_7_valout, sr_bit_2_8_valout, sr_bit_2_9_valout, sr_bit_2_10_valout, sr_bit_2_11_valout,
       sr_bit_2_o_1_valout;
  wire [2:0] bit_extender_4_out, bit_extender_5_out, bit_extender_6_out, bit_extender_7_out,
       bit_extender_8_out, bit_extender_9_out, bit_extender_10_out, controlled_buffer_5_out,
       controlled_buffer_7_out, controlled_buffer_9_out, controlled_buffer_11_out, controlled_buffer_13_out,
       controlled_buffer_15_out, controlled_buffer_17_out, controlled_buffer_25_out,
       controlled_buffer_26_out, freq_reg_1_blk, freq_reg_1_fnum_h, freq_reg_2_blk, freq_reg_2_fnum_h,
       nor_4_out, nor_5_out, nor_6_out, nor_7_out, nor_8_out, nor_9_out, nor_10_out, not_11_out, not_12_out,
       not_13_out, not_14_out, not_15_out, not_16_out, not_17_out, sr_bit_3_1_valout, sr_bit_3_2_valout,
       sr_bit_3_3_valout, sr_bit_3_4_valout, sr_bit_3_5_valout, sr_bit_3_6_valout, sr_bit_3_7_valout,
       sr_bit_3_8_valout, sr_bit_3_9_valout, sr_bit_3_10_valout, sr_bit_3_11_valout, sr_bit_3_12_valout,
       sr_bit_3_13_valout, sr_bit_3_14_valout, sr_bit_3_15_valout, sr_bit_3_16_valout, sr_bit_3_17_valout,
       sr_bit_3_18_valout, sr_bit_3_19_valout, sr_bit_3_20_valout, sr_bit_3_21_valout, sr_bit_3_22_valout,
       sr_bit_3_23_valout, sr_bit_3_24_valout, sr_bit_3_25_valout, sr_bit_3_26_valout, sr_bit_3_27_valout,
       sr_bit_3_28_valout, sr_bit_3_29_valout, sr_bit_3_30_valout, sr_bit_3_31_valout, sr_bit_3_32_valout,
       sr_bit_3_33_valout, sr_bit_3_34_valout, sr_bit_3_35_valout, sr_bit_3_36_valout, sr_bit_3_37_valout,
       sr_bit_3_38_valout, sr_bit_3_39_valout, sr_bit_3_o_1_valout, sr_bit_3_o_2_valout;
  wire [7:0] bit_extender_2_out, bit_extender_3_out, controlled_buffer_1_out, controlled_buffer_3_out,
       controlled_buffer_23_out, nor_2_out, nor_3_out, not_9_out, not_10_out, sr_bit_8_1_valout,
       sr_bit_8_2_valout, sr_bit_8_3_valout, sr_bit_8_4_valout, sr_bit_8_5_valout, sr_bit_8_6_valout,
       sr_bit_8_7_valout, sr_bit_8_8_valout, sr_bit_8_9_valout, sr_bit_8_10_valout, sr_bit_8_11_valout,
       sr_bit_8_12_valout;

  not not_1 (not_1_out, writeA0);
  not not_2 (not_2_out, writeA8);
  not not_3 (not_3_out, writeB0);
  not not_4 (not_4_out, writeB4);
  not not_5 (not_5_out, not_1_out);
  not not_6 (not_6_out, not_2_out);
  not not_7 (not_7_out, not_3_out);
  not not_8 (not_8_out, not_4_out);
  assign controlled_buffer_1_out = not_1_out ? data : 8'bz;  // Controlled_Buffer controlled_buffer_1
  assign controlled_buffer_1_out = not_5_out ? sr_bit_8_11_valout : 8'bz;  // Controlled_Buffer controlled_buffer_2
  assign controlled_buffer_3_out = not_2_out ? data : 8'bz;  // Controlled_Buffer controlled_buffer_3
  assign controlled_buffer_3_out = not_6_out ? sr_bit_8_12_valout : 8'bz;  // Controlled_Buffer controlled_buffer_4
  assign controlled_buffer_5_out = not_1_out ? freq_reg_1_fnum_h : 3'bz;  // Controlled_Buffer controlled_buffer_5
  assign controlled_buffer_5_out = not_5_out ? sr_bit_3_34_valout : 3'bz;  // Controlled_Buffer controlled_buffer_6
  assign controlled_buffer_7_out = not_1_out ? freq_reg_1_blk : 3'bz;  // Controlled_Buffer controlled_buffer_7
  assign controlled_buffer_7_out = not_5_out ? sr_bit_3_35_valout : 3'bz;  // Controlled_Buffer controlled_buffer_8
  assign controlled_buffer_9_out = not_2_out ? freq_reg_2_fnum_h : 3'bz;  // Controlled_Buffer controlled_buffer_9
  assign controlled_buffer_9_out = not_6_out ? sr_bit_3_36_valout : 3'bz;  // Controlled_Buffer controlled_buffer_10
  assign controlled_buffer_11_out = not_2_out ? freq_reg_2_blk : 3'bz;  // Controlled_Buffer controlled_buffer_11
  assign controlled_buffer_11_out = not_6_out ? sr_bit_3_37_valout : 3'bz;  // Controlled_Buffer controlled_buffer_12
  assign controlled_buffer_13_out = not_3_out ? data[2:0] : 3'bz;  // Controlled_Buffer controlled_buffer_13
  assign controlled_buffer_13_out = not_7_out ? sr_bit_3_38_valout : 3'bz;  // Controlled_Buffer controlled_buffer_14
  assign controlled_buffer_15_out = not_3_out ? data[5:3] : 3'bz;  // Controlled_Buffer controlled_buffer_15
  assign controlled_buffer_15_out = not_7_out ? sr_bit_3_39_valout : 3'bz;  // Controlled_Buffer controlled_buffer_16
  assign controlled_buffer_17_out = not_4_out ? data[2:0] : 3'bz;  // Controlled_Buffer controlled_buffer_17
  assign controlled_buffer_17_out = not_8_out ? pms : 3'bz;  // Controlled_Buffer controlled_buffer_18
  assign controlled_buffer_19_out = not_4_out ? data[5:4] : 2'bz;  // Controlled_Buffer controlled_buffer_19
  assign controlled_buffer_19_out = not_8_out ? sr_bit_2_11_valout : 2'bz;  // Controlled_Buffer controlled_buffer_20
  assign controlled_buffer_21_out = not_4_out ? data[7:6] : 2'bz;  // Controlled_Buffer controlled_buffer_21
  assign controlled_buffer_21_out = not_8_out ? sr_bit_2_o_1_valout : 2'bz;  // Controlled_Buffer controlled_buffer_22
  assign bit_extender_1_out = {{1{am}}, am};  // Bit_Extender bit_extender_1
  assign not_9_out = ~controlled_buffer_1_out;  // NOT_Gate not_9, 8 bits wide
  assign bit_extender_2_out = {{7{IC}}, IC};  // Bit_Extender bit_extender_2
  assign not_10_out = ~controlled_buffer_3_out;  // NOT_Gate not_10, 8 bits wide
  assign bit_extender_3_out = {{7{IC}}, IC};  // Bit_Extender bit_extender_3
  assign not_11_out = ~controlled_buffer_5_out;  // NOT_Gate not_11, 3 bits wide
  assign bit_extender_4_out = {{2{IC}}, IC};  // Bit_Extender bit_extender_4
  assign not_12_out = ~controlled_buffer_7_out;  // NOT_Gate not_12, 3 bits wide
  assign bit_extender_5_out = {{2{IC}}, IC};  // Bit_Extender bit_extender_5
  assign not_13_out = ~controlled_buffer_9_out;  // NOT_Gate not_13, 3 bits wide
  assign bit_extender_6_out = {{2{IC}}, IC};  // Bit_Extender bit_extender_6
  assign not_14_out = ~controlled_buffer_11_out;  // NOT_Gate not_14, 3 bits wide
  assign bit_extender_7_out = {{2{IC}}, IC};  // Bit_Extender bit_extender_7
  assign not_15_out = ~controlled_buffer_13_out;  // NOT_Gate not_15, 3 bits wide
  assign bit_extender_8_out = {{2{IC}}, IC};  // Bit_Extender bit_extender_8
  assign not_16_out = ~controlled_buffer_15_out;  // NOT_Gate not_16, 3 bits wide
  assign bit_extender_9_out = {{2{IC}}, IC};  // Bit_Extender bit_extender_9
  assign not_17_out = ~controlled_buffer_17_out;  // NOT_Gate not_17, 3 bits wide
  assign bit_extender_10_out = {{2{IC}}, IC};  // Bit_Extender bit_extender_10
  assign not_18_out = ~controlled_buffer_19_out;  // NOT_Gate not_18, 2 bits wide
  assign bit_extender_11_out = {{1{IC}}, IC};  // Bit_Extender bit_extender_11
  assign nor_1_out = ~(controlled_buffer_21_out | bit_extender_1_out);  // NOR_Gate nor_1, 2 bits wide
  assign nor_2_out = ~(not_9_out | bit_extender_2_out);  // NOR_Gate nor_2, 8 bits wide
  assign nor_3_out = ~(not_10_out | bit_extender_3_out);  // NOR_Gate nor_3, 8 bits wide
  assign nor_4_out = ~(not_11_out | bit_extender_4_out);  // NOR_Gate nor_4, 3 bits wide
  assign nor_5_out = ~(not_12_out | bit_extender_5_out);  // NOR_Gate nor_5, 3 bits wide
  assign nor_6_out = ~(not_13_out | bit_extender_6_out);  // NOR_Gate nor_6, 3 bits wide
  assign nor_7_out = ~(not_14_out | bit_extender_7_out);  // NOR_Gate nor_7, 3 bits wide
  assign nor_8_out = ~(not_15_out | bit_extender_8_out);  // NOR_Gate nor_8, 3 bits wide
  assign nor_9_out = ~(not_16_out | bit_extender_9_out);  // NOR_Gate nor_9, 3 bits wide
  assign nor_10_out = ~(not_17_out | bit_extender_10_out);  // NOR_Gate nor_10, 3 bits wide
  assign nor_11_out = ~(not_18_out | bit_extender_11_out);  // NOR_Gate nor_11, 2 bits wide
  assign not_19_out = ~nor_1_out;  // NOT_Gate not_19, 2 bits wide
  D_Flip_Flop #(.trigger("high")) d_ff_1 (.D(sync), .clk(clk2), .Qn(d_ff_1_qn));  // open: Q, preset, reset
  D_Flip_Flop #(.trigger("high")) d_ff_2 (
    .D(cnt_bit_2_valout), .clk(clk2), .Q(d_ff_2_q), .Qn(d_ff_2_qn));  // open: preset, reset
  D_Flip_Flop #(.trigger("high")) d_ff_3 (.D(ch3ext), .clk(clk2), .Q(d_ff_3_q));  // open: Qn, preset, reset
  nor nor_12 (nor_12_out, d_ff_1_qn, IC);
  nand nand_1 (nand_1_out, nor_12_out, d_ff_2_q);
  sr_bit_8 sr_bit_8_1 (.val(nor_2_out), .clk1(clk1), .clk2(clk2), .valout(sr_bit_8_1_valout));
  sr_bit_8 sr_bit_8_2 (.val(nor_3_out), .clk1(clk1), .clk2(clk2), .valout(sr_bit_8_2_valout));
  freq_reg freq_reg_1 (
    .clk1(clk1), .clk2(clk2), .data(data), .IC(IC), .write(writeA4), .fnum_h(freq_reg_1_fnum_h),
    .blk(freq_reg_1_blk));
  sr_bit_3 sr_bit_3_1 (.val(nor_4_out), .clk1(clk1), .clk2(clk2), .valout(sr_bit_3_1_valout));
  sr_bit_3 sr_bit_3_2 (.val(nor_5_out), .clk1(clk1), .clk2(clk2), .valout(sr_bit_3_2_valout));
  freq_reg freq_reg_2 (
    .clk1(clk1), .clk2(clk2), .data(data), .IC(IC), .write(writeAC), .fnum_h(freq_reg_2_fnum_h),
    .blk(freq_reg_2_blk));
  sr_bit_3 sr_bit_3_3 (.val(nor_6_out), .clk1(clk1), .clk2(clk2), .valout(sr_bit_3_3_valout));
  sr_bit_3 sr_bit_3_4 (.val(nor_7_out), .clk1(clk1), .clk2(clk2), .valout(sr_bit_3_4_valout));
  not not_20 (not_20_out, nor_12_out);
  sr_bit_3 sr_bit_3_5 (.val(nor_8_out), .clk1(clk1), .clk2(clk2), .valout(sr_bit_3_5_valout));
  sr_bit_3_o sr_bit_3_o_1 (.val(nor_9_out), .clk1(clk1), .clk2(clk2), .valout(sr_bit_3_o_1_valout), .out2(fb));
  sr_bit_3 sr_bit_3_6 (.val(nor_10_out), .clk1(clk1), .clk2(clk2), .valout(sr_bit_3_6_valout));
  sr_bit_2 sr_bit_2_1 (.val(nor_11_out), .clk1(clk1), .clk2(clk2), .valout(sr_bit_2_1_valout));
  sr_bit_2 sr_bit_2_2 (.val(not_19_out), .clk1(clk1), .clk2(clk2), .valout(sr_bit_2_2_valout));
  sr_bit_8 sr_bit_8_3 (.val(sr_bit_8_1_valout), .clk1(clk1), .clk2(clk2), .valout(sr_bit_8_3_valout));
  sr_bit_8 sr_bit_8_4 (.val(sr_bit_8_2_valout), .clk1(clk1), .clk2(clk2), .valout(sr_bit_8_4_valout));
  sr_bit_3 sr_bit_3_7 (.val(sr_bit_3_1_valout), .clk1(clk1), .clk2(clk2), .valout(sr_bit_3_7_valout));
  sr_bit_3 sr_bit_3_8 (.val(sr_bit_3_2_valout), .clk1(clk1), .clk2(clk2), .valout(sr_bit_3_8_valout));
  sr_bit_3 sr_bit_3_9 (.val(sr_bit_3_3_valout), .clk1(clk1), .clk2(clk2), .valout(sr_bit_3_9_valout));
  sr_bit_3 sr_bit_3_10 (.val(sr_bit_3_4_valout), .clk1(clk1), .clk2(clk2), .valout(sr_bit_3_10_valout));
  cnt_bit cnt_bit_1 (
    .cin(1'b1), .ic(nand_1_out), .clk1(clk1), .clk2(clk2), .cout(cnt_bit_1_cout), .valout(cnt_bit_1_valout));
  D_Flip_Flop #(.trigger("high")) d_ff_4 (.D(cnt_bit_1_valout), .clk(clk2), .Q(d_ff_4_q));  // open: Qn, preset, reset
  sr_bit_3 sr_bit_3_11 (.val(sr_bit_3_5_valout), .clk1(clk1), .clk2(clk2), .valout(sr_bit_3_11_valout));
  sr_bit_3 sr_bit_3_12 (.val(sr_bit_3_o_1_valout), .clk1(clk1), .clk2(clk2), .valout(sr_bit_3_12_valout));
  sr_bit_3 sr_bit_3_13 (.val(sr_bit_3_6_valout), .clk1(clk1), .clk2(clk2), .valout(sr_bit_3_13_valout));
  sr_bit_2 sr_bit_2_3 (.val(sr_bit_2_1_valout), .clk1(clk1), .clk2(clk2), .valout(sr_bit_2_3_valout));
  sr_bit_2 sr_bit_2_4 (.val(sr_bit_2_2_valout), .clk1(clk1), .clk2(clk2), .valout(sr_bit_2_4_valout));
  sr_bit_8 sr_bit_8_5 (.val(sr_bit_8_3_valout), .clk1(clk1), .clk2(clk2), .valout(sr_bit_8_5_valout));
  sr_bit_8 sr_bit_8_6 (.val(sr_bit_8_4_valout), .clk1(clk1), .clk2(clk2), .valout(sr_bit_8_6_valout));
  sr_bit_3 sr_bit_3_14 (.val(sr_bit_3_7_valout), .clk1(clk1), .clk2(clk2), .valout(sr_bit_3_14_valout));
  sr_bit_3 sr_bit_3_15 (.val(sr_bit_3_8_valout), .clk1(clk1), .clk2(clk2), .valout(sr_bit_3_15_valout));
  sr_bit_3 sr_bit_3_16 (.val(sr_bit_3_9_valout), .clk1(clk1), .clk2(clk2), .valout(sr_bit_3_16_valout));
  sr_bit_3 sr_bit_3_17 (.val(sr_bit_3_10_valout), .clk1(clk1), .clk2(clk2), .valout(sr_bit_3_17_valout));
  cnt_bit cnt_bit_2 (
    .cin(cnt_bit_1_cout), .ic(nand_1_out), .clk1(clk1), .clk2(clk2), .valout(cnt_bit_2_valout));  // open: cout
  sr_bit_3 sr_bit_3_18 (.val(sr_bit_3_11_valout), .clk1(clk1), .clk2(clk2), .valout(sr_bit_3_18_valout));
  sr_bit_3 sr_bit_3_19 (.val(sr_bit_3_12_valout), .clk1(clk1), .clk2(clk2), .valout(sr_bit_3_19_valout));
  sr_bit_3 sr_bit_3_20 (.val(sr_bit_3_13_valout), .clk1(clk1), .clk2(clk2), .valout(sr_bit_3_20_valout));
  sr_bit_2 sr_bit_2_5 (.val(sr_bit_2_3_valout), .clk1(clk1), .clk2(clk2), .valout(sr_bit_2_5_valout));
  sr_bit_2 sr_bit_2_6 (.val(sr_bit_2_4_valout), .clk1(clk1), .clk2(clk2), .valout(sr_bit_2_6_valout));
  D_Flip_Flop #(.trigger("high")) d_ff_5 (.D(cnt_bit_2_valout), .clk(clk2), .Qn(d_ff_5_qn));  // open: Q, preset, reset
  sr_bit_8 sr_bit_8_7 (.val(sr_bit_8_5_valout), .clk1(clk1), .clk2(clk2), .valout(sr_bit_8_7_valout));
  sr_bit_8 sr_bit_8_8 (.val(sr_bit_8_6_valout), .clk1(clk1), .clk2(clk2), .valout(sr_bit_8_8_valout));
  sr_bit_3 sr_bit_3_21 (.val(sr_bit_3_14_valout), .clk1(clk1), .clk2(clk2), .valout(sr_bit_3_21_valout));
  sr_bit_3 sr_bit_3_22 (.val(sr_bit_3_15_valout), .clk1(clk1), .clk2(clk2), .valout(sr_bit_3_22_valout));
  sr_bit_3 sr_bit_3_23 (.val(sr_bit_3_16_valout), .clk1(clk1), .clk2(clk2), .valout(sr_bit_3_23_valout));
  sr_bit_3 sr_bit_3_24 (.val(sr_bit_3_17_valout), .clk1(clk1), .clk2(clk2), .valout(sr_bit_3_24_valout));
  cnt_bit cnt_bit_3 (
    .cin(d_ff_2_qn), .ic(not_20_out), .clk1(clk1), .clk2(clk2), .cout(cnt_bit_3_cout),
    .valout(cnt_bit_3_valout));
  D_Flip_Flop #(.trigger("high")) d_ff_6 (.D(cnt_bit_3_valout), .clk(clk2), .Qn(d_ff_6_qn));  // open: Q, preset, reset
  sr_bit_3 sr_bit_3_25 (.val(sr_bit_3_18_valout), .clk1(clk1), .clk2(clk2), .valout(sr_bit_3_25_valout));
  sr_bit_3 sr_bit_3_26 (.val(sr_bit_3_19_valout), .clk1(clk1), .clk2(clk2), .valout(sr_bit_3_26_valout));
  sr_bit_3 sr_bit_3_27 (.val(sr_bit_3_20_valout), .clk1(clk1), .clk2(clk2), .valout(sr_bit_3_27_valout));
  sr_bit_2 sr_bit_2_7 (.val(sr_bit_2_5_valout), .clk1(clk1), .clk2(clk2), .valout(sr_bit_2_7_valout));
  sr_bit_2 sr_bit_2_8 (.val(sr_bit_2_6_valout), .clk1(clk1), .clk2(clk2), .valout(sr_bit_2_8_valout));
  sr_bit_8 sr_bit_8_9 (.val(sr_bit_8_7_valout), .clk1(clk1), .clk2(clk2), .valout(sr_bit_8_9_valout));
  sr_bit_8 sr_bit_8_10 (.val(sr_bit_8_8_valout), .clk1(clk1), .clk2(clk2), .valout(sr_bit_8_10_valout));
  sr_bit_3 sr_bit_3_28 (.val(sr_bit_3_21_valout), .clk1(clk1), .clk2(clk2), .valout(sr_bit_3_28_valout));
  sr_bit_3 sr_bit_3_29 (.val(sr_bit_3_22_valout), .clk1(clk1), .clk2(clk2), .valout(sr_bit_3_29_valout));
  sr_bit_3 sr_bit_3_30 (.val(sr_bit_3_23_valout), .clk1(clk1), .clk2(clk2), .valout(sr_bit_3_30_valout));
  sr_bit_3 sr_bit_3_31 (.val(sr_bit_3_24_valout), .clk1(clk1), .clk2(clk2), .valout(sr_bit_3_31_valout));
  cnt_bit cnt_bit_4 (
    .cin(cnt_bit_3_cout), .ic(not_20_out), .clk1(clk1), .clk2(clk2), .cout(cnt_bit_4_cout),
    .valout(cnt_bit_4_valout));
  sr_bit_3_o sr_bit_3_o_2 (
    .val(sr_bit_3_25_valout), .clk1(clk1), .clk2(clk2), .valout(sr_bit_3_o_2_valout), .out2(algorithm));
  sr_bit_3 sr_bit_3_32 (.val(sr_bit_3_26_valout), .clk1(clk1), .clk2(clk2), .valout(sr_bit_3_32_valout));
  sr_bit_3 sr_bit_3_33 (.val(sr_bit_3_27_valout), .clk1(clk1), .clk2(clk2), .valout(sr_bit_3_33_valout));
  sr_bit_2 sr_bit_2_9 (.val(sr_bit_2_7_valout), .clk1(clk1), .clk2(clk2), .valout(sr_bit_2_9_valout));
  sr_bit_2 sr_bit_2_10 (.val(sr_bit_2_8_valout), .clk1(clk1), .clk2(clk2), .valout(sr_bit_2_10_valout));
  D_Flip_Flop #(.trigger("high")) d_ff_7 (
    .D(cnt_bit_4_valout), .clk(clk2), .Q(d_ff_7_q), .Qn(d_ff_7_qn));  // open: preset, reset
  sr_bit_8 sr_bit_8_11 (.val(sr_bit_8_9_valout), .clk1(clk1), .clk2(clk2), .valout(sr_bit_8_11_valout));
  sr_bit_8 sr_bit_8_12 (.val(sr_bit_8_10_valout), .clk1(clk1), .clk2(clk2), .valout(sr_bit_8_12_valout));
  sr_bit_3 sr_bit_3_34 (.val(sr_bit_3_28_valout), .clk1(clk1), .clk2(clk2), .valout(sr_bit_3_34_valout));
  sr_bit_3 sr_bit_3_35 (.val(sr_bit_3_29_valout), .clk1(clk1), .clk2(clk2), .valout(sr_bit_3_35_valout));
  sr_bit_3 sr_bit_3_36 (.val(sr_bit_3_30_valout), .clk1(clk1), .clk2(clk2), .valout(sr_bit_3_36_valout));
  sr_bit_3 sr_bit_3_37 (.val(sr_bit_3_31_valout), .clk1(clk1), .clk2(clk2), .valout(sr_bit_3_37_valout));
  sr_bit_3 sr_bit_3_38 (.val(sr_bit_3_o_2_valout), .clk1(clk1), .clk2(clk2), .valout(sr_bit_3_38_valout));
  sr_bit_3 sr_bit_3_39 (.val(sr_bit_3_32_valout), .clk1(clk1), .clk2(clk2), .valout(sr_bit_3_39_valout));
  sr_bit_3 sr_bit_3_40 (.val(sr_bit_3_33_valout), .clk1(clk1), .clk2(clk2), .valout(pms));
  sr_bit_2 sr_bit_2_11 (.val(sr_bit_2_9_valout), .clk1(clk1), .clk2(clk2), .valout(sr_bit_2_11_valout));
  sr_bit_2_o sr_bit_2_o_1 (
    .val(sr_bit_2_10_valout), .clk1(clk1), .clk2(clk2), .valout(sr_bit_2_o_1_valout), .out2(pan));
  assign controlled_buffer_23_out = nor_16_out ? sr_bit_8_9_valout : 8'bz;  // Controlled_Buffer controlled_buffer_23
  assign controlled_buffer_23_out = nor_13_out ? sr_bit_8_10_valout : 8'bz;  // Controlled_Buffer controlled_buffer_24
  assign controlled_buffer_25_out = nor_16_out ? sr_bit_3_28_valout : 3'bz;  // Controlled_Buffer controlled_buffer_25
  assign controlled_buffer_26_out = nor_16_out ? sr_bit_3_29_valout : 3'bz;  // Controlled_Buffer controlled_buffer_26
  assign controlled_buffer_25_out = nor_13_out ? sr_bit_3_30_valout : 3'bz;  // Controlled_Buffer controlled_buffer_27
  assign controlled_buffer_26_out = nor_13_out ? sr_bit_3_31_valout : 3'bz;  // Controlled_Buffer controlled_buffer_28
  cnt_bit cnt_bit_5 (
    .cin(cnt_bit_4_cout), .ic(not_20_out), .clk1(clk1), .clk2(clk2), .valout(cnt_bit_5_valout));  // open: cout
  D_Flip_Flop #(.trigger("high")) d_ff_8 (
    .D(cnt_bit_5_valout), .clk(clk2), .Q(d_ff_8_q), .Qn(d_ff_8_qn));  // open: preset, reset
  assign bit_extender_12_out = {{1{am}}, am};  // Bit_Extender bit_extender_12
  assign controlled_buffer_23_out = nor_14_out ? sr_bit_8_12_valout : 8'bz;  // Controlled_Buffer controlled_buffer_29
  assign controlled_buffer_23_out = nor_15_out ? sr_bit_8_2_valout : 8'bz;  // Controlled_Buffer controlled_buffer_30
  assign controlled_buffer_25_out = nor_14_out ? sr_bit_3_36_valout : 3'bz;  // Controlled_Buffer controlled_buffer_31
  assign controlled_buffer_25_out = nor_15_out ? sr_bit_3_3_valout : 3'bz;  // Controlled_Buffer controlled_buffer_32
  assign controlled_buffer_26_out = nor_14_out ? sr_bit_3_37_valout : 3'bz;  // Controlled_Buffer controlled_buffer_33
  assign controlled_buffer_26_out = nor_15_out ? sr_bit_3_4_valout : 3'bz;  // Controlled_Buffer controlled_buffer_34
  assign ams = sr_bit_2_11_valout & bit_extender_12_out;  // AND_Gate and_1, 2 bits wide
  nor nor_13 (nor_13_out, d_ff_3_q, d_ff_4_q, d_ff_5_qn, d_ff_6_qn, d_ff_7_qn, d_ff_8_q);
  nor nor_14 (nor_14_out, d_ff_3_q, d_ff_4_q, d_ff_5_qn, d_ff_6_qn, d_ff_7_qn, d_ff_8_qn);
  nor nor_15 (nor_15_out, d_ff_3_q, d_ff_4_q, d_ff_5_qn, d_ff_6_qn, d_ff_7_q, d_ff_8_qn);
  nor nor_16 (nor_16_out, nor_13_out, nor_14_out, nor_15_out);
  not not_21 (not_21_out, controlled_buffer_23_out[7]);
  D_Flip_Flop #(.trigger("high")) d_ff_9 (
    .D(controlled_buffer_26_out[0]), .clk(clk1), .Qn(blk[0]));  // open: Q, preset, reset
  D_Flip_Flop #(.trigger("high")) d_ff_10 (
    .D(controlled_buffer_26_out[1]), .clk(clk1), .Qn(blk[1]));  // open: Q, preset, reset
  D_Flip_Flop #(.trigger("high")) d_ff_11 (
    .D(controlled_buffer_26_out[2]), .clk(clk1), .Qn(blk[2]));  // open: Q, preset, reset
  not not_22 (not_22_out, controlled_buffer_25_out[0]);
  not not_23 (not_23_out, controlled_buffer_25_out[1]);
  not not_24 (not_24_out, controlled_buffer_25_out[2]);
  nand nand_2 (nand_2_out, not_21_out, not_22_out, not_23_out);
  nor nor_17 (nor_17_out, not_21_out, not_22_out, not_23_out);
  assign controlled_buffer_35_out = not_24_out ? nor_17_out : 1'bz;  // Controlled_Buffer controlled_buffer_35
  sr_bit_11 sr_bit_11_1 (
    .val({controlled_buffer_25_out, controlled_buffer_23_out}), .clk1(clk1), .clk2(clk2), .valout(fnum));
  assign controlled_buffer_35_out = not_25_out ? nand_2_out : 1'bz;  // Controlled_Buffer controlled_buffer_36
  not not_25 (not_25_out, not_24_out);
  D_Flip_Flop #(.trigger("high")) d_ff_12 (
    .D(controlled_buffer_35_out), .clk(clk2), .Qn(note[0]));  // open: Q, preset, reset
  D_Flip_Flop #(.trigger("high")) d_ff_13 (.D(not_25_out), .clk(clk2), .Qn(note[1]));  // open: Q, preset, reset
endmodule

module sr_bit_8 (
  input  [7:0] val,
  input  clk1,
  input  clk2,
  output [7:0] valout
);

  wire [7:0] register_1_q;

  Register #(.trigger("high")) register_1 (.D(val), .en(clk1), .clk(clk1), .Q(register_1_q));  // open: clr
  Register #(.trigger("high")) register_2 (.D(register_1_q), .en(clk2), .clk(clk2), .Q(valout));  // open: clr
endmodule

module sr_bit_3 (
  input  [2:0] val,
  input  clk1,
  input  clk2,
  output [2:0] valout
);

  wire [2:0] register_1_q;

  Register #(.trigger("high"), .width(3)) register_1 (.D(val), .en(clk1), .clk(clk1), .Q(register_1_q));  // open: clr
  Register #(.trigger("high"), .width(3)) register_2 (
    .D(register_1_q), .en(clk2), .clk(clk2), .Q(valout));  // open: clr
endmodule

module freq_reg (
  input  clk1,
  input  clk2,
  input  [7:0] data,
  input  IC,
  input  write,
  output [2:0] fnum_h,
  output [2:0] blk
);

  wire controlled_buffer_1_out, controlled_buffer_3_out, controlled_buffer_5_out, controlled_buffer_7_out,
       controlled_buffer_9_out, controlled_buffer_11_out, d_ff_1_qn, d_ff_2_q, d_ff_3_q, d_ff_4_q, d_ff_5_q,
       d_ff_6_q, d_ff_7_q, nand_1_out, nand_2_out, nand_3_out, nand_4_out, nand_5_out, nand_6_out, not_1_out,
       not_2_out;

  not not_1 (not_1_out, write);
  D_Flip_Flop #(.trigger("high")) d_ff_1 (.D(IC), .clk(clk1), .Qn(d_ff_1_qn));  // open: Q, preset, reset
  not not_2 (not_2_out, not_1_out);
  assign controlled_buffer_1_out = not_1_out ? data[0] : 1'bz;  // Controlled_Buffer controlled_buffer_1
  assign controlled_buffer_1_out = not_2_out ? fnum_h[0] : 1'bz;  // Controlled_Buffer controlled_buffer_2
  assign controlled_buffer_3_out = not_1_out ? data[1] : 1'bz;  // Controlled_Buffer controlled_buffer_3
  assign controlled_buffer_3_out = not_2_out ? fnum_h[1] : 1'bz;  // Controlled_Buffer controlled_buffer_4
  assign controlled_buffer_5_out = not_1_out ? data[2] : 1'bz;  // Controlled_Buffer controlled_buffer_5
  assign controlled_buffer_5_out = not_2_out ? fnum_h[2] : 1'bz;  // Controlled_Buffer controlled_buffer_6
  assign controlled_buffer_7_out = not_1_out ? data[3] : 1'bz;  // Controlled_Buffer controlled_buffer_7
  assign controlled_buffer_7_out = not_2_out ? blk[0] : 1'bz;  // Controlled_Buffer controlled_buffer_8
  assign controlled_buffer_9_out = not_1_out ? data[4] : 1'bz;  // Controlled_Buffer controlled_buffer_9
  assign controlled_buffer_9_out = not_2_out ? blk[1] : 1'bz;  // Controlled_Buffer controlled_buffer_10
  assign controlled_buffer_11_out = not_1_out ? data[5] : 1'bz;  // Controlled_Buffer controlled_buffer_11
  assign controlled_buffer_11_out = not_2_out ? blk[2] : 1'bz;  // Controlled_Buffer controlled_buffer_12
  D_Flip_Flop #(.trigger("high")) d_ff_2 (
    .D(controlled_buffer_1_out), .clk(clk1), .Q(d_ff_2_q));  // open: Qn, preset, reset
  D_Flip_Flop #(.trigger("high")) d_ff_3 (
    .D(controlled_buffer_3_out), .clk(clk1), .Q(d_ff_3_q));  // open: Qn, preset, reset
  D_Flip_Flop #(.trigger("high")) d_ff_4 (
    .D(controlled_buffer_5_out), .clk(clk1), .Q(d_ff_4_q));  // open: Qn, preset, reset
  D_Flip_Flop #(.trigger("high")) d_ff_5 (
    .D(controlled_buffer_7_out), .clk(clk1), .Q(d_ff_5_q));  // open: Qn, preset, reset
  D_Flip_Flop #(.trigger("high")) d_ff_6 (
    .D(controlled_buffer_9_out), .clk(clk1), .Q(d_ff_6_q));  // open: Qn, preset, reset
  D_Flip_Flop #(.trigger("high")) d_ff_7 (
    .D(controlled_buffer_11_out), .clk(clk1), .Q(d_ff_7_q));  // open: Qn, preset, reset
  D_Flip_Flop #(.trigger("high")) d_ff_8 (.D(nand_1_out), .clk(clk2), .Qn(fnum_h[0]));  // open: Q, preset, reset
  nand nand_1 (nand_1_out, d_ff_2_q, d_ff_1_qn);
  D_Flip_Flop #(.trigger("high")) d_ff_9 (.D(nand_2_out), .clk(clk2), .Qn(fnum_h[1]));  // open: Q, preset, reset
  nand nand_2 (nand_2_out, d_ff_3_q, d_ff_1_qn);
  D_Flip_Flop #(.trigger("high")) d_ff_10 (.D(nand_3_out), .clk(clk2), .Qn(fnum_h[2]));  // open: Q, preset, reset
  nand nand_3 (nand_3_out, d_ff_4_q, d_ff_1_qn);
  D_Flip_Flop #(.trigger("high")) d_ff_11 (.D(nand_4_out), .clk(clk2), .Qn(blk[0]));  // open: Q, preset, reset
  nand nand_4 (nand_4_out, d_ff_5_q, d_ff_1_qn);
  D_Flip_Flop #(.trigger("high")) d_ff_12 (.D(nand_5_out), .clk(clk2), .Qn(blk[1]));  // open: Q, preset, reset
  nand nand_5 (nand_5_out, d_ff_6_q, d_ff_1_qn);
  D_Flip_Flop #(.trigger("high")) d_ff_13 (.D(nand_6_out), .clk(clk2), .Qn(blk[2]));  // open: Q, preset, reset
  nand nand_6 (nand_6_out, d_ff_7_q, d_ff_1_qn);
endmodule

module sr_bit_3_o (
  input  [2:0] val,
  input  clk1,
  input  clk2,
  output [2:0] valout,
  output [2:0] out2
);

  wire [2:0] register_1_q;

  Register #(.trigger("high"), .width(3)) register_1 (.D(val), .en(clk1), .clk(clk1), .Q(register_1_q));  // open: clr
  Register #(.trigger("high"), .width(3)) register_2 (
    .D(register_1_q), .en(clk2), .clk(clk2), .Q(valout));  // open: clr
  assign out2 = ~register_1_q;  // NOT_Gate not_1, 3 bits wide
endmodule

module sr_bit_2 (
  input  [1:0] val,
  input  clk1,
  input  clk2,
  output [1:0] valout
);

  wire [1:0] register_1_q;

  Register #(.trigger("high"), .width(2)) register_1 (.D(val), .en(clk1), .clk(clk1), .Q(register_1_q));  // open: clr
  Register #(.trigger("high"), .width(2)) register_2 (
    .D(register_1_q), .en(clk2), .clk(clk2), .Q(valout));  // open: clr
endmodule

module sr_bit_2_o (
  input  [1:0] val,
  input  clk1,
  input  clk2,
  output [1:0] valout,
  output [1:0] out2
);

  wire [1:0] register_1_q;

  Register #(.trigger("high"), .width(2)) register_1 (.D(val), .en(clk1), .clk(clk1), .Q(register_1_q));  // open: clr
  Register #(.trigger("high"), .width(2)) register_2 (
    .D(register_1_q), .en(clk2), .clk(clk2), .Q(valout));  // open: clr
  assign out2 = ~register_1_q;  // NOT_Gate not_1, 2 bits wide
endmodule

module sr_bit_11 (
  input  [10:0] val,
  input  clk1,
  input  clk2,
  output [10:0] valout
);

  wire [10:0] register_1_q;

  Register #(.trigger("high"), .width(11)) register_1 (.D(val), .en(clk1), .clk(clk1), .Q(register_1_q));  // open: clr
  Register #(.trigger("high"), .width(11)) register_2 (
    .D(register_1_q), .en(clk2), .clk(clk2), .Q(valout));  // open: clr
endmodule
module reg_op (
  input  clk1,
  input  clk2,
  input  [7:0] data,
  input  [1:0] eg_state,
  input  ic,
  input  out_sel,
  input  wr_sel,
  input  write90,
  input  write30,
  input  write40,
  input  write50,
  input  write60,
  input  write70,
  input  write80,
  output ssg_enable,
  output ssg_inv,
  output ssg_b0,
  output ssg_0_or_4,
  output ssg_2_or_6,
  output ssg_3_or_7,
  output ssg_3_or_5,
  output [2:0] detune,
  output [3:0] multi,
  output [6:0] tl,
  output [1:0] ks,
  output [4:0] rate,
  output am,
  output [3:0] sl
);

  wire controlled_buffer_29_out, controlled_buffer_31_out, controlled_buffer_59_out, d_ff_1_q, d_ff_1_qn,
       nor_1_out, nor_2_out, nor_3_out, nor_4_out, nor_5_out, nor_6_out, nor_7_out, nor_8_out, nor_9_out,
       nor_10_out, nor_11_out, nor_12_out, nor_13_out, nor_14_out, nor_29_out, nor_30_out, nor_40_out,
       nor_41_out, nor_42_out, nor_43_out, nor_44_out, not_1_out, not_2_out, not_3_out, not_4_out, not_5_out,
       not_6_out, not_7_out, not_8_out, not_9_out, not_10_out, not_11_out, not_12_out, not_13_out,
       not_14_out, not_15_out, not_16_out, not_17_out, not_18_out, not_19_out, not_20_out, not_21_out,
       not_36_out, not_37_out, not_44_out, not_46_out, not_47_out, not_50_out, sr_bit_1_valout,
       sr_bit_2_valout, sr_bit_3_valout, sr_bit_4_valout, sr_bit_5_valout, sr_bit_6_valout, sr_bit_7_valout,
       sr_bit_8_valout, sr_bit_9_valout, sr_bit_10_valout, sr_bit_11_valout, sr_bit_12_valout,
       sr_bit_13_valout, sr_bit_14_valout, sr_bit_15_valout, sr_bit_16_valout, sr_bit_17_valout,
       sr_bit_18_valout, sr_bit_19_valout, sr_bit_20_valout, sr_bit_21_valout, sr_bit_22_valout,
       sr_bit_23_valout, sr_bit_24_valout;
  wire [0:0] nor_45_out;
  wire [1:0] bit_extender_11_out, bit_extender_12_out, controlled_buffer_21_out, controlled_buffer_23_out,
       controlled_buffer_55_out, nor_25_out, nor_26_out, not_32_out, not_33_out, not_49_out,
       sr_bit_2_1_valout, sr_bit_2_2_valout, sr_bit_2_3_valout, sr_bit_2_4_valout, sr_bit_2_5_valout,
       sr_bit_2_6_valout, sr_bit_2_7_valout, sr_bit_2_8_valout, sr_bit_2_9_valout, sr_bit_2_10_valout,
       sr_bit_2_11_valout, sr_bit_2_12_valout, sr_bit_2_13_valout, sr_bit_2_14_valout, sr_bit_2_15_valout,
       sr_bit_2_16_valout, sr_bit_2_17_valout, sr_bit_2_18_valout, sr_bit_2_19_valout, sr_bit_2_20_valout,
       sr_bit_2_21_valout, sr_bit_2_22_valout, sr_bit_2_23_valout, sr_bit_2_24_valout;
  wire [2:0] bit_extender_3_out, bit_extender_4_out, controlled_buffer_5_out, controlled_buffer_7_out,
       controlled_buffer_47_out, nor_17_out, nor_18_out, not_24_out, not_25_out, sr_bit_3_1_valout,
       sr_bit_3_2_valout, sr_bit_3_3_valout, sr_bit_3_4_valout, sr_bit_3_5_valout, sr_bit_3_6_valout,
       sr_bit_3_7_valout, sr_bit_3_8_valout, sr_bit_3_9_valout, sr_bit_3_10_valout, sr_bit_3_11_valout,
       sr_bit_3_12_valout, sr_bit_3_13_valout, sr_bit_3_14_valout, sr_bit_3_15_valout, sr_bit_3_16_valout,
       sr_bit_3_17_valout, sr_bit_3_18_valout, sr_bit_3_19_valout, sr_bit_3_20_valout, sr_bit_3_21_valout,
       sr_bit_3_22_valout, sr_bit_3_23_valout, sr_bit_3_24_valout;
  wire [3:0] and_1_out, bit_extender_1_out, bit_extender_2_out, bit_extender_5_out, bit_extender_6_out,
       bit_extender_17_out, bit_extender_18_out, bit_extender_19_out, bit_extender_20_out,
       bit_extender_24_out, controlled_buffer_1_out, controlled_buffer_3_out, controlled_buffer_9_out,
       controlled_buffer_11_out, controlled_buffer_37_out, controlled_buffer_39_out,
       controlled_buffer_41_out, controlled_buffer_43_out, controlled_buffer_45_out,
       controlled_buffer_49_out, controlled_buffer_63_out, controlled_buffer_65_out, d_ff_29_q, nor_15_out,
       nor_16_out, nor_19_out, nor_20_out, nor_33_out, nor_34_out, nor_35_out, nor_36_out, not_22_out,
       not_23_out, not_26_out, not_27_out, not_40_out, not_41_out, not_42_out, not_43_out, sr_bit_4_1_valout,
       sr_bit_4_2_valout, sr_bit_4_3_valout, sr_bit_4_4_valout, sr_bit_4_5_valout, sr_bit_4_6_valout,
       sr_bit_4_7_valout, sr_bit_4_8_valout, sr_bit_4_9_valout, sr_bit_4_10_valout, sr_bit_4_11_valout,
       sr_bit_4_12_valout, sr_bit_4_13_valout, sr_bit_4_14_valout, sr_bit_4_15_valout, sr_bit_4_16_valout,
       sr_bit_4_17_valout, sr_bit_4_18_valout, sr_bit_4_19_valout, sr_bit_4_20_valout, sr_bit_4_21_valout,
       sr_bit_4_22_valout, sr_bit_4_23_valout, sr_bit_4_24_valout, sr_bit_4_25_valout, sr_bit_4_26_valout,
       sr_bit_4_27_valout, sr_bit_4_28_valout, sr_bit_4_29_valout, sr_bit_4_30_valout, sr_bit_4_31_valout,
       sr_bit_4_32_valout, sr_bit_4_33_valout, sr_bit_4_34_valout, sr_bit_4_35_valout, sr_bit_4_36_valout,
       sr_bit_4_37_valout, sr_bit_4_38_valout, sr_bit_4_39_valout, sr_bit_4_40_valout, sr_bit_4_41_valout,
       sr_bit_4_42_valout, sr_bit_4_43_valout, sr_bit_4_44_valout, sr_bit_4_45_valout, sr_bit_4_46_valout,
       sr_bit_4_47_valout, sr_bit_4_48_valout, sr_bit_4_49_valout, sr_bit_4_50_valout, sr_bit_4_51_valout,
       sr_bit_4_52_valout, sr_bit_4_53_valout, sr_bit_4_54_valout, sr_bit_4_55_valout, sr_bit_4_56_valout,
       sr_bit_4_57_valout, sr_bit_4_58_valout, sr_bit_4_59_valout, sr_bit_4_60_valout, sr_bit_4_61_valout,
       sr_bit_4_62_valout, sr_bit_4_63_valout, sr_bit_4_64_valout, sr_bit_4_65_valout, sr_bit_4_66_valout,
       sr_bit_4_67_valout, sr_bit_4_68_valout, sr_bit_4_69_valout, sr_bit_4_70_valout, sr_bit_4_71_valout,
       sr_bit_4_72_valout, sr_bit_4_73_valout, sr_bit_4_74_valout, sr_bit_4_75_valout, sr_bit_4_76_valout,
       sr_bit_4_77_valout, sr_bit_4_78_valout, sr_bit_4_79_valout, sr_bit_4_80_valout, sr_bit_4_81_valout,
       sr_bit_4_82_valout, sr_bit_4_83_valout, sr_bit_4_84_valout, sr_bit_4_85_valout, sr_bit_4_86_valout,
       sr_bit_4_87_valout, sr_bit_4_88_valout, sr_bit_4_89_valout, sr_bit_4_90_valout, sr_bit_4_91_valout,
       sr_bit_4_92_valout, sr_bit_4_93_valout, sr_bit_4_94_valout, sr_bit_4_95_valout, sr_bit_4_96_valout,
       sr_bit_4_97_valout;
  wire [4:0] and_2_out, and_3_out, and_4_out, bit_extender_9_out, bit_extender_10_out, bit_extender_13_out,
       bit_extender_14_out, bit_extender_15_out, bit_extender_16_out, bit_extender_21_out,
       bit_extender_22_out, bit_extender_23_out, controlled_buffer_17_out, controlled_buffer_19_out,
       controlled_buffer_25_out, controlled_buffer_27_out, controlled_buffer_33_out,
       controlled_buffer_35_out, controlled_buffer_53_out, controlled_buffer_57_out,
       controlled_buffer_61_out, d_ff_14_q, d_ff_19_q, d_ff_24_q, nor_23_out, nor_24_out, nor_27_out,
       nor_28_out, nor_31_out, nor_32_out, not_30_out, not_31_out, not_34_out, not_35_out, not_38_out,
       not_39_out, sr_bit_5_1_valout, sr_bit_5_2_valout, sr_bit_5_3_valout, sr_bit_5_4_valout,
       sr_bit_5_5_valout, sr_bit_5_6_valout, sr_bit_5_7_valout, sr_bit_5_8_valout, sr_bit_5_9_valout,
       sr_bit_5_10_valout, sr_bit_5_11_valout, sr_bit_5_12_valout, sr_bit_5_13_valout, sr_bit_5_14_valout,
       sr_bit_5_15_valout, sr_bit_5_16_valout, sr_bit_5_17_valout, sr_bit_5_18_valout, sr_bit_5_19_valout,
       sr_bit_5_20_valout, sr_bit_5_21_valout, sr_bit_5_22_valout, sr_bit_5_23_valout, sr_bit_5_24_valout,
       sr_bit_5_25_valout, sr_bit_5_26_valout, sr_bit_5_27_valout, sr_bit_5_28_valout, sr_bit_5_29_valout,
       sr_bit_5_30_valout, sr_bit_5_31_valout, sr_bit_5_32_valout, sr_bit_5_33_valout, sr_bit_5_34_valout,
       sr_bit_5_35_valout, sr_bit_5_36_valout, sr_bit_5_37_valout, sr_bit_5_38_valout, sr_bit_5_39_valout,
       sr_bit_5_40_valout, sr_bit_5_41_valout, sr_bit_5_42_valout, sr_bit_5_43_valout, sr_bit_5_44_valout,
       sr_bit_5_45_valout, sr_bit_5_46_valout, sr_bit_5_47_valout, sr_bit_5_48_valout, sr_bit_5_49_valout,
       sr_bit_5_50_valout, sr_bit_5_51_valout, sr_bit_5_52_valout, sr_bit_5_53_valout, sr_bit_5_54_valout,
       sr_bit_5_55_valout, sr_bit_5_56_valout, sr_bit_5_57_valout, sr_bit_5_58_valout, sr_bit_5_59_valout,
       sr_bit_5_60_valout, sr_bit_5_61_valout, sr_bit_5_62_valout, sr_bit_5_63_valout, sr_bit_5_64_valout,
       sr_bit_5_65_valout, sr_bit_5_66_valout, sr_bit_5_67_valout, sr_bit_5_68_valout, sr_bit_5_69_valout,
       sr_bit_5_70_valout, sr_bit_5_71_valout, sr_bit_5_72_valout;
  wire [6:0] bit_extender_7_out, bit_extender_8_out, controlled_buffer_13_out, controlled_buffer_15_out,
       controlled_buffer_51_out, nor_21_out, nor_22_out, not_28_out, not_29_out, sr_bit_7_1_valout,
       sr_bit_7_2_valout, sr_bit_7_3_valout, sr_bit_7_4_valout, sr_bit_7_5_valout, sr_bit_7_6_valout,
       sr_bit_7_7_valout, sr_bit_7_8_valout, sr_bit_7_9_valout, sr_bit_7_10_valout, sr_bit_7_11_valout,
       sr_bit_7_12_valout, sr_bit_7_13_valout, sr_bit_7_14_valout, sr_bit_7_15_valout, sr_bit_7_16_valout,
       sr_bit_7_17_valout, sr_bit_7_18_valout, sr_bit_7_19_valout, sr_bit_7_20_valout, sr_bit_7_21_valout,
       sr_bit_7_22_valout, sr_bit_7_23_valout, sr_bit_7_24_valout;

  nor nor_1 (nor_1_out, wr_sel, write90);
  nor nor_2 (nor_2_out, write90, not_1_out);
  not not_1 (not_1_out, wr_sel);
  nor nor_3 (nor_3_out, wr_sel, write30);
  nor nor_4 (nor_4_out, write30, not_2_out);
  not not_2 (not_2_out, wr_sel);
  nor nor_5 (nor_5_out, wr_sel, write40);
  nor nor_6 (nor_6_out, write40, not_3_out);
  not not_3 (not_3_out, wr_sel);
  nor nor_7 (nor_7_out, wr_sel, write50);
  nor nor_8 (nor_8_out, write50, not_4_out);
  not not_4 (not_4_out, wr_sel);
  nor nor_9 (nor_9_out, wr_sel, write60);
  nor nor_10 (nor_10_out, write60, not_5_out);
  not not_5 (not_5_out, wr_sel);
  nor nor_11 (nor_11_out, wr_sel, write70);
  nor nor_12 (nor_12_out, write70, not_6_out);
  not not_6 (not_6_out, wr_sel);
  nor nor_13 (nor_13_out, wr_sel, write80);
  nor nor_14 (nor_14_out, write80, not_7_out);
  not not_7 (not_7_out, wr_sel);
  not not_8 (not_8_out, nor_1_out);
  not not_9 (not_9_out, nor_2_out);
  not not_10 (not_10_out, nor_3_out);
  not not_11 (not_11_out, nor_4_out);
  not not_12 (not_12_out, nor_5_out);
  not not_13 (not_13_out, nor_6_out);
  not not_14 (not_14_out, nor_7_out);
  not not_15 (not_15_out, nor_8_out);
  not not_16 (not_16_out, nor_9_out);
  not not_17 (not_17_out, nor_10_out);
  not not_18 (not_18_out, nor_11_out);
  not not_19 (not_19_out, nor_12_out);
  not not_20 (not_20_out, nor_13_out);
  not not_21 (not_21_out, nor_14_out);
  assign controlled_buffer_1_out = nor_1_out ? data[3:0] : 4'bz;  // Controlled_Buffer controlled_buffer_1
  assign controlled_buffer_1_out = not_8_out ? sr_bit_4_89_valout : 4'bz;  // Controlled_Buffer controlled_buffer_2
  assign controlled_buffer_3_out = nor_2_out ? data[3:0] : 4'bz;  // Controlled_Buffer controlled_buffer_3
  assign controlled_buffer_3_out = not_9_out ? sr_bit_4_90_valout : 4'bz;  // Controlled_Buffer controlled_buffer_4
  assign controlled_buffer_5_out = nor_3_out ? data[6:4] : 3'bz;  // Controlled_Buffer controlled_buffer_5
  assign controlled_buffer_5_out = not_10_out ? sr_bit_3_23_valout : 3'bz;  // Controlled_Buffer controlled_buffer_6
  assign controlled_buffer_7_out = nor_4_out ? data[6:4] : 3'bz;  // Controlled_Buffer controlled_buffer_7
  assign controlled_buffer_7_out = not_11_out ? sr_bit_3_24_valout : 3'bz;  // Controlled_Buffer controlled_buffer_8
  assign controlled_buffer_9_out = nor_3_out ? data[3:0] : 4'bz;  // Controlled_Buffer controlled_buffer_9
  assign controlled_buffer_9_out = not_10_out ? sr_bit_4_91_valout : 4'bz;  // Controlled_Buffer controlled_buffer_10
  assign controlled_buffer_11_out = nor_4_out ? data[3:0] : 4'bz;  // Controlled_Buffer controlled_buffer_11
  assign controlled_buffer_11_out = not_11_out ? sr_bit_4_92_valout : 4'bz;  // Controlled_Buffer controlled_buffer_12
  assign controlled_buffer_13_out = nor_5_out ? data[6:0] : 7'bz;  // Controlled_Buffer controlled_buffer_13
  assign controlled_buffer_13_out = not_12_out ? sr_bit_7_23_valout : 7'bz;  // Controlled_Buffer controlled_buffer_14
  assign controlled_buffer_15_out = nor_6_out ? data[6:0] : 7'bz;  // Controlled_Buffer controlled_buffer_15
  assign controlled_buffer_15_out = not_13_out ? sr_bit_7_24_valout : 7'bz;  // Controlled_Buffer controlled_buffer_16
  assign controlled_buffer_17_out = nor_7_out ? data[4:0] : 5'bz;  // Controlled_Buffer controlled_buffer_17
  assign controlled_buffer_17_out = not_14_out ? sr_bit_5_67_valout : 5'bz;  // Controlled_Buffer controlled_buffer_18
  assign controlled_buffer_19_out = nor_8_out ? data[4:0] : 5'bz;  // Controlled_Buffer controlled_buffer_19
  assign controlled_buffer_19_out = not_15_out ? sr_bit_5_68_valout : 5'bz;  // Controlled_Buffer controlled_buffer_20
  assign controlled_buffer_21_out = nor_7_out ? data[7:6] : 2'bz;  // Controlled_Buffer controlled_buffer_21
  assign controlled_buffer_21_out = not_14_out ? sr_bit_2_23_valout : 2'bz;  // Controlled_Buffer controlled_buffer_22
  assign controlled_buffer_23_out = nor_8_out ? data[7:6] : 2'bz;  // Controlled_Buffer controlled_buffer_23
  assign controlled_buffer_23_out = not_15_out ? sr_bit_2_24_valout : 2'bz;  // Controlled_Buffer controlled_buffer_24
  assign controlled_buffer_25_out = nor_9_out ? data[4:0] : 5'bz;  // Controlled_Buffer controlled_buffer_25
  assign controlled_buffer_25_out = not_16_out ? sr_bit_5_69_valout : 5'bz;  // Controlled_Buffer controlled_buffer_26
  assign controlled_buffer_27_out = nor_10_out ? data[4:0] : 5'bz;  // Controlled_Buffer controlled_buffer_27
  assign controlled_buffer_27_out = not_17_out ? sr_bit_5_70_valout : 5'bz;  // Controlled_Buffer controlled_buffer_28
  assign controlled_buffer_29_out = nor_9_out ? data[7] : 1'bz;  // Controlled_Buffer controlled_buffer_29
  assign controlled_buffer_29_out = not_16_out ? sr_bit_23_valout : 1'bz;  // Controlled_Buffer controlled_buffer_30
  assign controlled_buffer_31_out = nor_10_out ? data[7] : 1'bz;  // Controlled_Buffer controlled_buffer_31
  assign controlled_buffer_31_out = not_17_out ? sr_bit_24_valout : 1'bz;  // Controlled_Buffer controlled_buffer_32
  assign controlled_buffer_33_out = nor_11_out ? data[4:0] : 5'bz;  // Controlled_Buffer controlled_buffer_33
  assign controlled_buffer_33_out = not_18_out ? sr_bit_5_71_valout : 5'bz;  // Controlled_Buffer controlled_buffer_34
  assign controlled_buffer_35_out = nor_12_out ? data[4:0] : 5'bz;  // Controlled_Buffer controlled_buffer_35
  assign controlled_buffer_35_out = not_19_out ? sr_bit_5_72_valout : 5'bz;  // Controlled_Buffer controlled_buffer_36
  assign controlled_buffer_37_out = nor_13_out ? data[3:0] : 4'bz;  // Controlled_Buffer controlled_buffer_37
  assign controlled_buffer_37_out = not_20_out ? sr_bit_4_93_valout : 4'bz;  // Controlled_Buffer controlled_buffer_38
  assign controlled_buffer_39_out = nor_14_out ? data[3:0] : 4'bz;  // Controlled_Buffer controlled_buffer_39
  assign controlled_buffer_39_out = not_21_out ? sr_bit_4_94_valout : 4'bz;  // Controlled_Buffer controlled_buffer_40
  assign controlled_buffer_41_out = nor_13_out ? data[7:4] : 4'bz;  // Controlled_Buffer controlled_buffer_41
  assign controlled_buffer_41_out = not_20_out ? sr_bit_4_95_valout : 4'bz;  // Controlled_Buffer controlled_buffer_42
  assign controlled_buffer_43_out = nor_14_out ? data[7:4] : 4'bz;  // Controlled_Buffer controlled_buffer_43
  assign controlled_buffer_43_out = not_21_out ? sr_bit_4_96_valout : 4'bz;  // Controlled_Buffer controlled_buffer_44
  assign not_22_out = ~controlled_buffer_1_out;  // NOT_Gate not_22, 4 bits wide
  assign bit_extender_1_out = {{3{ic}}, ic};  // Bit_Extender bit_extender_1
  assign not_23_out = ~controlled_buffer_3_out;  // NOT_Gate not_23, 4 bits wide
  assign bit_extender_2_out = {{3{ic}}, ic};  // Bit_Extender bit_extender_2
  assign not_24_out = ~controlled_buffer_5_out;  // NOT_Gate not_24, 3 bits wide
  assign bit_extender_3_out = {{2{ic}}, ic};  // Bit_Extender bit_extender_3
  assign not_25_out = ~controlled_buffer_7_out;  // NOT_Gate not_25, 3 bits wide
  assign bit_extender_4_out = {{2{ic}}, ic};  // Bit_Extender bit_extender_4
  assign not_26_out = ~controlled_buffer_9_out;  // NOT_Gate not_26, 4 bits wide
  assign bit_extender_5_out = {{3{ic}}, ic};  // Bit_Extender bit_extender_5
  assign not_27_out = ~controlled_buffer_11_out;  // NOT_Gate not_27, 4 bits wide
  assign bit_extender_6_out = {{3{ic}}, ic};  // Bit_Extender bit_extender_6
  assign not_28_out = ~controlled_buffer_13_out;  // NOT_Gate not_28, 7 bits wide
  Bit_Extender #(.in_width(1), .out_width(7)) bit_extender_7 (.out(bit_extender_7_out));  // open: in
  assign not_29_out = ~controlled_buffer_15_out;  // NOT_Gate not_29, 7 bits wide
  Bit_Extender #(.in_width(1), .out_width(7)) bit_extender_8 (.out(bit_extender_8_out));  // open: in
  assign not_30_out = ~controlled_buffer_17_out;  // NOT_Gate not_30, 5 bits wide
  assign bit_extender_9_out = {{4{ic}}, ic};  // Bit_Extender bit_extender_9
  assign not_31_out = ~controlled_buffer_19_out;  // NOT_Gate not_31, 5 bits wide
  assign bit_extender_10_out = {{4{ic}}, ic};  // Bit_Extender bit_extender_10
  assign not_32_out = ~controlled_buffer_21_out;  // NOT_Gate not_32, 2 bits wide
  assign bit_extender_11_out = {{1{ic}}, ic};  // Bit_Extender bit_extender_11
  assign not_33_out = ~controlled_buffer_23_out;  // NOT_Gate not_33, 2 bits wide
  assign bit_extender_12_out = {{1{ic}}, ic};  // Bit_Extender bit_extender_12
  assign not_34_out = ~controlled_buffer_25_out;  // NOT_Gate not_34, 5 bits wide
  assign bit_extender_13_out = {{4{ic}}, ic};  // Bit_Extender bit_extender_13
  assign not_35_out = ~controlled_buffer_27_out;  // NOT_Gate not_35, 5 bits wide
  assign bit_extender_14_out = {{4{ic}}, ic};  // Bit_Extender bit_extender_14
  not not_36 (not_36_out, controlled_buffer_29_out);
  not not_37 (not_37_out, controlled_buffer_31_out);
  assign not_38_out = ~controlled_buffer_33_out;  // NOT_Gate not_38, 5 bits wide
  assign bit_extender_15_out = {{4{ic}}, ic};  // Bit_Extender bit_extender_15
  assign not_39_out = ~controlled_buffer_35_out;  // NOT_Gate not_39, 5 bits wide
  assign bit_extender_16_out = {{4{ic}}, ic};  // Bit_Extender bit_extender_16
  assign not_40_out = ~controlled_buffer_37_out;  // NOT_Gate not_40, 4 bits wide
  assign bit_extender_17_out = {{3{ic}}, ic};  // Bit_Extender bit_extender_17
  assign not_41_out = ~controlled_buffer_39_out;  // NOT_Gate not_41, 4 bits wide
  assign bit_extender_18_out = {{3{ic}}, ic};  // Bit_Extender bit_extender_18
  assign not_42_out = ~controlled_buffer_41_out;  // NOT_Gate not_42, 4 bits wide
  assign bit_extender_19_out = {{3{ic}}, ic};  // Bit_Extender bit_extender_19
  assign not_43_out = ~controlled_buffer_43_out;  // NOT_Gate not_43, 4 bits wide
  assign bit_extender_20_out = {{3{ic}}, ic};  // Bit_Extender bit_extender_20
  assign nor_15_out = ~(not_22_out | bit_extender_1_out);  // NOR_Gate nor_15, 4 bits wide
  assign nor_16_out = ~(not_23_out | bit_extender_2_out);  // NOR_Gate nor_16, 4 bits wide
  assign nor_17_out = ~(not_24_out | bit_extender_3_out);  // NOR_Gate nor_17, 3 bits wide
  assign nor_18_out = ~(not_25_out | bit_extender_4_out);  // NOR_Gate nor_18, 3 bits wide
  assign nor_19_out = ~(not_26_out | bit_extender_5_out);  // NOR_Gate nor_19, 4 bits wide
  assign nor_20_out = ~(not_27_out | bit_extender_6_out);  // NOR_Gate nor_20, 4 bits wide
  assign nor_21_out = ~(not_28_out | bit_extender_7_out);  // NOR_Gate nor_21, 7 bits wide
  assign nor_22_out = ~(not_29_out | bit_extender_8_out);  // NOR_Gate nor_22, 7 bits wide
  assign nor_23_out = ~(not_30_out | bit_extender_9_out);  // NOR_Gate nor_23, 5 bits wide
  assign nor_24_out = ~(not_31_out | bit_extender_10_out);  // NOR_Gate nor_24, 5 bits wide
  assign nor_25_out = ~(not_32_out | bit_extender_11_out);  // NOR_Gate nor_25, 2 bits wide
  assign nor_26_out = ~(not_33_out | bit_extender_12_out);  // NOR_Gate nor_26, 2 bits wide
  assign nor_27_out = ~(not_34_out | bit_extender_13_out);  // NOR_Gate nor_27, 5 bits wide
  assign nor_28_out = ~(not_35_out | bit_extender_14_out);  // NOR_Gate nor_28, 5 bits wide
  nor nor_29 (nor_29_out, not_36_out, ic);
  nor nor_30 (nor_30_out, not_37_out, ic);
  assign nor_31_out = ~(not_38_out | bit_extender_15_out);  // NOR_Gate nor_31, 5 bits wide
  assign nor_32_out = ~(not_39_out | bit_extender_16_out);  // NOR_Gate nor_32, 5 bits wide
  assign nor_33_out = ~(not_40_out | bit_extender_17_out);  // NOR_Gate nor_33, 4 bits wide
  assign nor_34_out = ~(not_41_out | bit_extender_18_out);  // NOR_Gate nor_34, 4 bits wide
  assign nor_35_out = ~(not_42_out | bit_extender_19_out);  // NOR_Gate nor_35, 4 bits wide
  assign nor_36_out = ~(not_43_out | bit_extender_20_out);  // NOR_Gate nor_36, 4 bits wide
  D_Flip_Flop #(.trigger("high")) d_ff_1 (
    .D(out_sel), .clk(clk2), .Q(d_ff_1_q), .Qn(d_ff_1_qn));  // open: preset, reset
  sr_bit_4 sr_bit_4_1 (.val(nor_15_out), .clk1(clk1), .clk2(clk2), .valout(sr_bit_4_1_valout));
  sr_bit_4 sr_bit_4_2 (.val(nor_16_out), .clk1(clk1), .clk2(clk2), .valout(sr_bit_4_2_valout));
  sr_bit_3 sr_bit_3_1 (.val(nor_17_out), .clk1(clk1), .clk2(clk2), .valout(sr_bit_3_1_valout));
  sr_bit_3 sr_bit_3_2 (.val(nor_18_out), .clk1(clk1), .clk2(clk2), .valout(sr_bit_3_2_valout));
  sr_bit_4 sr_bit_4_3 (.val(nor_19_out), .clk1(clk1), .clk2(clk2), .valout(sr_bit_4_3_valout));
  sr_bit_4 sr_bit_4_4 (.val(nor_20_out), .clk1(clk1), .clk2(clk2), .valout(sr_bit_4_4_valout));
  sr_bit_7 sr_bit_7_1 (.val(nor_21_out), .clk1(clk1), .clk2(clk2), .valout(sr_bit_7_1_valout));
  sr_bit_7 sr_bit_7_2 (.val(nor_22_out), .clk1(clk1), .clk2(clk2), .valout(sr_bit_7_2_valout));
  sr_bit_5 sr_bit_5_1 (.val(nor_23_out), .clk1(clk1), .clk2(clk2), .valout(sr_bit_5_1_valout));
  sr_bit_5 sr_bit_5_2 (.val(nor_24_out), .clk1(clk1), .clk2(clk2), .valout(sr_bit_5_2_valout));
  sr_bit_2 sr_bit_2_1 (.val(nor_25_out), .clk1(clk1), .clk2(clk2), .valout(sr_bit_2_1_valout));
  sr_bit_2 sr_bit_2_2 (.val(nor_26_out), .clk1(clk1), .clk2(clk2), .valout(sr_bit_2_2_valout));
  sr_bit_5 sr_bit_5_3 (.val(nor_27_out), .clk1(clk1), .clk2(clk2), .valout(sr_bit_5_3_valout));
  sr_bit_5 sr_bit_5_4 (.val(nor_28_out), .clk1(clk1), .clk2(clk2), .valout(sr_bit_5_4_valout));
  sr_bit sr_bit_1 (.clk1(clk1), .clk2(clk2), .val(nor_29_out), .valout(sr_bit_1_valout));  // open: nvalout
  sr_bit sr_bit_2 (.clk1(clk1), .clk2(clk2), .val(nor_30_out), .valout(sr_bit_2_valout));  // open: nvalout
  sr_bit_5 sr_bit_5_5 (.val(nor_31_out), .clk1(clk1), .clk2(clk2), .valout(sr_bit_5_5_valout));
  sr_bit_5 sr_bit_5_6 (.val(nor_32_out), .clk1(clk1), .clk2(clk2), .valout(sr_bit_5_6_valout));
  sr_bit_4 sr_bit_4_5 (.val(nor_33_out), .clk1(clk1), .clk2(clk2), .valout(sr_bit_4_5_valout));
  sr_bit_4 sr_bit_4_6 (.val(nor_34_out), .clk1(clk1), .clk2(clk2), .valout(sr_bit_4_6_valout));
  sr_bit_4 sr_bit_4_7 (.val(nor_35_out), .clk1(clk1), .clk2(clk2), .valout(sr_bit_4_7_valout));
  sr_bit_4 sr_bit_4_8 (.val(nor_36_out), .clk1(clk1), .clk2(clk2), .valout(sr_bit_4_8_valout));
  sr_bit_4 sr_bit_4_9 (.val(sr_bit_4_1_valout), .clk1(clk1), .clk2(clk2), .valout(sr_bit_4_9_valout));
  sr_bit_4 sr_bit_4_10 (.val(sr_bit_4_2_valout), .clk1(clk1), .clk2(clk2), .valout(sr_bit_4_10_valout));
  sr_bit_3 sr_bit_3_3 (.val(sr_bit_3_1_valout), .clk1(clk1), .clk2(clk2), .valout(sr_bit_3_3_valout));
  sr_bit_3 sr_bit_3_4 (.val(sr_bit_3_2_valout), .clk1(clk1), .clk2(clk2), .valout(sr_bit_3_4_valout));
  sr_bit_4 sr_bit_4_11 (.val(sr_bit_4_3_valout), .clk1(clk1), .clk2(clk2), .valout(sr_bit_4_11_valout));
  sr_bit_4 sr_bit_4_12 (.val(sr_bit_4_4_valout), .clk1(clk1), .clk2(clk2), .valout(sr_bit_4_12_valout));
  sr_bit_7 sr_bit_7_3 (.val(sr_bit_7_1_valout), .clk1(clk1), .clk2(clk2), .valout(sr_bit_7_3_valout));
  sr_bit_7 sr_bit_7_4 (.val(sr_bit_7_2_valout), .clk1(clk1), .clk2(clk2), .valout(sr_bit_7_4_valout));
  sr_bit_5 sr_bit_5_7 (.val(sr_bit_5_1_valout), .clk1(clk1), .clk2(clk2), .valout(sr_bit_5_7_valout));
  sr_bit_5 sr_bit_5_8 (.val(sr_bit_5_2_valout), .clk1(clk1), .clk2(clk2), .valout(sr_bit_5_8_valout));
  sr_bit_2 sr_bit_2_3 (.val(sr_bit_2_1_valout), .clk1(clk1), .clk2(clk2), .valout(sr_bit_2_3_valout));
  sr_bit_2 sr_bit_2_4 (.val(sr_bit_2_2_valout), .clk1(clk1), .clk2(clk2), .valout(sr_bit_2_4_valout));
  sr_bit_5 sr_bit_5_9 (.val(sr_bit_5_3_valout), .clk1(clk1), .clk2(clk2), .valout(sr_bit_5_9_valout));
  sr_bit_5 sr_bit_5_10 (.val(sr_bit_5_4_valout), .clk1(clk1), .clk2(clk2), .valout(sr_bit_5_10_valout));
  sr_bit sr_bit_3 (.clk1(clk1), .clk2(clk2), .val(sr_bit_1_valout), .valout(sr_bit_3_valout));  // open: nvalout
  sr_bit sr_bit_4 (.clk1(clk1), .clk2(clk2), .val(sr_bit_2_valout), .valout(sr_bit_4_valout));  // open: nvalout
  sr_bit_5 sr_bit_5_11 (.val(sr_bit_5_5_valout), .clk1(clk1), .clk2(clk2), .valout(sr_bit_5_11_valout));
  sr_bit_5 sr_bit_5_12 (.val(sr_bit_5_6_valout), .clk1(clk1), .clk2(clk2), .valout(sr_bit_5_12_valout));
  sr_bit_4 sr_bit_4_13 (.val(sr_bit_4_5_valout), .clk1(clk1), .clk2(clk2), .valout(sr_bit_4_13_valout));
  sr_bit_4 sr_bit_4_14 (.val(sr_bit_4_6_valout), .clk1(clk1), .clk2(clk2), .valout(sr_bit_4_14_valout));
  sr_bit_4 sr_bit_4_15 (.val(sr_bit_4_7_valout), .clk1(clk1), .clk2(clk2), .valout(sr_bit_4_15_valout));
  sr_bit_4 sr_bit_4_16 (.val(sr_bit_4_8_valout), .clk1(clk1), .clk2(clk2), .valout(sr_bit_4_16_valout));
  sr_bit_4 sr_bit_4_17 (.val(sr_bit_4_9_valout), .clk1(clk1), .clk2(clk2), .valout(sr_bit_4_17_valout));
  sr_bit_4 sr_bit_4_18 (.val(sr_bit_4_10_valout), .clk1(clk1), .clk2(clk2), .valout(sr_bit_4_18_valout));
  sr_bit_3 sr_bit_3_5 (.val(sr_bit_3_3_valout), .clk1(clk1), .clk2(clk2), .valout(sr_bit_3_5_valout));
  sr_bit_3 sr_bit_3_6 (.val(sr_bit_3_4_valout), .clk1(clk1), .clk2(clk2), .valout(sr_bit_3_6_valout));
  sr_bit_4 sr_bit_4_19 (.val(sr_bit_4_11_valout), .clk1(clk1), .clk2(clk2), .valout(sr_bit_4_19_valout));
  sr_bit_4 sr_bit_4_20 (.val(sr_bit_4_12_valout), .clk1(clk1), .clk2(clk2), .valout(sr_bit_4_20_valout));
  sr_bit_7 sr_bit_7_5 (.val(sr_bit_7_3_valout), .clk1(clk1), .clk2(clk2), .valout(sr_bit_7_5_valout));
  sr_bit_7 sr_bit_7_6 (.val(sr_bit_7_4_valout), .clk1(clk1), .clk2(clk2), .valout(sr_bit_7_6_valout));
  sr_bit_5 sr_bit_5_13 (.val(sr_bit_5_7_valout), .clk1(clk1), .clk2(clk2), .valout(sr_bit_5_13_valout));
  sr_bit_5 sr_bit_5_14 (.val(sr_bit_5_8_valout), .clk1(clk1), .clk2(clk2), .valout(sr_bit_5_14_valout));
  sr_bit_2 sr_bit_2_5 (.val(sr_bit_2_3_valout), .clk1(clk1), .clk2(clk2), .valout(sr_bit_2_5_valout));
  sr_bit_2 sr_bit_2_6 (.val(sr_bit_2_4_valout), .clk1(clk1), .clk2(clk2), .valout(sr_bit_2_6_valout));
  sr_bit_5 sr_bit_5_15 (.val(sr_bit_5_9_valout), .clk1(clk1), .clk2(clk2), .valout(sr_bit_5_15_valout));
  sr_bit_5 sr_bit_5_16 (.val(sr_bit_5_10_valout), .clk1(clk1), .clk2(clk2), .valout(sr_bit_5_16_valout));
  sr_bit sr_bit_5 (.clk1(clk1), .clk2(clk2), .val(sr_bit_3_valout), .valout(sr_bit_5_valout));  // open: nvalout
  sr_bit sr_bit_6 (.clk1(clk1), .clk2(clk2), .val(sr_bit_4_valout), .valout(sr_bit_6_valout));  // open: nvalout
  sr_bit_5 sr_bit_5_17 (.val(sr_bit_5_11_valout), .clk1(clk1), .clk2(clk2), .valout(sr_bit_5_17_valout));
  sr_bit_5 sr_bit_5_18 (.val(sr_bit_5_12_valout), .clk1(clk1), .clk2(clk2), .valout(sr_bit_5_18_valout));
  sr_bit_4 sr_bit_4_21 (.val(sr_bit_4_13_valout), .clk1(clk1), .clk2(clk2), .valout(sr_bit_4_21_valout));
  sr_bit_4 sr_bit_4_22 (.val(sr_bit_4_14_valout), .clk1(clk1), .clk2(clk2), .valout(sr_bit_4_22_valout));
  sr_bit_4 sr_bit_4_23 (.val(sr_bit_4_15_valout), .clk1(clk1), .clk2(clk2), .valout(sr_bit_4_23_valout));
  sr_bit_4 sr_bit_4_24 (.val(sr_bit_4_16_valout), .clk1(clk1), .clk2(clk2), .valout(sr_bit_4_24_valout));
  sr_bit_4 sr_bit_4_25 (.val(sr_bit_4_17_valout), .clk1(clk1), .clk2(clk2), .valout(sr_bit_4_25_valout));
  sr_bit_4 sr_bit_4_26 (.val(sr_bit_4_18_valout), .clk1(clk1), .clk2(clk2), .valout(sr_bit_4_26_valout));
  sr_bit_3 sr_bit_3_7 (.val(sr_bit_3_5_valout), .clk1(clk1), .clk2(clk2), .valout(sr_bit_3_7_valout));
  sr_bit_3 sr_bit_3_8 (.val(sr_bit_3_6_valout), .clk1(clk1), .clk2(clk2), .valout(sr_bit_3_8_valout));
  sr_bit_4 sr_bit_4_27 (.val(sr_bit_4_19_valout), .clk1(clk1), .clk2(clk2), .valout(sr_bit_4_27_valout));
  sr_bit_4 sr_bit_4_28 (.val(sr_bit_4_20_valout), .clk1(clk1), .clk2(clk2), .valout(sr_bit_4_28_valout));
  sr_bit_7 sr_bit_7_7 (.val(sr_bit_7_5_valout), .clk1(clk1), .clk2(clk2), .valout(sr_bit_7_7_valout));
  sr_bit_7 sr_bit_7_8 (.val(sr_bit_7_6_valout), .clk1(clk1), .clk2(clk2), .valout(sr_bit_7_8_valout));
  sr_bit_5 sr_bit_5_19 (.val(sr_bit_5_13_valout), .clk1(clk1), .clk2(clk2), .valout(sr_bit_5_19_valout));
  sr_bit_5 sr_bit_5_20 (.val(sr_bit_5_14_valout), .clk1(clk1), .clk2(clk2), .valout(sr_bit_5_20_valout));
  sr_bit_2 sr_bit_2_7 (.val(sr_bit_2_5_valout), .clk1(clk1), .clk2(clk2), .valout(sr_bit_2_7_valout));
  sr_bit_2 sr_bit_2_8 (.val(sr_bit_2_6_valout), .clk1(clk1), .clk2(clk2), .valout(sr_bit_2_8_valout));
  sr_bit_5 sr_bit_5_21 (.val(sr_bit_5_15_valout), .clk1(clk1), .clk2(clk2), .valout(sr_bit_5_21_valout));
  sr_bit_5 sr_bit_5_22 (.val(sr_bit_5_16_valout), .clk1(clk1), .clk2(clk2), .valout(sr_bit_5_22_valout));
  sr_bit sr_bit_7 (.clk1(clk1), .clk2(clk2), .val(sr_bit_5_valout), .valout(sr_bit_7_valout));  // open: nvalout
  sr_bit sr_bit_8 (.clk1(clk1), .clk2(clk2), .val(sr_bit_6_valout), .valout(sr_bit_8_valout));  // open: nvalout
  sr_bit_5 sr_bit_5_23 (.val(sr_bit_5_17_valout), .clk1(clk1), .clk2(clk2), .valout(sr_bit_5_23_valout));
  sr_bit_5 sr_bit_5_24 (.val(sr_bit_5_18_valout), .clk1(clk1), .clk2(clk2), .valout(sr_bit_5_24_valout));
  sr_bit_4 sr_bit_4_29 (.val(sr_bit_4_21_valout), .clk1(clk1), .clk2(clk2), .valout(sr_bit_4_29_valout));
  sr_bit_4 sr_bit_4_30 (.val(sr_bit_4_22_valout), .clk1(clk1), .clk2(clk2), .valout(sr_bit_4_30_valout));
  sr_bit_4 sr_bit_4_31 (.val(sr_bit_4_23_valout), .clk1(clk1), .clk2(clk2), .valout(sr_bit_4_31_valout));
  sr_bit_4 sr_bit_4_32 (.val(sr_bit_4_24_valout), .clk1(clk1), .clk2(clk2), .valout(sr_bit_4_32_valout));
  sr_bit_4 sr_bit_4_33 (.val(sr_bit_4_25_valout), .clk1(clk1), .clk2(clk2), .valout(sr_bit_4_33_valout));
  sr_bit_4 sr_bit_4_34 (.val(sr_bit_4_26_valout), .clk1(clk1), .clk2(clk2), .valout(sr_bit_4_34_valout));
  sr_bit_3 sr_bit_3_9 (.val(sr_bit_3_7_valout), .clk1(clk1), .clk2(clk2), .valout(sr_bit_3_9_valout));
  sr_bit_3 sr_bit_3_10 (.val(sr_bit_3_8_valout), .clk1(clk1), .clk2(clk2), .valout(sr_bit_3_10_valout));
  sr_bit_4 sr_bit_4_35 (.val(sr_bit_4_27_valout), .clk1(clk1), .clk2(clk2), .valout(sr_bit_4_35_valout));
  sr_bit_4 sr_bit_4_36 (.val(sr_bit_4_28_valout), .clk1(clk1), .clk2(clk2), .valout(sr_bit_4_36_valout));
  sr_bit_7 sr_bit_7_9 (.val(sr_bit_7_7_valout), .clk1(clk1), .clk2(clk2), .valout(sr_bit_7_9_valout));
  sr_bit_7 sr_bit_7_10 (.val(sr_bit_7_8_valout), .clk1(clk1), .clk2(clk2), .valout(sr_bit_7_10_valout));
  sr_bit_5 sr_bit_5_25 (.val(sr_bit_5_19_valout), .clk1(clk1), .clk2(clk2), .valout(sr_bit_5_25_valout));
  sr_bit_5 sr_bit_5_26 (.val(sr_bit_5_20_valout), .clk1(clk1), .clk2(clk2), .valout(sr_bit_5_26_valout));
  sr_bit_2 sr_bit_2_9 (.val(sr_bit_2_7_valout), .clk1(clk1), .clk2(clk2), .valout(sr_bit_2_9_valout));
  sr_bit_2 sr_bit_2_10 (.val(sr_bit_2_8_valout), .clk1(clk1), .clk2(clk2), .valout(sr_bit_2_10_valout));
  sr_bit_5 sr_bit_5_27 (.val(sr_bit_5_21_valout), .clk1(clk1), .clk2(clk2), .valout(sr_bit_5_27_valout));
  sr_bit_5 sr_bit_5_28 (.val(sr_bit_5_22_valout), .clk1(clk1), .clk2(clk2), .valout(sr_bit_5_28_valout));
  sr_bit sr_bit_9 (.clk1(clk1), .clk2(clk2), .val(sr_bit_7_valout), .valout(sr_bit_9_valout));  // open: nvalout
  sr_bit sr_bit_10 (.clk1(clk1), .clk2(clk2), .val(sr_bit_8_valout), .valout(sr_bit_10_valout));  // open: nvalout
  sr_bit_5 sr_bit_5_29 (.val(sr_bit_5_23_valout), .clk1(clk1), .clk2(clk2), .valout(sr_bit_5_29_valout));
  sr_bit_5 sr_bit_5_30 (.val(sr_bit_5_24_valout), .clk1(clk1), .clk2(clk2), .valout(sr_bit_5_30_valout));
  sr_bit_4 sr_bit_4_37 (.val(sr_bit_4_29_valout), .clk1(clk1), .clk2(clk2), .valout(sr_bit_4_37_valout));
  sr_bit_4 sr_bit_4_38 (.val(sr_bit_4_30_valout), .clk1(clk1), .clk2(clk2), .valout(sr_bit_4_38_valout));
  sr_bit_4 sr_bit_4_39 (.val(sr_bit_4_31_valout), .clk1(clk1), .clk2(clk2), .valout(sr_bit_4_39_valout));
  sr_bit_4 sr_bit_4_40 (.val(sr_bit_4_32_valout), .clk1(clk1), .clk2(clk2), .valout(sr_bit_4_40_valout));
  sr_bit_4 sr_bit_4_41 (.val(sr_bit_4_33_valout), .clk1(clk1), .clk2(clk2), .valout(sr_bit_4_41_valout));
  sr_bit_4 sr_bit_4_42 (.val(sr_bit_4_34_valout), .clk1(clk1), .clk2(clk2), .valout(sr_bit_4_42_valout));
  sr_bit_3 sr_bit_3_11 (.val(sr_bit_3_9_valout), .clk1(clk1), .clk2(clk2), .valout(sr_bit_3_11_valout));
  sr_bit_3 sr_bit_3_12 (.val(sr_bit_3_10_valout), .clk1(clk1), .clk2(clk2), .valout(sr_bit_3_12_valout));
  sr_bit_4 sr_bit_4_43 (.val(sr_bit_4_35_valout), .clk1(clk1), .clk2(clk2), .valout(sr_bit_4_43_valout));
  sr_bit_4 sr_bit_4_44 (.val(sr_bit_4_36_valout), .clk1(clk1), .clk2(clk2), .valout(sr_bit_4_44_valout));
  sr_bit_7 sr_bit_7_11 (.val(sr_bit_7_9_valout), .clk1(clk1), .clk2(clk2), .valout(sr_bit_7_11_valout));
  sr_bit_7 sr_bit_7_12 (.val(sr_bit_7_10_valout), .clk1(clk1), .clk2(clk2), .valout(sr_bit_7_12_valout));
  sr_bit_5 sr_bit_5_31 (.val(sr_bit_5_25_valout), .clk1(clk1), .clk2(clk2), .valout(sr_bit_5_31_valout));
  sr_bit_5 sr_bit_5_32 (.val(sr_bit_5_26_valout), .clk1(clk1), .clk2(clk2), .valout(sr_bit_5_32_valout));
  sr_bit_2 sr_bit_2_11 (.val(sr_bit_2_9_valout), .clk1(clk1), .clk2(clk2), .valout(sr_bit_2_11_valout));
  sr_bit_2 sr_bit_2_12 (.val(sr_bit_2_10_valout), .clk1(clk1), .clk2(clk2), .valout(sr_bit_2_12_valout));
  sr_bit_5 sr_bit_5_33 (.val(sr_bit_5_27_valout), .clk1(clk1), .clk2(clk2), .valout(sr_bit_5_33_valout));
  sr_bit_5 sr_bit_5_34 (.val(sr_bit_5_28_valout), .clk1(clk1), .clk2(clk2), .valout(sr_bit_5_34_valout));
  sr_bit sr_bit_11 (.clk1(clk1), .clk2(clk2), .val(sr_bit_9_valout), .valout(sr_bit_11_valout));  // open: nvalout
  sr_bit sr_bit_12 (.clk1(clk1), .clk2(clk2), .val(sr_bit_10_valout), .valout(sr_bit_12_valout));  // open: nvalout
  sr_bit_5 sr_bit_5_35 (.val(sr_bit_5_29_valout), .clk1(clk1), .clk2(clk2), .valout(sr_bit_5_35_valout));
  sr_bit_5 sr_bit_5_36 (.val(sr_bit_5_30_valout), .clk1(clk1), .clk2(clk2), .valout(sr_bit_5_36_valout));
  sr_bit_4 sr_bit_4_45 (.val(sr_bit_4_37_valout), .clk1(clk1), .clk2(clk2), .valout(sr_bit_4_45_valout));
  sr_bit_4 sr_bit_4_46 (.val(sr_bit_4_38_valout), .clk1(clk1), .clk2(clk2), .valout(sr_bit_4_46_valout));
  sr_bit_4 sr_bit_4_47 (.val(sr_bit_4_39_valout), .clk1(clk1), .clk2(clk2), .valout(sr_bit_4_47_valout));
  sr_bit_4 sr_bit_4_48 (.val(sr_bit_4_40_valout), .clk1(clk1), .clk2(clk2), .valout(sr_bit_4_48_valout));
  sr_bit_4 sr_bit_4_49 (.val(sr_bit_4_41_valout), .clk1(clk1), .clk2(clk2), .valout(sr_bit_4_49_valout));
  sr_bit_4 sr_bit_4_50 (.val(sr_bit_4_42_valout), .clk1(clk1), .clk2(clk2), .valout(sr_bit_4_50_valout));
  sr_bit_3 sr_bit_3_13 (.val(sr_bit_3_11_valout), .clk1(clk1), .clk2(clk2), .valout(sr_bit_3_13_valout));
  sr_bit_3 sr_bit_3_14 (.val(sr_bit_3_12_valout), .clk1(clk1), .clk2(clk2), .valout(sr_bit_3_14_valout));
  sr_bit_4 sr_bit_4_51 (.val(sr_bit_4_43_valout), .clk1(clk1), .clk2(clk2), .valout(sr_bit_4_51_valout));
  sr_bit_4 sr_bit_4_52 (.val(sr_bit_4_44_valout), .clk1(clk1), .clk2(clk2), .valout(sr_bit_4_52_valout));
  sr_bit_7 sr_bit_7_13 (.val(sr_bit_7_11_valout), .clk1(clk1), .clk2(clk2), .valout(sr_bit_7_13_valout));
  sr_bit_7 sr_bit_7_14 (.val(sr_bit_7_12_valout), .clk1(clk1), .clk2(clk2), .valout(sr_bit_7_14_valout));
  sr_bit_5 sr_bit_5_37 (.val(sr_bit_5_31_valout), .clk1(clk1), .clk2(clk2), .valout(sr_bit_5_37_valout));
  sr_bit_5 sr_bit_5_38 (.val(sr_bit_5_32_valout), .clk1(clk1), .clk2(clk2), .valout(sr_bit_5_38_valout));
  sr_bit_2 sr_bit_2_13 (.val(sr_bit_2_11_valout), .clk1(clk1), .clk2(clk2), .valout(sr_bit_2_13_valout));
  sr_bit_2 sr_bit_2_14 (.val(sr_bit_2_12_valout), .clk1(clk1), .clk2(clk2), .valout(sr_bit_2_14_valout));
  sr_bit_5 sr_bit_5_39 (.val(sr_bit_5_33_valout), .clk1(clk1), .clk2(clk2), .valout(sr_bit_5_39_valout));
  sr_bit_5 sr_bit_5_40 (.val(sr_bit_5_34_valout), .clk1(clk1), .clk2(clk2), .valout(sr_bit_5_40_valout));
  sr_bit sr_bit_13 (.clk1(clk1), .clk2(clk2), .val(sr_bit_11_valout), .valout(sr_bit_13_valout));  // open: nvalout
  sr_bit sr_bit_14 (.clk1(clk1), .clk2(clk2), .val(sr_bit_12_valout), .valout(sr_bit_14_valout));  // open: nvalout
  sr_bit_5 sr_bit_5_41 (.val(sr_bit_5_35_valout), .clk1(clk1), .clk2(clk2), .valout(sr_bit_5_41_valout));
  sr_bit_5 sr_bit_5_42 (.val(sr_bit_5_36_valout), .clk1(clk1), .clk2(clk2), .valout(sr_bit_5_42_valout));
  sr_bit_4 sr_bit_4_53 (.val(sr_bit_4_45_valout), .clk1(clk1), .clk2(clk2), .valout(sr_bit_4_53_valout));
  sr_bit_4 sr_bit_4_54 (.val(sr_bit_4_46_valout), .clk1(clk1), .clk2(clk2), .valout(sr_bit_4_54_valout));
  sr_bit_4 sr_bit_4_55 (.val(sr_bit_4_47_valout), .clk1(clk1), .clk2(clk2), .valout(sr_bit_4_55_valout));
  sr_bit_4 sr_bit_4_56 (.val(sr_bit_4_48_valout), .clk1(clk1), .clk2(clk2), .valout(sr_bit_4_56_valout));
  sr_bit_4 sr_bit_4_57 (.val(sr_bit_4_49_valout), .clk1(clk1), .clk2(clk2), .valout(sr_bit_4_57_valout));
  sr_bit_4 sr_bit_4_58 (.val(sr_bit_4_50_valout), .clk1(clk1), .clk2(clk2), .valout(sr_bit_4_58_valout));
  sr_bit_3 sr_bit_3_15 (.val(sr_bit_3_13_valout), .clk1(clk1), .clk2(clk2), .valout(sr_bit_3_15_valout));
  sr_bit_3 sr_bit_3_16 (.val(sr_bit_3_14_valout), .clk1(clk1), .clk2(clk2), .valout(sr_bit_3_16_valout));
  sr_bit_4 sr_bit_4_59 (.val(sr_bit_4_51_valout), .clk1(clk1), .clk2(clk2), .valout(sr_bit_4_59_valout));
  sr_bit_4 sr_bit_4_60 (.val(sr_bit_4_52_valout), .clk1(clk1), .clk2(clk2), .valout(sr_bit_4_60_valout));
  sr_bit_7 sr_bit_7_15 (.val(sr_bit_7_13_valout), .clk1(clk1), .clk2(clk2), .valout(sr_bit_7_15_valout));
  sr_bit_7 sr_bit_7_16 (.val(sr_bit_7_14_valout), .clk1(clk1), .clk2(clk2), .valout(sr_bit_7_16_valout));
  sr_bit_5 sr_bit_5_43 (.val(sr_bit_5_37_valout), .clk1(clk1), .clk2(clk2), .valout(sr_bit_5_43_valout));
  sr_bit_5 sr_bit_5_44 (.val(sr_bit_5_38_valout), .clk1(clk1), .clk2(clk2), .valout(sr_bit_5_44_valout));
  sr_bit_2 sr_bit_2_15 (.val(sr_bit_2_13_valout), .clk1(clk1), .clk2(clk2), .valout(sr_bit_2_15_valout));
  sr_bit_2 sr_bit_2_16 (.val(sr_bit_2_14_valout), .clk1(clk1), .clk2(clk2), .valout(sr_bit_2_16_valout));
  sr_bit_5 sr_bit_5_45 (.val(sr_bit_5_39_valout), .clk1(clk1), .clk2(clk2), .valout(sr_bit_5_45_valout));
  sr_bit_5 sr_bit_5_46 (.val(sr_bit_5_40_valout), .clk1(clk1), .clk2(clk2), .valout(sr_bit_5_46_valout));
  sr_bit sr_bit_15 (.clk1(clk1), .clk2(clk2), .val(sr_bit_13_valout), .valout(sr_bit_15_valout));  // open: nvalout
  sr_bit sr_bit_16 (.clk1(clk1), .clk2(clk2), .val(sr_bit_14_valout), .valout(sr_bit_16_valout));  // open: nvalout
  sr_bit_5 sr_bit_5_47 (.val(sr_bit_5_41_valout), .clk1(clk1), .clk2(clk2), .valout(sr_bit_5_47_valout));
  sr_bit_5 sr_bit_5_48 (.val(sr_bit_5_42_valout), .clk1(clk1), .clk2(clk2), .valout(sr_bit_5_48_valout));
  sr_bit_4 sr_bit_4_61 (.val(sr_bit_4_53_valout), .clk1(clk1), .clk2(clk2), .valout(sr_bit_4_61_valout));
  sr_bit_4 sr_bit_4_62 (.val(sr_bit_4_54_valout), .clk1(clk1), .clk2(clk2), .valout(sr_bit_4_62_valout));
  sr_bit_4 sr_bit_4_63 (.val(sr_bit_4_55_valout), .clk1(clk1), .clk2(clk2), .valout(sr_bit_4_63_valout));
  sr_bit_4 sr_bit_4_64 (.val(sr_bit_4_56_valout), .clk1(clk1), .clk2(clk2), .valout(sr_bit_4_64_valout));
  sr_bit_4 sr_bit_4_65 (.val(sr_bit_4_57_valout), .clk1(clk1), .clk2(clk2), .valout(sr_bit_4_65_valout));
  sr_bit_4 sr_bit_4_66 (.val(sr_bit_4_58_valout), .clk1(clk1), .clk2(clk2), .valout(sr_bit_4_66_valout));
  sr_bit_3 sr_bit_3_17 (.val(sr_bit_3_15_valout), .clk1(clk1), .clk2(clk2), .valout(sr_bit_3_17_valout));
  sr_bit_3 sr_bit_3_18 (.val(sr_bit_3_16_valout), .clk1(clk1), .clk2(clk2), .valout(sr_bit_3_18_valout));
  sr_bit_4 sr_bit_4_67 (.val(sr_bit_4_59_valout), .clk1(clk1), .clk2(clk2), .valout(sr_bit_4_67_valout));
  sr_bit_4 sr_bit_4_68 (.val(sr_bit_4_60_valout), .clk1(clk1), .clk2(clk2), .valout(sr_bit_4_68_valout));
  sr_bit_7 sr_bit_7_17 (.val(sr_bit_7_15_valout), .clk1(clk1), .clk2(clk2), .valout(sr_bit_7_17_valout));
  sr_bit_7 sr_bit_7_18 (.val(sr_bit_7_16_valout), .clk1(clk1), .clk2(clk2), .valout(sr_bit_7_18_valout));
  sr_bit_5 sr_bit_5_49 (.val(sr_bit_5_43_valout), .clk1(clk1), .clk2(clk2), .valout(sr_bit_5_49_valout));
  sr_bit_5 sr_bit_5_50 (.val(sr_bit_5_44_valout), .clk1(clk1), .clk2(clk2), .valout(sr_bit_5_50_valout));
  sr_bit_2 sr_bit_2_17 (.val(sr_bit_2_15_valout), .clk1(clk1), .clk2(clk2), .valout(sr_bit_2_17_valout));
  sr_bit_2 sr_bit_2_18 (.val(sr_bit_2_16_valout), .clk1(clk1), .clk2(clk2), .valout(sr_bit_2_18_valout));
  sr_bit_5 sr_bit_5_51 (.val(sr_bit_5_45_valout), .clk1(clk1), .clk2(clk2), .valout(sr_bit_5_51_valout));
  sr_bit_5 sr_bit_5_52 (.val(sr_bit_5_46_valout), .clk1(clk1), .clk2(clk2), .valout(sr_bit_5_52_valout));
  sr_bit sr_bit_17 (.clk1(clk1), .clk2(clk2), .val(sr_bit_15_valout), .valout(sr_bit_17_valout));  // open: nvalout
  sr_bit sr_bit_18 (.clk1(clk1), .clk2(clk2), .val(sr_bit_16_valout), .valout(sr_bit_18_valout));  // open: nvalout
  sr_bit_5 sr_bit_5_53 (.val(sr_bit_5_47_valout), .clk1(clk1), .clk2(clk2), .valout(sr_bit_5_53_valout));
  sr_bit_5 sr_bit_5_54 (.val(sr_bit_5_48_valout), .clk1(clk1), .clk2(clk2), .valout(sr_bit_5_54_valout));
  sr_bit_4 sr_bit_4_69 (.val(sr_bit_4_61_valout), .clk1(clk1), .clk2(clk2), .valout(sr_bit_4_69_valout));
  sr_bit_4 sr_bit_4_70 (.val(sr_bit_4_62_valout), .clk1(clk1), .clk2(clk2), .valout(sr_bit_4_70_valout));
  sr_bit_4 sr_bit_4_71 (.val(sr_bit_4_63_valout), .clk1(clk1), .clk2(clk2), .valout(sr_bit_4_71_valout));
  sr_bit_4 sr_bit_4_72 (.val(sr_bit_4_64_valout), .clk1(clk1), .clk2(clk2), .valout(sr_bit_4_72_valout));
  sr_bit_4 sr_bit_4_73 (.val(sr_bit_4_65_valout), .clk1(clk1), .clk2(clk2), .valout(sr_bit_4_73_valout));
  sr_bit_4 sr_bit_4_74 (.val(sr_bit_4_66_valout), .clk1(clk1), .clk2(clk2), .valout(sr_bit_4_74_valout));
  sr_bit_3 sr_bit_3_19 (.val(sr_bit_3_17_valout), .clk1(clk1), .clk2(clk2), .valout(sr_bit_3_19_valout));
  sr_bit_3 sr_bit_3_20 (.val(sr_bit_3_18_valout), .clk1(clk1), .clk2(clk2), .valout(sr_bit_3_20_valout));
  sr_bit_4 sr_bit_4_75 (.val(sr_bit_4_67_valout), .clk1(clk1), .clk2(clk2), .valout(sr_bit_4_75_valout));
  sr_bit_4 sr_bit_4_76 (.val(sr_bit_4_68_valout), .clk1(clk1), .clk2(clk2), .valout(sr_bit_4_76_valout));
  sr_bit_7 sr_bit_7_19 (.val(sr_bit_7_17_valout), .clk1(clk1), .clk2(clk2), .valout(sr_bit_7_19_valout));
  sr_bit_7 sr_bit_7_20 (.val(sr_bit_7_18_valout), .clk1(clk1), .clk2(clk2), .valout(sr_bit_7_20_valout));
  sr_bit_5 sr_bit_5_55 (.val(sr_bit_5_49_valout), .clk1(clk1), .clk2(clk2), .valout(sr_bit_5_55_valout));
  sr_bit_5 sr_bit_5_56 (.val(sr_bit_5_50_valout), .clk1(clk1), .clk2(clk2), .valout(sr_bit_5_56_valout));
  sr_bit_2 sr_bit_2_19 (.val(sr_bit_2_17_valout), .clk1(clk1), .clk2(clk2), .valout(sr_bit_2_19_valout));
  sr_bit_2 sr_bit_2_20 (.val(sr_bit_2_18_valout), .clk1(clk1), .clk2(clk2), .valout(sr_bit_2_20_valout));
  sr_bit_5 sr_bit_5_57 (.val(sr_bit_5_51_valout), .clk1(clk1), .clk2(clk2), .valout(sr_bit_5_57_valout));
  sr_bit_5 sr_bit_5_58 (.val(sr_bit_5_52_valout), .clk1(clk1), .clk2(clk2), .valout(sr_bit_5_58_valout));
  sr_bit sr_bit_19 (.clk1(clk1), .clk2(clk2), .val(sr_bit_17_valout), .valout(sr_bit_19_valout));  // open: nvalout
  sr_bit sr_bit_20 (.clk1(clk1), .clk2(clk2), .val(sr_bit_18_valout), .valout(sr_bit_20_valout));  // open: nvalout
  sr_bit_5 sr_bit_5_59 (.val(sr_bit_5_53_valout), .clk1(clk1), .clk2(clk2), .valout(sr_bit_5_59_valout));
  sr_bit_5 sr_bit_5_60 (.val(sr_bit_5_54_valout), .clk1(clk1), .clk2(clk2), .valout(sr_bit_5_60_valout));
  sr_bit_4 sr_bit_4_77 (.val(sr_bit_4_69_valout), .clk1(clk1), .clk2(clk2), .valout(sr_bit_4_77_valout));
  sr_bit_4 sr_bit_4_78 (.val(sr_bit_4_70_valout), .clk1(clk1), .clk2(clk2), .valout(sr_bit_4_78_valout));
  sr_bit_4 sr_bit_4_79 (.val(sr_bit_4_71_valout), .clk1(clk1), .clk2(clk2), .valout(sr_bit_4_79_valout));
  sr_bit_4 sr_bit_4_80 (.val(sr_bit_4_72_valout), .clk1(clk1), .clk2(clk2), .valout(sr_bit_4_80_valout));
  sr_bit_4 sr_bit_4_81 (.val(sr_bit_4_73_valout), .clk1(clk1), .clk2(clk2), .valout(sr_bit_4_81_valout));
  sr_bit_4 sr_bit_4_82 (.val(sr_bit_4_74_valout), .clk1(clk1), .clk2(clk2), .valout(sr_bit_4_82_valout));
  sr_bit_3 sr_bit_3_21 (.val(sr_bit_3_19_valout), .clk1(clk1), .clk2(clk2), .valout(sr_bit_3_21_valout));
  sr_bit_3 sr_bit_3_22 (.val(sr_bit_3_20_valout), .clk1(clk1), .clk2(clk2), .valout(sr_bit_3_22_valout));
  sr_bit_4 sr_bit_4_83 (.val(sr_bit_4_75_valout), .clk1(clk1), .clk2(clk2), .valout(sr_bit_4_83_valout));
  sr_bit_4 sr_bit_4_84 (.val(sr_bit_4_76_valout), .clk1(clk1), .clk2(clk2), .valout(sr_bit_4_84_valout));
  sr_bit_7 sr_bit_7_21 (.val(sr_bit_7_19_valout), .clk1(clk1), .clk2(clk2), .valout(sr_bit_7_21_valout));
  sr_bit_7 sr_bit_7_22 (.val(sr_bit_7_20_valout), .clk1(clk1), .clk2(clk2), .valout(sr_bit_7_22_valout));
  sr_bit_5 sr_bit_5_61 (.val(sr_bit_5_55_valout), .clk1(clk1), .clk2(clk2), .valout(sr_bit_5_61_valout));
  sr_bit_5 sr_bit_5_62 (.val(sr_bit_5_56_valout), .clk1(clk1), .clk2(clk2), .valout(sr_bit_5_62_valout));
  sr_bit_2 sr_bit_2_21 (.val(sr_bit_2_19_valout), .clk1(clk1), .clk2(clk2), .valout(sr_bit_2_21_valout));
  sr_bit_2 sr_bit_2_22 (.val(sr_bit_2_20_valout), .clk1(clk1), .clk2(clk2), .valout(sr_bit_2_22_valout));
  sr_bit_5 sr_bit_5_63 (.val(sr_bit_5_57_valout), .clk1(clk1), .clk2(clk2), .valout(sr_bit_5_63_valout));
  sr_bit_5 sr_bit_5_64 (.val(sr_bit_5_58_valout), .clk1(clk1), .clk2(clk2), .valout(sr_bit_5_64_valout));
  sr_bit sr_bit_21 (.clk1(clk1), .clk2(clk2), .val(sr_bit_19_valout), .valout(sr_bit_21_valout));  // open: nvalout
  sr_bit sr_bit_22 (.clk1(clk1), .clk2(clk2), .val(sr_bit_20_valout), .valout(sr_bit_22_valout));  // open: nvalout
  sr_bit_5 sr_bit_5_65 (.val(sr_bit_5_59_valout), .clk1(clk1), .clk2(clk2), .valout(sr_bit_5_65_valout));
  sr_bit_5 sr_bit_5_66 (.val(sr_bit_5_60_valout), .clk1(clk1), .clk2(clk2), .valout(sr_bit_5_66_valout));
  sr_bit_4 sr_bit_4_85 (.val(sr_bit_4_77_valout), .clk1(clk1), .clk2(clk2), .valout(sr_bit_4_85_valout));
  sr_bit_4 sr_bit_4_86 (.val(sr_bit_4_78_valout), .clk1(clk1), .clk2(clk2), .valout(sr_bit_4_86_valout));
  sr_bit_4 sr_bit_4_87 (.val(sr_bit_4_79_valout), .clk1(clk1), .clk2(clk2), .valout(sr_bit_4_87_valout));
  sr_bit_4 sr_bit_4_88 (.val(sr_bit_4_80_valout), .clk1(clk1), .clk2(clk2), .valout(sr_bit_4_88_valout));
  sr_bit_4 sr_bit_4_89 (.val(sr_bit_4_81_valout), .clk1(clk1), .clk2(clk2), .valout(sr_bit_4_89_valout));
  sr_bit_4 sr_bit_4_90 (.val(sr_bit_4_82_valout), .clk1(clk1), .clk2(clk2), .valout(sr_bit_4_90_valout));
  sr_bit_3 sr_bit_3_23 (.val(sr_bit_3_21_valout), .clk1(clk1), .clk2(clk2), .valout(sr_bit_3_23_valout));
  sr_bit_3 sr_bit_3_24 (.val(sr_bit_3_22_valout), .clk1(clk1), .clk2(clk2), .valout(sr_bit_3_24_valout));
  sr_bit_4 sr_bit_4_91 (.val(sr_bit_4_83_valout), .clk1(clk1), .clk2(clk2), .valout(sr_bit_4_91_valout));
  sr_bit_4 sr_bit_4_92 (.val(sr_bit_4_84_valout), .clk1(clk1), .clk2(clk2), .valout(sr_bit_4_92_valout));
  sr_bit_7 sr_bit_7_23 (.val(sr_bit_7_21_valout), .clk1(clk1), .clk2(clk2), .valout(sr_bit_7_23_valout));
  sr_bit_7 sr_bit_7_24 (.val(sr_bit_7_22_valout), .clk1(clk1), .clk2(clk2), .valout(sr_bit_7_24_valout));
  sr_bit_5 sr_bit_5_67 (.val(sr_bit_5_61_valout), .clk1(clk1), .clk2(clk2), .valout(sr_bit_5_67_valout));
  sr_bit_5 sr_bit_5_68 (.val(sr_bit_5_62_valout), .clk1(clk1), .clk2(clk2), .valout(sr_bit_5_68_valout));
  sr_bit_2 sr_bit_2_23 (.val(sr_bit_2_21_valout), .clk1(clk1), .clk2(clk2), .valout(sr_bit_2_23_valout));
  sr_bit_2 sr_bit_2_24 (.val(sr_bit_2_22_valout), .clk1(clk1), .clk2(clk2), .valout(sr_bit_2_24_valout));
  sr_bit_5 sr_bit_5_69 (.val(sr_bit_5_63_valout), .clk1(clk1), .clk2(clk2), .valout(sr_bit_5_69_valout));
  sr_bit_5 sr_bit_5_70 (.val(sr_bit_5_64_valout), .clk1(clk1), .clk2(clk2), .valout(sr_bit_5_70_valout));
  sr_bit sr_bit_23 (.clk1(clk1), .clk2(clk2), .val(sr_bit_21_valout), .valout(sr_bit_23_valout));  // open: nvalout
  sr_bit sr_bit_24 (.clk1(clk1), .clk2(clk2), .val(sr_bit_22_valout), .valout(sr_bit_24_valout));  // open: nvalout
  sr_bit_5 sr_bit_5_71 (.val(sr_bit_5_65_valout), .clk1(clk1), .clk2(clk2), .valout(sr_bit_5_71_valout));
  sr_bit_5 sr_bit_5_72 (.val(sr_bit_5_66_valout), .clk1(clk1), .clk2(clk2), .valout(sr_bit_5_72_valout));
  sr_bit_4 sr_bit_4_93 (.val(sr_bit_4_85_valout), .clk1(clk1), .clk2(clk2), .valout(sr_bit_4_93_valout));
  sr_bit_4 sr_bit_4_94 (.val(sr_bit_4_86_valout), .clk1(clk1), .clk2(clk2), .valout(sr_bit_4_94_valout));
  sr_bit_4 sr_bit_4_95 (.val(sr_bit_4_87_valout), .clk1(clk1), .clk2(clk2), .valout(sr_bit_4_95_valout));
  sr_bit_4 sr_bit_4_96 (.val(sr_bit_4_88_valout), .clk1(clk1), .clk2(clk2), .valout(sr_bit_4_96_valout));
  assign controlled_buffer_45_out = d_ff_1_q ? sr_bit_4_89_valout : 4'bz;  // Controlled_Buffer controlled_buffer_45
  assign controlled_buffer_45_out = d_ff_1_qn ? sr_bit_4_90_valout : 4'bz;  // Controlled_Buffer controlled_buffer_46
  assign controlled_buffer_47_out = d_ff_1_q ? sr_bit_3_23_valout : 3'bz;  // Controlled_Buffer controlled_buffer_47
  assign controlled_buffer_47_out = d_ff_1_qn ? sr_bit_3_24_valout : 3'bz;  // Controlled_Buffer controlled_buffer_48
  assign controlled_buffer_49_out = d_ff_1_q ? sr_bit_4_91_valout : 4'bz;  // Controlled_Buffer controlled_buffer_49
  assign controlled_buffer_49_out = d_ff_1_qn ? sr_bit_4_92_valout : 4'bz;  // Controlled_Buffer controlled_buffer_50
  assign controlled_buffer_51_out = d_ff_1_q ? sr_bit_7_23_valout : 7'bz;  // Controlled_Buffer controlled_buffer_51
  assign controlled_buffer_51_out = d_ff_1_qn ? sr_bit_7_24_valout : 7'bz;  // Controlled_Buffer controlled_buffer_52
  assign controlled_buffer_53_out = d_ff_1_q ? sr_bit_5_67_valout : 5'bz;  // Controlled_Buffer controlled_buffer_53
  assign controlled_buffer_53_out = d_ff_1_qn ? sr_bit_5_68_valout : 5'bz;  // Controlled_Buffer controlled_buffer_54
  assign controlled_buffer_55_out = d_ff_1_q ? sr_bit_2_23_valout : 2'bz;  // Controlled_Buffer controlled_buffer_55
  assign controlled_buffer_55_out = d_ff_1_qn ? sr_bit_2_24_valout : 2'bz;  // Controlled_Buffer controlled_buffer_56
  assign controlled_buffer_57_out = d_ff_1_q ? sr_bit_5_69_valout : 5'bz;  // Controlled_Buffer controlled_buffer_57
  assign controlled_buffer_57_out = d_ff_1_qn ? sr_bit_5_70_valout : 5'bz;  // Controlled_Buffer controlled_buffer_58
  assign controlled_buffer_59_out = d_ff_1_q ? sr_bit_23_valout : 1'bz;  // Controlled_Buffer controlled_buffer_59
  assign controlled_buffer_59_out = d_ff_1_qn ? sr_bit_24_valout : 1'bz;  // Controlled_Buffer controlled_buffer_60
  assign controlled_buffer_61_out = d_ff_1_q ? sr_bit_5_71_valout : 5'bz;  // Controlled_Buffer controlled_buffer_61
  assign controlled_buffer_61_out = d_ff_1_qn ? sr_bit_5_72_valout : 5'bz;  // Controlled_Buffer controlled_buffer_62
  assign controlled_buffer_63_out = d_ff_1_q ? sr_bit_4_93_valout : 4'bz;  // Controlled_Buffer controlled_buffer_63
  assign controlled_buffer_63_out = d_ff_1_qn ? sr_bit_4_94_valout : 4'bz;  // Controlled_Buffer controlled_buffer_64
  assign controlled_buffer_65_out = d_ff_1_q ? sr_bit_4_95_valout : 4'bz;  // Controlled_Buffer controlled_buffer_65
  assign controlled_buffer_65_out = d_ff_1_qn ? sr_bit_4_96_valout : 4'bz;  // Controlled_Buffer controlled_buffer_66
  D_Flip_Flop #(.trigger("high")) d_ff_2 (
    .D(controlled_buffer_47_out[0]), .clk(clk1), .Qn(detune[0]));  // open: Q, preset, reset
  D_Flip_Flop #(.trigger("high")) d_ff_3 (
    .D(controlled_buffer_47_out[1]), .clk(clk1), .Qn(detune[1]));  // open: Q, preset, reset
  D_Flip_Flop #(.trigger("high")) d_ff_4 (
    .D(controlled_buffer_47_out[2]), .clk(clk1), .Qn(detune[2]));  // open: Q, preset, reset
  D_Flip_Flop #(.trigger("high")) d_ff_5 (
    .D(controlled_buffer_55_out[0]), .clk(clk1), .Qn(ks[0]));  // open: Q, preset, reset
  D_Flip_Flop #(.trigger("high")) d_ff_6 (
    .D(controlled_buffer_55_out[1]), .clk(clk1), .Qn(ks[1]));  // open: Q, preset, reset
  not not_44 (not_44_out, controlled_buffer_45_out[3]);
  not not_45 (ssg_b0, controlled_buffer_45_out[0]);
  not not_46 (not_46_out, controlled_buffer_45_out[1]);
  not not_47 (not_47_out, controlled_buffer_45_out[2]);
  D_Flip_Flop #(.trigger("high")) d_ff_7 (
    .D(controlled_buffer_51_out[0]), .clk(clk1), .Qn(tl[0]));  // open: Q, preset, reset
  D_Flip_Flop #(.trigger("high")) d_ff_8 (
    .D(controlled_buffer_51_out[1]), .clk(clk1), .Qn(tl[1]));  // open: Q, preset, reset
  D_Flip_Flop #(.trigger("high")) d_ff_9 (
    .D(controlled_buffer_51_out[2]), .clk(clk1), .Qn(tl[2]));  // open: Q, preset, reset
  D_Flip_Flop #(.trigger("high")) d_ff_10 (
    .D(controlled_buffer_51_out[3]), .clk(clk1), .Qn(tl[3]));  // open: Q, preset, reset
  D_Flip_Flop #(.trigger("high")) d_ff_11 (
    .D(controlled_buffer_51_out[4]), .clk(clk1), .Qn(tl[4]));  // open: Q, preset, reset
  D_Flip_Flop #(.trigger("high")) d_ff_12 (
    .D(controlled_buffer_51_out[5]), .clk(clk1), .Qn(tl[5]));  // open: Q, preset, reset
  D_Flip_Flop #(.trigger("high")) d_ff_13 (
    .D(controlled_buffer_51_out[6]), .clk(clk1), .Qn(tl[6]));  // open: Q, preset, reset
  D_Flip_Flop #(.trigger("high")) d_ff_14 (
    .D(controlled_buffer_53_out[0]), .clk(clk1), .Q(d_ff_14_q[0]));  // open: Qn, preset, reset
  D_Flip_Flop #(.trigger("high")) d_ff_15 (
    .D(controlled_buffer_53_out[1]), .clk(clk1), .Q(d_ff_14_q[1]));  // open: Qn, preset, reset
  D_Flip_Flop #(.trigger("high")) d_ff_16 (
    .D(controlled_buffer_53_out[2]), .clk(clk1), .Q(d_ff_14_q[2]));  // open: Qn, preset, reset
  D_Flip_Flop #(.trigger("high")) d_ff_17 (
    .D(controlled_buffer_53_out[3]), .clk(clk1), .Q(d_ff_14_q[3]));  // open: Qn, preset, reset
  D_Flip_Flop #(.trigger("high")) d_ff_18 (
    .D(controlled_buffer_53_out[4]), .clk(clk1), .Q(d_ff_14_q[4]));  // open: Qn, preset, reset
  D_Flip_Flop #(.trigger("high")) d_ff_19 (
    .D(controlled_buffer_57_out[0]), .clk(clk1), .Q(d_ff_19_q[0]));  // open: Qn, preset, reset
  D_Flip_Flop #(.trigger("high")) d_ff_20 (
    .D(controlled_buffer_57_out[1]), .clk(clk1), .Q(d_ff_19_q[1]));  // open: Qn, preset, reset
  D_Flip_Flop #(.trigger("high")) d_ff_21 (
    .D(controlled_buffer_57_out[2]), .clk(clk1), .Q(d_ff_19_q[2]));  // open: Qn, preset, reset
  D_Flip_Flop #(.trigger("high")) d_ff_22 (
    .D(controlled_buffer_57_out[3]), .clk(clk1), .Q(d_ff_19_q[3]));  // open: Qn, preset, reset
  D_Flip_Flop #(.trigger("high")) d_ff_23 (
    .D(controlled_buffer_57_out[4]), .clk(clk1), .Q(d_ff_19_q[4]));  // open: Qn, preset, reset
  D_Flip_Flop #(.trigger("high")) d_ff_24 (
    .D(controlled_buffer_61_out[0]), .clk(clk1), .Q(d_ff_24_q[0]));  // open: Qn, preset, reset
  D_Flip_Flop #(.trigger("high")) d_ff_25 (
    .D(controlled_buffer_61_out[1]), .clk(clk1), .Q(d_ff_24_q[1]));  // open: Qn, preset, reset
  D_Flip_Flop #(.trigger("high")) d_ff_26 (
    .D(controlled_buffer_61_out[2]), .clk(clk1), .Q(d_ff_24_q[2]));  // open: Qn, preset, reset
  D_Flip_Flop #(.trigger("high")) d_ff_27 (
    .D(controlled_buffer_61_out[3]), .clk(clk1), .Q(d_ff_24_q[3]));  // open: Qn, preset, reset
  D_Flip_Flop #(.trigger("high")) d_ff_28 (
    .D(controlled_buffer_61_out[4]), .clk(clk1), .Q(d_ff_24_q[4]));  // open: Qn, preset, reset
  D_Flip_Flop #(.trigger("high")) d_ff_29 (
    .D(controlled_buffer_63_out[0]), .clk(clk1), .Q(d_ff_29_q[0]));  // open: Qn, preset, reset
  D_Flip_Flop #(.trigger("high")) d_ff_30 (
    .D(controlled_buffer_63_out[1]), .clk(clk1), .Q(d_ff_29_q[1]));  // open: Qn, preset, reset
  D_Flip_Flop #(.trigger("high")) d_ff_31 (
    .D(controlled_buffer_63_out[2]), .clk(clk1), .Q(d_ff_29_q[2]));  // open: Qn, preset, reset
  D_Flip_Flop #(.trigger("high")) d_ff_32 (
    .D(controlled_buffer_63_out[3]), .clk(clk1), .Q(d_ff_29_q[3]));  // open: Qn, preset, reset
  D_Flip_Flop #(.trigger("high")) d_ff_33 (
    .D(controlled_buffer_65_out[0]), .clk(clk1), .Qn(sl[0]));  // open: Q, preset, reset
  D_Flip_Flop #(.trigger("high")) d_ff_34 (
    .D(controlled_buffer_65_out[1]), .clk(clk1), .Qn(sl[1]));  // open: Q, preset, reset
  D_Flip_Flop #(.trigger("high")) d_ff_35 (
    .D(controlled_buffer_65_out[2]), .clk(clk1), .Qn(sl[2]));  // open: Q, preset, reset
  D_Flip_Flop #(.trigger("high")) d_ff_36 (
    .D(controlled_buffer_65_out[3]), .clk(clk1), .Qn(sl[3]));  // open: Q, preset, reset
  not not_48 (ssg_enable, not_44_out);
  nand nand_1 (ssg_inv, ssg_enable, controlled_buffer_45_out[2]);
  nor nor_37 (ssg_0_or_4, controlled_buffer_45_out[0], controlled_buffer_45_out[1]);
  nor nor_38 (ssg_2_or_6, not_46_out, controlled_buffer_45_out[0]);
  nor nor_39 (ssg_3_or_7, ssg_b0, not_46_out);
  nor nor_40 (nor_40_out, ssg_b0, controlled_buffer_45_out[1], not_47_out);
  nor nor_41 (nor_41_out, ssg_b0, not_46_out, controlled_buffer_45_out[2]);
  sr_bit_4 sr_bit_4_97 (.val(controlled_buffer_49_out), .clk1(clk1), .clk2(clk2), .valout(sr_bit_4_97_valout));
  assign not_49_out = ~eg_state;  // NOT_Gate not_49, 2 bits wide
  or or_1 (ssg_3_or_5, nor_40_out, nor_41_out);
  assign bit_extender_21_out = {{4{nor_42_out}}, nor_42_out};  // Bit_Extender bit_extender_21
  assign bit_extender_22_out = {{4{nor_43_out}}, nor_43_out};  // Bit_Extender bit_extender_22
  not not_50 (not_50_out, controlled_buffer_59_out);
  assign bit_extender_23_out = {{4{nor_44_out}}, nor_44_out};  // Bit_Extender bit_extender_23
  assign and_1_out = d_ff_29_q & bit_extender_24_out;  // AND_Gate and_1, 4 bits wide
  assign bit_extender_24_out = {{3{nor_45_out[0]}}, nor_45_out[0]};  // Bit_Extender bit_extender_24
  nor nor_42 (nor_42_out, eg_state[1], eg_state[0]);
  nor nor_43 (nor_43_out, not_49_out[1], eg_state[0]);
  nor nor_44 (nor_44_out, eg_state[1], not_49_out[0]);
  nor nor_45 (nor_45_out[0], not_49_out[1], not_49_out[0]);
  assign and_2_out = d_ff_14_q & bit_extender_21_out;  // AND_Gate and_2, 5 bits wide
  assign and_3_out = d_ff_19_q & bit_extender_22_out;  // AND_Gate and_3, 5 bits wide
  not not_51 (am, not_50_out);
  assign and_4_out = d_ff_24_q & bit_extender_23_out;  // AND_Gate and_4, 5 bits wide
  sr_bit_4 sr_bit_4_98 (.val(sr_bit_4_97_valout), .clk1(clk1), .clk2(clk2), .valout(multi));
  assign rate = and_2_out | and_3_out | and_4_out | {and_1_out, nor_45_out[0]};  // OR_Gate or_2, 5 bits wide
endmodule

module sr_bit_4 (
  input  [3:0] val,
  input  clk1,
  input  clk2,
  output [3:0] valout
);

  wire [3:0] register_1_q;

  Register #(.trigger("high"), .width(4)) register_1 (.D(val), .en(clk1), .clk(clk1), .Q(register_1_q));  // open: clr
  Register #(.trigger("high"), .width(4)) register_2 (
    .D(register_1_q), .en(clk2), .clk(clk2), .Q(valout));  // open: clr
endmodule

module sr_bit_7 (
  input  [6:0] val,
  input  clk1,
  input  clk2,
  output [6:0] valout
);

  wire [6:0] register_1_q;

  Register #(.trigger("high"), .width(7)) register_1 (.D(val), .en(clk1), .clk(clk1), .Q(register_1_q));  // open: clr
  Register #(.trigger("high"), .width(7)) register_2 (
    .D(register_1_q), .en(clk2), .clk(clk2), .Q(valout));  // open: clr
endmodule

module sr_bit_5 (
  input  [4:0] val,
  input  clk1,
  input  clk2,
  output [4:0] valout
);

  wire [4:0] register_1_q;

  Register #(.trigger("high"), .width(5)) register_1 (.D(val), .en(clk1), .clk(clk1), .Q(register_1_q));  // open: clr
  Register #(.trigger("high"), .width(5)) register_2 (
    .D(register_1_q), .en(clk2), .clk(clk2), .Q(valout));  // open: clr
endmodule

module lfo (
  input  clk1,
  input  clk2,
  input  sync,
  input  [2:0] lfo_val,
  input  lfo_enable,
  input  in_6,
  input  [2:0] pms,
  output [5:0] lfo_am,
  output lfo_sign,
  output lfo_sh1_0,
  output lfo_sh1_1,
  output lfo_sh2_1,
  output lfo_sh2_2,
  output lfo_sh_2,
  output lfo_sh_1,
  output lfo_sh_0
);

  wire and_1_out, and_2_out, and_4_out, controlled_buffer_1_out, controlled_buffer_9_out,
       controlled_buffer_11_out, d_ff_1_qn, d_ff_2_qn, d_ff_6_qn, d_ff_7_qn, nand_1_out, nand_2_out,
       nand_3_out, nand_4_out, nand_5_out, nor_1_out, nor_2_out, nor_3_out, nor_4_out, nor_5_out, nor_6_out,
       nor_7_out, nor_8_out, nor_9_out, nor_10_out, nor_11_out, nor_12_out, nor_13_out, nor_14_out,
       nor_15_out, nor_17_out, nor_18_out, nor_19_out, nor_20_out, nor_21_out, nor_22_out, nor_23_out,
       nor_24_out, nor_25_out, nor_26_out, nor_27_out, nor_28_out, nor_29_out, nor_31_out, nor_32_out,
       nor_33_out, nor_34_out, nor_35_out, nor_36_out, not_1_out, not_3_out, not_4_out, not_7_out, not_8_out,
       not_10_out, not_11_out, not_12_out, not_13_out, not_14_out, not_15_out, sr_bit_1_valout;
  wire [2:0] bit_extender_2_out, not_2_out, not_5_out, not_6_out, xor_1_out;
  wire [5:0] bit_extender_4_out, not_19_out;
  wire [6:0] adder_1_out, adder_2_out, bit_extender_1_out, bit_extender_3_out, nor_16_out, nor_30_out,
       not_9_out, not_18_out, register_1_q, sr_bit_7_1_valout, sr_bit_7_o_1_out2, sr_bit_7_o_1_valout;

  not not_1 (not_1_out, in_6);
  nand nand_1 (nand_1_out, not_1_out, not_8_out);
  assign not_2_out = ~lfo_val;  // NOT_Gate not_2, 3 bits wide
  assign bit_extender_1_out = {{6{nand_1_out}}, nand_1_out};  // Bit_Extender bit_extender_1
  nor nor_1 (nor_1_out, sr_bit_7_o_1_out2[2], sr_bit_7_o_1_out2[3], sr_bit_7_o_1_out2[5], sr_bit_7_o_1_out2[6]);
  nor nor_2 (nor_2_out, sr_bit_7_o_1_out2[0], sr_bit_7_o_1_out2[2], sr_bit_7_o_1_out2[3], sr_bit_7_o_1_out2[6]);
  nor nor_3 (nor_3_out, sr_bit_7_o_1_out2[0], sr_bit_7_o_1_out2[1], sr_bit_7_o_1_out2[2], sr_bit_7_o_1_out2[6]);
  nor nor_4 (nor_4_out, sr_bit_7_o_1_out2[0], sr_bit_7_o_1_out2[1], sr_bit_7_o_1_out2[6]);
  nor nor_5 (nor_5_out, sr_bit_7_o_1_out2[1], sr_bit_7_o_1_out2[2], sr_bit_7_o_1_out2[3], sr_bit_7_o_1_out2[4], sr_bit_7_o_1_out2[5]);
  nor nor_6 (nor_6_out, sr_bit_7_o_1_out2[2], sr_bit_7_o_1_out2[3], sr_bit_7_o_1_out2[5]);
  not not_3 (not_3_out, sr_bit_7_o_1_out2[3]);
  nor nor_7 (nor_7_out, sr_bit_7_o_1_out2[0], sr_bit_7_o_1_out2[2]);
  nor nor_8 (nor_8_out, not_2_out[0], not_2_out[1], not_2_out[2]);
  nor nor_9 (nor_9_out, lfo_val[0], not_2_out[1], not_2_out[2]);
  nor nor_10 (nor_10_out, not_2_out[0], lfo_val[1], not_2_out[2]);
  nor nor_11 (nor_11_out, lfo_val[0], lfo_val[1], not_2_out[2]);
  nor nor_12 (nor_12_out, not_2_out[2], not_2_out[1], lfo_val[2]);
  nor nor_13 (nor_13_out, lfo_val[0], not_2_out[1], lfo_val[2]);
  nor nor_14 (nor_14_out, not_2_out[2], lfo_val[1], lfo_val[2]);
  nor nor_15 (nor_15_out, lfo_val[0], lfo_val[1], lfo_val[2]);
  assign nor_16_out = ~(bit_extender_1_out | not_9_out);  // NOR_Gate nor_16, 7 bits wide
  assign controlled_buffer_1_out = nor_8_out ? nor_1_out : 1'bz;  // Controlled_Buffer controlled_buffer_1
  assign controlled_buffer_1_out = nor_9_out ? nor_2_out : 1'bz;  // Controlled_Buffer controlled_buffer_2
  assign controlled_buffer_1_out = nor_10_out ? nor_3_out : 1'bz;  // Controlled_Buffer controlled_buffer_3
  D_Flip_Flop #(.trigger("high")) d_ff_1 (.D(sync), .clk(clk2), .Qn(d_ff_1_qn));  // open: Q, preset, reset
  assign controlled_buffer_1_out = nor_11_out ? nor_4_out : 1'bz;  // Controlled_Buffer controlled_buffer_4
  assign controlled_buffer_1_out = nor_12_out ? nor_5_out : 1'bz;  // Controlled_Buffer controlled_buffer_5
  assign controlled_buffer_1_out = nor_13_out ? nor_6_out : 1'bz;  // Controlled_Buffer controlled_buffer_6
  assign controlled_buffer_1_out = nor_14_out ? not_3_out : 1'bz;  // Controlled_Buffer controlled_buffer_7
  assign controlled_buffer_1_out = nor_15_out ? nor_7_out : 1'bz;  // Controlled_Buffer controlled_buffer_8
  sr_bit_7_o sr_bit_7_o_1 (
    .val(nor_16_out), .clk1(clk1), .clk2(clk2), .valout(sr_bit_7_o_1_valout), .out2(sr_bit_7_o_1_out2));
  D_Flip_Flop #(.trigger("high")) d_ff_2 (.D(not_4_out), .clk(clk2), .Qn(d_ff_2_qn));  // open: Q, preset, reset
  not not_4 (not_4_out, controlled_buffer_1_out);
  assign bit_extender_2_out = {{2{not_19_out[5]}}, not_19_out[5]};  // Bit_Extender bit_extender_2
  assign not_5_out = ~xor_1_out;  // NOT_Gate not_5, 3 bits wide
  assign not_6_out = ~pms;  // NOT_Gate not_6, 3 bits wide
  not not_7 (not_7_out, lfo_enable);
  Adder #(.width(7)) adder_1 (
    .a(sr_bit_7_o_1_valout), .b({7{1'b0}}), .out(adder_1_out), .cin(d_ff_1_qn));  // open: cout
  not not_8 (not_8_out, d_ff_2_qn);
  assign xor_1_out = not_19_out[4:2] ^ bit_extender_2_out;  // XOR_Gate xor_1, 3 bits wide
  nand nand_2 (nand_2_out, not_5_out[2], xor_1_out[1]);
  nor nor_17 (nor_17_out, not_5_out[0], xor_1_out[1]);
  nor nor_18 (nor_18_out, xor_1_out[0], not_5_out[1]);
  nor nor_19 (nor_19_out, not_5_out[0], not_5_out[1], xor_1_out[2]);
  nor nor_20 (nor_20_out, xor_1_out[1], not_5_out[2]);
  nor nor_21 (nor_21_out, xor_1_out[0], not_5_out[1], not_5_out[2]);
  nand nand_3 (nand_3_out, xor_1_out[0], xor_1_out[1], xor_1_out[2]);
  nor nor_22 (nor_22_out, not_6_out[0], not_6_out[1], not_6_out[2]);
  nor nor_23 (nor_23_out, pms[0], not_6_out[1], not_6_out[2]);
  nor nor_24 (nor_24_out, pms[0], pms[1], pms[2]);
  nor nor_25 (nor_25_out, pms[0], pms[1], not_6_out[2]);
  nor nor_26 (nor_26_out, not_6_out[0], not_6_out[1], pms[2]);
  nor nor_27 (nor_27_out, pms[0], not_6_out[1], pms[2]);
  nor nor_28 (nor_28_out, not_6_out[0], pms[1], pms[2]);
  nand nand_4 (nand_4_out, pms[0], not_6_out[1], pms[2]);
  assign not_9_out = ~adder_1_out;  // NOT_Gate not_9, 7 bits wide
  not not_10 (not_10_out, not_8_out);
  not not_11 (not_11_out, nand_3_out);
  not not_12 (not_12_out, nor_22_out);
  nor nor_29 (nor_29_out, nor_22_out, nor_23_out);
  not not_13 (not_13_out, nor_23_out);
  nand nand_5 (nand_5_out, nand_4_out, nor_29_out);
  D_Flip_Flop #(.trigger("high")) d_ff_3 (.D(not_12_out), .clk(clk1), .Qn(lfo_sh_2));  // open: Q, preset, reset
  D_Flip_Flop #(.trigger("high")) d_ff_4 (.D(not_14_out), .clk(clk1), .Qn(lfo_sh_0));  // open: Q, preset, reset
  not not_14 (not_14_out, nor_29_out);
  D_Flip_Flop #(.trigger("high")) d_ff_5 (.D(not_13_out), .clk(clk1), .Qn(lfo_sh_1));  // open: Q, preset, reset
  assign bit_extender_3_out = {{6{not_7_out}}, not_7_out};  // Bit_Extender bit_extender_3
  assign nor_30_out = ~(bit_extender_3_out | not_18_out);  // NOR_Gate nor_30, 7 bits wide
  nor nor_31 (nor_31_out, nor_19_out, nor_20_out);
  nor nor_32 (nor_32_out, nor_18_out, nor_19_out, not_11_out);
  nor nor_33 (nor_33_out, nor_17_out, nor_18_out);
  nor nor_34 (nor_34_out, nor_17_out, nor_19_out, nor_21_out);
  nor nor_35 (nor_35_out, nor_21_out, not_11_out);
  nor nor_36 (nor_36_out, nor_19_out, nor_20_out, nor_21_out);
  D_Flip_Flop #(.trigger("high")) d_ff_6 (.D(sync), .clk(clk2), .Qn(d_ff_6_qn));  // open: Q, preset, reset
  assign bit_extender_4_out = {{5{lfo_sign}}, lfo_sign};  // Bit_Extender bit_extender_4
  assign controlled_buffer_9_out = nor_24_out ? 1'b1 : 1'bz;  // Controlled_Buffer controlled_buffer_9
  assign controlled_buffer_9_out = nor_28_out ? not_5_out[2] : 1'bz;  // Controlled_Buffer controlled_buffer_10
  assign controlled_buffer_11_out = nor_24_out ? 1'b1 : 1'bz;  // Controlled_Buffer controlled_buffer_11
  assign controlled_buffer_11_out = nor_28_out ? 1'b1 : 1'bz;  // Controlled_Buffer controlled_buffer_12
  assign lfo_am = ~(not_19_out ^ bit_extender_4_out);  // XNOR_Gate xnor_1, 6 bits wide
  assign controlled_buffer_9_out = nor_27_out ? nor_31_out : 1'bz;  // Controlled_Buffer controlled_buffer_13
  assign controlled_buffer_9_out = nor_26_out ? nor_32_out : 1'bz;  // Controlled_Buffer controlled_buffer_14
  assign controlled_buffer_9_out = nor_25_out ? nor_33_out : 1'bz;  // Controlled_Buffer controlled_buffer_15
  assign controlled_buffer_11_out = nor_27_out ? nor_35_out : 1'bz;  // Controlled_Buffer controlled_buffer_16
  assign controlled_buffer_11_out = nor_26_out ? not_5_out[2] : 1'bz;  // Controlled_Buffer controlled_buffer_17
  assign controlled_buffer_11_out = nor_25_out ? nor_36_out : 1'bz;  // Controlled_Buffer controlled_buffer_18
  sr_bit sr_bit_1 (.clk1(clk1), .clk2(clk2), .val(d_ff_6_qn), .valout(sr_bit_1_valout));  // open: nvalout
  assign controlled_buffer_9_out = nand_5_out ? nor_34_out : 1'bz;  // Controlled_Buffer controlled_buffer_19
  assign controlled_buffer_11_out = nand_5_out ? nand_2_out : 1'bz;  // Controlled_Buffer controlled_buffer_20
  not not_15 (not_15_out, not_5_out[2]);
  D_Flip_Flop #(.trigger("high")) d_ff_7 (.D(sr_bit_1_valout), .clk(clk1), .Qn(d_ff_7_qn));  // open: Q, preset, reset
  sr_bit_7 sr_bit_7_1 (.val(nor_30_out), .clk1(clk1), .clk2(clk2), .valout(sr_bit_7_1_valout));
  Adder #(.width(7)) adder_2 (.a(sr_bit_7_1_valout), .b({7{1'b0}}), .out(adder_2_out), .cin(not_10_out));  // open: cout
  not not_16 (lfo_sh2_2, controlled_buffer_9_out);
  not not_17 (lfo_sh1_1, controlled_buffer_11_out);
  and and_1 (and_1_out, not_15_out, nand_5_out);
  and and_2 (and_2_out, not_11_out, nor_25_out);
  and and_3 (lfo_sh2_1, not_11_out, nand_5_out);
  assign not_18_out = ~adder_2_out;  // NOT_Gate not_18, 7 bits wide
  or or_1 (lfo_sh1_0, and_1_out, and_2_out);
  and and_4 (and_4_out, d_ff_7_qn, sr_bit_1_valout);
  Register #(.trigger("high"), .width(7)) register_1 (
    .D(sr_bit_7_1_valout), .en(and_4_out), .clk(and_4_out), .Q(register_1_q));  // open: clr
  assign {lfo_sign, not_19_out} = ~register_1_q;  // NOT_Gate not_19, 7 bits wide
endmodule

module sr_bit_8_o (
  input  [7:0] val,
  input  clk1,
  input  clk2,
  output [7:0] valout,
  output [7:0] out2
);

  wire [7:0] register_1_q;

  Register #(.trigger("high")) register_1 (.D(val), .en(clk1), .clk(clk1), .Q(register_1_q));  // open: clr
  Register #(.trigger("high")) register_2 (.D(register_1_q), .en(clk2), .clk(clk2), .Q(valout));  // open: clr
  assign out2 = ~register_1_q;  // NOT_Gate not_1, 8 bits wide
endmodule

module sr_bit_7_o (
  input  [6:0] val,
  input  clk1,
  input  clk2,
  output [6:0] valout,
  output [6:0] out2
);

  wire [6:0] register_1_q;

  Register #(.trigger("high"), .width(7)) register_1 (.D(val), .en(clk1), .clk(clk1), .Q(register_1_q));  // open: clr
  Register #(.trigger("high"), .width(7)) register_2 (
    .D(register_1_q), .en(clk2), .clk(clk2), .Q(valout));  // open: clr
  assign out2 = ~register_1_q;  // NOT_Gate not_1, 7 bits wide
endmodule

module lfo_2612 (
  input  clk1,
  input  clk2,
  input  sync,
  input  [2:0] lfo_val,
  input  lfo_enable,
  input  in_6,
  input  [2:0] pms,
  input  test,
  output [5:0] lfo_am,
  output lfo_sign,
  output lfo_sh1_0,
  output lfo_sh1_1,
  output lfo_sh2_1,
  output lfo_sh2_2,
  output lfo_sh_2,
  output lfo_sh_1,
  output lfo_sh_0
);

  wire and_1_out, and_2_out, and_4_out, controlled_buffer_1_out, controlled_buffer_9_out,
       controlled_buffer_11_out, d_ff_1_qn, d_ff_2_qn, d_ff_3_qn, d_ff_7_qn, d_ff_8_qn, nand_1_out,
       nand_2_out, nand_3_out, nand_4_out, nand_5_out, nand_6_out, nor_1_out, nor_2_out, nor_3_out,
       nor_4_out, nor_5_out, nor_6_out, nor_7_out, nor_8_out, nor_9_out, nor_10_out, nor_11_out, nor_12_out,
       nor_13_out, nor_14_out, nor_15_out, nor_17_out, nor_18_out, nor_19_out, nor_20_out, nor_21_out,
       nor_22_out, nor_23_out, nor_24_out, nor_25_out, nor_26_out, nor_27_out, nor_28_out, nor_30_out,
       nor_31_out, nor_32_out, nor_33_out, nor_34_out, nor_35_out, not_1_out, not_3_out, not_4_out,
       not_7_out, not_8_out, not_10_out, not_11_out, not_12_out, not_13_out, not_14_out, sr_bit_1_valout;
  wire [2:0] bit_extender_2_out, not_2_out, not_5_out, not_6_out, xor_1_out;
  wire [5:0] bit_extender_4_out, not_18_out;
  wire [6:0] adder_1_out, adder_2_out, bit_extender_1_out, bit_extender_3_out, nor_16_out, nor_29_out,
       not_9_out, not_17_out, register_1_q, sr_bit_7_1_valout, sr_bit_7_o_1_out2, sr_bit_7_o_1_valout;

  not not_1 (not_1_out, in_6);
  nand nand_1 (nand_1_out, not_1_out, not_8_out);
  assign not_2_out = ~lfo_val;  // NOT_Gate not_2, 3 bits wide
  assign bit_extender_1_out = {{6{nand_1_out}}, nand_1_out};  // Bit_Extender bit_extender_1
  nor nor_1 (nor_1_out, sr_bit_7_o_1_out2[2], sr_bit_7_o_1_out2[3], sr_bit_7_o_1_out2[5], sr_bit_7_o_1_out2[6]);
  nor nor_2 (nor_2_out, sr_bit_7_o_1_out2[0], sr_bit_7_o_1_out2[2], sr_bit_7_o_1_out2[3], sr_bit_7_o_1_out2[6]);
  nor nor_3 (nor_3_out, sr_bit_7_o_1_out2[0], sr_bit_7_o_1_out2[1], sr_bit_7_o_1_out2[2], sr_bit_7_o_1_out2[6]);
  nor nor_4 (nor_4_out, sr_bit_7_o_1_out2[0], sr_bit_7_o_1_out2[1], sr_bit_7_o_1_out2[6]);
  nor nor_5 (nor_5_out, sr_bit_7_o_1_out2[1], sr_bit_7_o_1_out2[2], sr_bit_7_o_1_out2[3], sr_bit_7_o_1_out2[4], sr_bit_7_o_1_out2[5]);
  nor nor_6 (nor_6_out, sr_bit_7_o_1_out2[2], sr_bit_7_o_1_out2[3], sr_bit_7_o_1_out2[5]);
  not not_3 (not_3_out, sr_bit_7_o_1_out2[3]);
  nor nor_7 (nor_7_out, sr_bit_7_o_1_out2[0], sr_bit_7_o_1_out2[2]);
  nor nor_8 (nor_8_out, not_2_out[0], not_2_out[1], not_2_out[2]);
  nor nor_9 (nor_9_out, lfo_val[0], not_2_out[1], not_2_out[2]);
  nor nor_10 (nor_10_out, not_2_out[0], lfo_val[1], not_2_out[2]);
  nor nor_11 (nor_11_out, lfo_val[0], lfo_val[1], not_2_out[2]);
  nor nor_12 (nor_12_out, not_2_out[2], not_2_out[1], lfo_val[2]);
  nor nor_13 (nor_13_out, lfo_val[0], not_2_out[1], lfo_val[2]);
  nor nor_14 (nor_14_out, not_2_out[2], lfo_val[1], lfo_val[2]);
  nor nor_15 (nor_15_out, lfo_val[0], lfo_val[1], lfo_val[2]);
  assign nor_16_out = ~(bit_extender_1_out | not_9_out);  // NOR_Gate nor_16, 7 bits wide
  assign controlled_buffer_1_out = nor_8_out ? nor_1_out : 1'bz;  // Controlled_Buffer controlled_buffer_1
  assign controlled_buffer_1_out = nor_9_out ? nor_2_out : 1'bz;  // Controlled_Buffer controlled_buffer_2
  assign controlled_buffer_1_out = nor_10_out ? nor_3_out : 1'bz;  // Controlled_Buffer controlled_buffer_3
  D_Flip_Flop #(.trigger("high")) d_ff_1 (.D(sync), .clk(clk2), .Qn(d_ff_1_qn));  // open: Q, preset, reset
  assign controlled_buffer_1_out = nor_11_out ? nor_4_out : 1'bz;  // Controlled_Buffer controlled_buffer_4
  assign controlled_buffer_1_out = nor_12_out ? nor_5_out : 1'bz;  // Controlled_Buffer controlled_buffer_5
  assign controlled_buffer_1_out = nor_13_out ? nor_6_out : 1'bz;  // Controlled_Buffer controlled_buffer_6
  assign controlled_buffer_1_out = nor_14_out ? not_3_out : 1'bz;  // Controlled_Buffer controlled_buffer_7
  assign controlled_buffer_1_out = nor_15_out ? nor_7_out : 1'bz;  // Controlled_Buffer controlled_buffer_8
  D_Flip_Flop #(.trigger("high")) d_ff_2 (.D(test), .clk(clk2), .Qn(d_ff_2_qn));  // open: Q, preset, reset
  sr_bit_7_o sr_bit_7_o_1 (
    .val(nor_16_out), .clk1(clk1), .clk2(clk2), .valout(sr_bit_7_o_1_valout), .out2(sr_bit_7_o_1_out2));
  D_Flip_Flop #(.trigger("high")) d_ff_3 (.D(not_4_out), .clk(clk2), .Qn(d_ff_3_qn));  // open: Q, preset, reset
  not not_4 (not_4_out, controlled_buffer_1_out);
  assign bit_extender_2_out = {{2{not_18_out[5]}}, not_18_out[5]};  // Bit_Extender bit_extender_2
  assign not_5_out = ~xor_1_out;  // NOT_Gate not_5, 3 bits wide
  assign not_6_out = ~pms;  // NOT_Gate not_6, 3 bits wide
  not not_7 (not_7_out, lfo_enable);
  nand nand_2 (nand_2_out, d_ff_1_qn, d_ff_2_qn);
  Adder #(.width(7)) adder_1 (
    .a(sr_bit_7_o_1_valout), .b({7{1'b0}}), .out(adder_1_out), .cin(nand_2_out));  // open: cout
  not not_8 (not_8_out, d_ff_3_qn);
  assign xor_1_out = not_18_out[4:2] ^ bit_extender_2_out;  // XOR_Gate xor_1, 3 bits wide
  nand nand_3 (nand_3_out, not_5_out[2], xor_1_out[1]);
  nor nor_17 (nor_17_out, xor_1_out[0], not_5_out[1]);
  nor nor_18 (nor_18_out, not_5_out[0], not_5_out[1], xor_1_out[2]);
  nor nor_19 (nor_19_out, xor_1_out[1], not_5_out[2]);
  nor nor_20 (nor_20_out, xor_1_out[0], not_5_out[1], not_5_out[2]);
  nand nand_4 (nand_4_out, xor_1_out[0], xor_1_out[1], xor_1_out[2]);
  nor nor_21 (nor_21_out, not_6_out[0], not_6_out[1], not_6_out[2]);
  nor nor_22 (nor_22_out, pms[0], not_6_out[1], not_6_out[2]);
  nor nor_23 (nor_23_out, pms[0], pms[1], pms[2]);
  nor nor_24 (nor_24_out, pms[0], pms[1], not_6_out[2]);
  nor nor_25 (nor_25_out, not_6_out[0], not_6_out[1], pms[2]);
  nor nor_26 (nor_26_out, pms[0], not_6_out[1], pms[2]);
  nor nor_27 (nor_27_out, not_6_out[0], pms[1], pms[2]);
  nand nand_5 (nand_5_out, pms[0], not_6_out[1], pms[2]);
  assign not_9_out = ~adder_1_out;  // NOT_Gate not_9, 7 bits wide
  not not_10 (not_10_out, nand_4_out);
  not not_11 (not_11_out, nor_21_out);
  nor nor_28 (nor_28_out, nor_21_out, nor_22_out);
  not not_12 (not_12_out, nor_22_out);
  nand nand_6 (nand_6_out, nand_5_out, nor_28_out);
  D_Flip_Flop #(.trigger("high")) d_ff_4 (.D(not_11_out), .clk(clk1), .Qn(lfo_sh_2));  // open: Q, preset, reset
  D_Flip_Flop #(.trigger("high")) d_ff_5 (.D(not_13_out), .clk(clk1), .Qn(lfo_sh_0));  // open: Q, preset, reset
  not not_13 (not_13_out, nor_28_out);
  D_Flip_Flop #(.trigger("high")) d_ff_6 (.D(not_12_out), .clk(clk1), .Qn(lfo_sh_1));  // open: Q, preset, reset
  assign bit_extender_3_out = {{6{not_7_out}}, not_7_out};  // Bit_Extender bit_extender_3
  assign nor_29_out = ~(bit_extender_3_out | not_17_out);  // NOR_Gate nor_29, 7 bits wide
  nor nor_30 (nor_30_out, nor_18_out, nor_19_out);
  nor nor_31 (nor_31_out, nor_17_out, nor_18_out, not_10_out);
  nor nor_32 (nor_32_out, 1'b0, nor_17_out);
  nor nor_33 (nor_33_out, 1'b0, nor_18_out, nor_20_out);
  nor nor_34 (nor_34_out, nor_20_out, not_10_out);
  nor nor_35 (nor_35_out, nor_18_out, nor_19_out, nor_20_out);
  D_Flip_Flop #(.trigger("high")) d_ff_7 (.D(sync), .clk(clk2), .Qn(d_ff_7_qn));  // open: Q, preset, reset
  assign bit_extender_4_out = {{5{lfo_sign}}, lfo_sign};  // Bit_Extender bit_extender_4
  assign controlled_buffer_9_out = nor_23_out ? 1'b1 : 1'bz;  // Controlled_Buffer controlled_buffer_9
  assign controlled_buffer_9_out = nor_27_out ? not_5_out[2] : 1'bz;  // Controlled_Buffer controlled_buffer_10
  assign controlled_buffer_11_out = nor_23_out ? 1'b1 : 1'bz;  // Controlled_Buffer controlled_buffer_11
  assign controlled_buffer_11_out = nor_27_out ? 1'b1 : 1'bz;  // Controlled_Buffer controlled_buffer_12
  assign lfo_am = ~(not_18_out ^ bit_extender_4_out);  // XNOR_Gate xnor_1, 6 bits wide
  assign controlled_buffer_9_out = nor_26_out ? nor_30_out : 1'bz;  // Controlled_Buffer controlled_buffer_13
  assign controlled_buffer_9_out = nor_25_out ? nor_31_out : 1'bz;  // Controlled_Buffer controlled_buffer_14
  assign controlled_buffer_9_out = nor_24_out ? nor_32_out : 1'bz;  // Controlled_Buffer controlled_buffer_15
  assign controlled_buffer_11_out = nor_26_out ? nor_34_out : 1'bz;  // Controlled_Buffer controlled_buffer_16
  assign controlled_buffer_11_out = nor_25_out ? not_5_out[2] : 1'bz;  // Controlled_Buffer controlled_buffer_17
  assign controlled_buffer_11_out = nor_24_out ? nor_35_out : 1'bz;  // Controlled_Buffer controlled_buffer_18
  sr_bit sr_bit_1 (.clk1(clk1), .clk2(clk2), .val(d_ff_7_qn), .valout(sr_bit_1_valout));  // open: nvalout
  assign controlled_buffer_9_out = nand_6_out ? nor_33_out : 1'bz;  // Controlled_Buffer controlled_buffer_19
  assign controlled_buffer_11_out = nand_6_out ? nand_3_out : 1'bz;  // Controlled_Buffer controlled_buffer_20
  not not_14 (not_14_out, not_5_out[2]);
  D_Flip_Flop #(.trigger("high")) d_ff_8 (.D(sr_bit_1_valout), .clk(clk1), .Qn(d_ff_8_qn));  // open: Q, preset, reset
  sr_bit_7 sr_bit_7_1 (.val(nor_29_out), .clk1(clk1), .clk2(clk2), .valout(sr_bit_7_1_valout));
  Adder #(.width(7)) adder_2 (.a(sr_bit_7_1_valout), .b({7{1'b0}}), .out(adder_2_out), .cin(d_ff_3_qn));  // open: cout
  not not_15 (lfo_sh2_2, controlled_buffer_9_out);
  not not_16 (lfo_sh1_1, controlled_buffer_11_out);
  and and_1 (and_1_out, not_14_out, nand_6_out);
  and and_2 (and_2_out, not_10_out, nor_24_out);
  and and_3 (lfo_sh2_1, not_10_out, nand_6_out);
  assign not_17_out = ~adder_2_out;  // NOT_Gate not_17, 7 bits wide
  or or_1 (lfo_sh1_0, and_1_out, and_2_out);
  and and_4 (and_4_out, d_ff_8_qn, sr_bit_1_valout);
  Register #(.trigger("high"), .width(7)) register_1 (
    .D(sr_bit_7_1_valout), .en(and_4_out), .clk(and_4_out), .Q(register_1_q));  // open: clr
  assign {lfo_sign, not_18_out} = ~register_1_q;  // NOT_Gate not_18, 7 bits wide
endmodule

module lfo_pm (
  input  clk1,
  input  clk2,
  input  lfo_sign,
  input  lfo_sh1_0,
  input  lfo_sh1_1,
  input  lfo_sh2_1,
  input  lfo_sh2_2,
  input  lfo_sh_2,
  input  lfo_sh_1,
  input  lfo_sh_0,
  input  [10:0] fnum,
  output [11:0] fnum_lfo
);

  wire adder_1_cout, d_ff_2_q;
  wire [6:0] adder_1_out, and_1_out, and_2_out, and_3_out, and_4_out, bit_extender_1_out, bit_extender_2_out,
       bit_extender_3_out, bit_extender_4_out, nor_1_out, nor_2_out, not_1_out, register_1_q, register_2_q;
  wire [7:0] and_5_out, and_6_out, and_7_out, bit_extender_5_out, bit_extender_6_out, bit_extender_7_out,
       bit_extender_8_out, nor_3_out, xnor_1_out;
  wire [7:7] not_2_out;
  wire [11:0] adder_2_out, not_3_out, register_3_q;
  wire [11:1] sr_bit_11_1_valout;
  wire [11:11] d_ff_1_qn;

  assign bit_extender_1_out = {{6{lfo_sh1_0}}, lfo_sh1_0};  // Bit_Extender bit_extender_1
  assign bit_extender_2_out = {{6{lfo_sh1_1}}, lfo_sh1_1};  // Bit_Extender bit_extender_2
  assign bit_extender_3_out = {{6{lfo_sh2_1}}, lfo_sh2_1};  // Bit_Extender bit_extender_3
  assign bit_extender_4_out = {{6{lfo_sh2_2}}, lfo_sh2_2};  // Bit_Extender bit_extender_4
  assign and_1_out = fnum[10:4] & bit_extender_1_out;  // AND_Gate and_1, 7 bits wide
  assign and_2_out = {1'b0, fnum[10:5]} & bit_extender_2_out;  // AND_Gate and_2, 7 bits wide
  assign and_3_out = {1'b0, fnum[10:5]} & bit_extender_3_out;  // AND_Gate and_3, 7 bits wide
  assign and_4_out = {2'b00, fnum[10:6]} & bit_extender_4_out;  // AND_Gate and_4, 7 bits wide
  sr_bit_11 sr_bit_11_1 (.val(fnum), .clk1(clk1), .clk2(clk2), .valout(sr_bit_11_1_valout));
  assign nor_1_out = ~(and_1_out | and_2_out);  // NOR_Gate nor_1, 7 bits wide
  assign nor_2_out = ~(and_3_out | and_4_out);  // NOR_Gate nor_2, 7 bits wide
  D_Flip_Flop #(.trigger("high")) d_ff_1 (.D(lfo_sign), .clk(clk1), .Qn(d_ff_1_qn[11]));  // open: Q, preset, reset
  Register #(.trigger("high"), .width(7)) register_1 (
    .D(nor_1_out), .en(clk1), .clk(clk1), .Q(register_1_q));  // open: clr
  Register #(.trigger("high"), .width(7)) register_2 (
    .D(nor_2_out), .en(clk1), .clk(clk1), .Q(register_2_q));  // open: clr
  D_Flip_Flop #(.trigger("high")) d_ff_2 (.D(d_ff_1_qn[11]), .clk(clk2), .Q(d_ff_2_q));  // open: Qn, preset, reset
  Adder #(.width(7)) adder_1 (.a(register_1_q), .b(register_2_q), .out(adder_1_out), .cin(1'b1), .cout(adder_1_cout));
  assign not_1_out = ~adder_1_out;  // NOT_Gate not_1, 7 bits wide
  not not_2 (not_2_out[7], adder_1_cout);
  assign bit_extender_5_out = {{7{lfo_sh_2}}, lfo_sh_2};  // Bit_Extender bit_extender_5
  assign bit_extender_6_out = {{7{lfo_sh_1}}, lfo_sh_1};  // Bit_Extender bit_extender_6
  assign bit_extender_7_out = {{7{lfo_sh_0}}, lfo_sh_0};  // Bit_Extender bit_extender_7
  assign and_5_out = {not_2_out[7], not_1_out} & bit_extender_5_out;  // AND_Gate and_5, 8 bits wide
  assign and_6_out = {1'b0, not_2_out[7], not_1_out[6:1]} & bit_extender_6_out;  // AND_Gate and_6, 8 bits wide
  assign and_7_out = {2'b00, not_2_out[7], not_1_out[6:2]} & bit_extender_7_out;  // AND_Gate and_7, 8 bits wide
  assign nor_3_out = ~(and_5_out | and_6_out | and_7_out);  // NOR_Gate nor_3, 8 bits wide
  assign bit_extender_8_out = {{7{d_ff_1_qn[11]}}, d_ff_1_qn[11]};  // Bit_Extender bit_extender_8
  assign xnor_1_out = ~(nor_3_out ^ bit_extender_8_out);  // XNOR_Gate xnor_1, 8 bits wide
  Register #(.trigger("high"), .width(12)) register_3 (
    .D({{4{d_ff_1_qn[11]}}, xnor_1_out}), .en(clk2), .clk(clk2), .Q(register_3_q));  // open: clr
  Adder #(.width(12)) adder_2 (
    .a(register_3_q), .b({sr_bit_11_1_valout, 1'b0}), .out(adder_2_out), .cin(d_ff_2_q));  // open: cout
  Register #(.trigger("high"), .width(12)) register_4 (
    .D(not_3_out), .en(clk1), .clk(clk1), .Q(fnum_lfo));  // open: clr
  assign not_3_out = ~adder_2_out;  // NOT_Gate not_3, 12 bits wide
endmodule
module pg (
  input  clk1,
  input  clk2,
  input  [2:0] blk,
  input  [1:0] note,
  input  [11:0] fnum_lfo,
  input  [3:0] multi,
  input  [2:0] detune,
  input  pg_reset,
  input  dbg,
  output [2:0] blk_l,
  output [1:0] note_l,
  output [9:0] phase,
  output dbg_bit
);

  wire adder_1_cout, adder_3_cout, adder_5_cout, d_ff_1_qn, d_ff_2_q, d_ff_3_qn, d_ff_4_qn, d_ff_5_qn,
       pg_detune_1_dt_sign, pg_multi_decoder_1_multi_sel3, pg_multi_decoder_1_multi_sel4,
       pg_multi_decoder_1_pg_res_l1, pg_multi_decoder_1_pg_res_l2;
  wire [2:0] pg_multi_decoder_1_multi_sel1;
  wire [4:0] pg_detune_1_dt_value, pg_multi_decoder_1_multi_sel2;
  wire [9:0] adder_1_out, adder_2_out, adder_3_out, adder_4_out, adder_5_out, adder_6_out,
       bit_extender_1_out, bit_extender_2_out, bit_extender_3_out, bit_extender_4_out, bit_extender_5_out,
       bit_extender_6_out, nand_1_out, nand_2_out, nand_3_out, nand_4_out, nand_5_out, nand_6_out, not_1_out,
       not_2_out, not_3_out, not_4_out, not_5_out, not_6_out, not_7_out, not_8_out, not_9_out, not_10_out,
       not_11_out, not_12_out, not_13_out, not_14_out, not_15_out, register_1_q, register_2_q, register_3_q,
       register_4_q, register_5_q, register_6_q, register_7_q, register_8_q, register_9_q, register_10_q,
       register_11_q, register_12_q, register_13_q, register_14_q, register_15_q, register_16_q,
       register_17_q, register_18_q, register_19_q, register_20_q, register_21_q, register_22_q,
       register_23_q, register_24_q, register_25_q, sr_bit_10_1_valout, sr_bit_10_2_valout,
       sr_bit_10_3_valout, sr_bit_10_4_valout, sr_bit_10_5_valout, sr_bit_10_6_valout, sr_bit_10_7_valout,
       sr_bit_10_8_valout, sr_bit_10_9_valout, sr_bit_10_10_valout, sr_bit_10_11_valout, sr_bit_10_12_valout,
       sr_bit_10_13_valout, sr_bit_10_14_valout, sr_bit_10_15_valout, sr_bit_10_16_valout,
       sr_bit_10_17_valout, sr_bit_10_18_valout, sr_bit_10_19_valout, sr_bit_10_20_valout,
       sr_bit_10_21_valout, sr_bit_10_22_valout, sr_bit_10_23_valout, sr_bit_10_24_valout,
       sr_bit_10_25_valout, sr_bit_10_26_valout, sr_bit_10_27_valout, sr_bit_10_28_valout,
       sr_bit_10_29_valout, sr_bit_10_30_valout, sr_bit_10_32_valout, sr_bit_10_33_valout,
       sr_bit_10_34_valout, sr_bit_10_35_valout, sr_bit_10_36_valout, sr_bit_10_37_valout,
       sr_bit_10_38_valout, sr_bit_10_39_valout, sr_bit_10_40_valout, sr_bit_10_41_valout,
       sr_bit_10_42_valout, sr_bit_10_43_valout, sr_bit_10_44_valout, sr_bit_10_45_valout,
       sr_bit_10_46_valout, sr_bit_10_47_valout, sr_bit_10_48_valout, sr_bit_10_49_valout;
  wire [16:0] pg_fnum_block_1_fnum_block, pg_freq_detune_1_freq_dt;
  wire [19:0] pg_multi_shifts_1_val1, pg_multi_shifts_1_val2, pg_multi_shifts_1_val3;

  D_Flip_Flop #(.trigger("high")) d_ff_1 (.D(dbg), .clk(clk2), .Qn(d_ff_1_qn));  // open: Q, preset, reset
  Register #(.trigger("high"), .width(10)) register_1 (
    .D(pg_multi_shifts_1_val1[9:0]), .en(clk1), .clk(clk1), .Q(register_1_q));  // open: clr
  Register #(.trigger("high"), .width(10)) register_2 (
    .D(pg_multi_shifts_1_val2[9:0]), .en(clk1), .clk(clk1), .Q(register_2_q));  // open: clr
  Register #(.trigger("high"), .width(10)) register_3 (
    .D(pg_multi_shifts_1_val1[19:10]), .en(clk1), .clk(clk1), .Q(register_3_q));  // open: clr
  Register #(.trigger("high"), .width(10)) register_4 (
    .D(pg_multi_shifts_1_val2[19:10]), .en(clk1), .clk(clk1), .Q(register_4_q));  // open: clr
  sr_bit_3 sr_bit_3_1 (.val(blk), .clk1(clk2), .clk2(clk1), .valout(blk_l));
  sr_bit_2 sr_bit_2_1 (.val(note), .clk1(clk2), .clk2(clk1), .valout(note_l));
  pg_multi_decoder pg_multi_decoder_1 (
    .clk1(clk1), .clk2(clk2), .multi(multi), .pg_reset(pg_reset), .multi_sel1(pg_multi_decoder_1_multi_sel1),
    .multi_sel2(pg_multi_decoder_1_multi_sel2), .multi_sel3(pg_multi_decoder_1_multi_sel3),
    .multi_sel4(pg_multi_decoder_1_multi_sel4), .pg_res_l1(pg_multi_decoder_1_pg_res_l1),
    .pg_res_l2(pg_multi_decoder_1_pg_res_l2));
  assign not_1_out = ~register_3_q;  // NOT_Gate not_1, 10 bits wide
  assign not_2_out = ~register_4_q;  // NOT_Gate not_2, 10 bits wide
  D_Flip_Flop #(.trigger("high")) d_ff_2 (
    .D(pg_multi_decoder_1_multi_sel3), .clk(clk1), .Q(d_ff_2_q));  // open: Qn, preset, reset
  Register #(.trigger("high"), .width(10)) register_5 (
    .D(not_1_out), .en(clk2), .clk(clk2), .Q(register_5_q));  // open: clr
  Register #(.trigger("high"), .width(10)) register_6 (
    .D(not_2_out), .en(clk2), .clk(clk2), .Q(register_6_q));  // open: clr
  Adder #(.width(10)) adder_1 (
    .a(register_1_q), .b(register_2_q), .out(adder_1_out), .cin(d_ff_2_q), .cout(adder_1_cout));
  sr_bit_10 sr_bit_10_1 (.val(pg_multi_shifts_1_val3[9:0]), .clk1(clk1), .clk2(clk2), .valout(sr_bit_10_1_valout));
  D_Flip_Flop #(.trigger("high")) d_ff_3 (.D(adder_1_cout), .clk(clk2), .Qn(d_ff_3_qn));  // open: Q, preset, reset
  sr_bit_10 sr_bit_10_2 (.val(pg_multi_shifts_1_val3[19:10]), .clk1(clk1), .clk2(clk2), .valout(sr_bit_10_2_valout));
  assign not_3_out = ~adder_1_out;  // NOT_Gate not_3, 10 bits wide
  Register #(.trigger("high"), .width(10)) register_7 (
    .D(sr_bit_10_1_valout), .en(clk1), .clk(clk1), .Q(register_7_q));  // open: clr
  Adder #(.width(10)) adder_2 (.a(register_5_q), .b(register_6_q), .out(adder_2_out), .cin(d_ff_3_qn));  // open: cout
  pg_fnum_block pg_fnum_block_1 (
    .clk1(clk1), .clk2(clk2), .fnum_lfo(fnum_lfo), .blk(blk_l), .fnum_block(pg_fnum_block_1_fnum_block));
  pg_detune pg_detune_1 (
    .clk1(clk1), .clk2(clk2), .blk(blk_l), .note(note_l), .detune(detune), .dt_sign(pg_detune_1_dt_sign),
    .dt_value(pg_detune_1_dt_value));
  assign not_4_out = ~adder_2_out;  // NOT_Gate not_4, 10 bits wide
  Register #(.trigger("high"), .width(10)) register_8 (
    .D(not_4_out), .en(clk1), .clk(clk1), .Q(register_8_q));  // open: clr
  Register #(.trigger("high"), .width(10)) register_9 (
    .D(sr_bit_10_2_valout), .en(clk1), .clk(clk1), .Q(register_9_q));  // open: clr
  sr_bit_10 sr_bit_10_3 (.val(not_3_out), .clk1(clk2), .clk2(clk1), .valout(sr_bit_10_3_valout));
  assign not_5_out = ~register_8_q;  // NOT_Gate not_5, 10 bits wide
  assign bit_extender_1_out = {{9{pg_multi_decoder_1_pg_res_l1}}, pg_multi_decoder_1_pg_res_l1};  // Bit_Extender bit_extender_1
  assign bit_extender_2_out = {{9{pg_multi_decoder_1_multi_sel4}}, pg_multi_decoder_1_multi_sel4};  // Bit_Extender bit_extender_2
  assign bit_extender_3_out = {{9{pg_multi_decoder_1_pg_res_l1}}, pg_multi_decoder_1_pg_res_l1};  // Bit_Extender bit_extender_3
  assign bit_extender_4_out = {{9{pg_multi_decoder_1_multi_sel4}}, pg_multi_decoder_1_multi_sel4};  // Bit_Extender bit_extender_4
  pg_freq_detune pg_freq_detune_1 (
    .clk1(clk1), .clk2(clk2), .freq(pg_fnum_block_1_fnum_block), .dt_sign(pg_detune_1_dt_sign),
    .dt_value(pg_detune_1_dt_value), .freq_dt(pg_freq_detune_1_freq_dt));
  Register #(.trigger("high"), .width(10)) register_10 (
    .D(nand_1_out), .en(clk2), .clk(clk2), .Q(register_10_q));  // open: clr
  assign nand_1_out = ~(sr_bit_10_3_valout & bit_extender_1_out);  // NAND_Gate nand_1, 10 bits wide
  Register #(.trigger("high"), .width(10)) register_11 (
    .D(nand_2_out), .en(clk2), .clk(clk2), .Q(register_11_q));  // open: clr
  assign nand_2_out = ~(register_7_q & bit_extender_2_out);  // NAND_Gate nand_2, 10 bits wide
  Register #(.trigger("high"), .width(10)) register_12 (
    .D(nand_3_out), .en(clk2), .clk(clk2), .Q(register_12_q));  // open: clr
  assign nand_3_out = ~(not_5_out & bit_extender_3_out);  // NAND_Gate nand_3, 10 bits wide
  Register #(.trigger("high"), .width(10)) register_13 (
    .D(nand_4_out), .en(clk2), .clk(clk2), .Q(register_13_q));  // open: clr
  assign nand_4_out = ~(register_9_q & bit_extender_4_out);  // NAND_Gate nand_4, 10 bits wide
  Adder #(.width(10)) adder_3 (
    .a(register_10_q), .b(register_11_q), .out(adder_3_out), .cin(1'b1), .cout(adder_3_cout));
  D_Flip_Flop #(.trigger("high")) d_ff_4 (.D(adder_3_cout), .clk(clk1), .Qn(d_ff_4_qn));  // open: Q, preset, reset
  Register #(.trigger("high"), .width(10)) register_14 (
    .D(not_6_out), .en(clk1), .clk(clk1), .Q(register_14_q));  // open: clr
  assign not_6_out = ~register_12_q;  // NOT_Gate not_6, 10 bits wide
  Register #(.trigger("high"), .width(10)) register_15 (
    .D(not_7_out), .en(clk1), .clk(clk1), .Q(register_15_q));  // open: clr
  assign not_7_out = ~register_13_q;  // NOT_Gate not_7, 10 bits wide
  Register #(.trigger("high"), .width(10)) register_16 (
    .D(not_8_out), .en(clk1), .clk(clk1), .Q(register_16_q));  // open: clr
  assign not_8_out = ~adder_3_out;  // NOT_Gate not_8, 10 bits wide
  pg_multi_shifts pg_multi_shifts_1 (
    .freq(pg_freq_detune_1_freq_dt), .mul_sel1(pg_multi_decoder_1_multi_sel1),
    .mul_sel2(pg_multi_decoder_1_multi_sel2), .val1(pg_multi_shifts_1_val1), .val2(pg_multi_shifts_1_val2),
    .val3(pg_multi_shifts_1_val3));
  Adder #(.width(10)) adder_4 (.a(register_14_q), .b(register_15_q), .out(adder_4_out), .cin(d_ff_4_qn));  // open: cout
  Register #(.trigger("high"), .width(10)) register_17 (
    .D(sr_bit_10_45_valout), .en(clk1), .clk(clk1), .Q(register_17_q));  // open: clr
  Register #(.trigger("high"), .width(10)) register_18 (
    .D(sr_bit_10_47_valout), .en(clk1), .clk(clk1), .Q(register_18_q));  // open: clr
  Register #(.trigger("high"), .width(10)) register_19 (
    .D(nand_6_out), .en(clk2), .clk(clk2), .Q(register_19_q));  // open: clr
  Register #(.trigger("high"), .width(10)) register_20 (
    .D(not_9_out), .en(clk2), .clk(clk2), .Q(register_20_q));  // open: clr
  assign not_9_out = ~register_16_q;  // NOT_Gate not_9, 10 bits wide
  Register #(.trigger("high"), .width(10)) register_21 (
    .D(not_10_out), .en(clk2), .clk(clk2), .Q(register_21_q));  // open: clr
  assign not_10_out = ~adder_4_out;  // NOT_Gate not_10, 10 bits wide
  assign bit_extender_5_out = {{9{pg_multi_decoder_1_pg_res_l2}}, pg_multi_decoder_1_pg_res_l2};  // Bit_Extender bit_extender_5
  assign bit_extender_6_out = {{9{pg_multi_decoder_1_pg_res_l2}}, pg_multi_decoder_1_pg_res_l2};  // Bit_Extender bit_extender_6
  Register #(.trigger("high"), .width(10)) register_22 (
    .D(not_11_out), .en(clk1), .clk(clk1), .Q(register_22_q));  // open: clr
  assign not_11_out = ~register_19_q;  // NOT_Gate not_11, 10 bits wide
  Adder #(.width(10)) adder_5 (
    .a(register_20_q), .b(register_24_q), .out(adder_5_out), .cin(1'b1), .cout(adder_5_cout));
  Register #(.trigger("high"), .width(10)) register_23 (
    .D(not_12_out), .en(clk1), .clk(clk1), .Q(register_23_q));  // open: clr
  assign not_12_out = ~register_21_q;  // NOT_Gate not_12, 10 bits wide
  Register #(.trigger("high"), .width(10)) register_24 (
    .D(nand_5_out), .en(clk2), .clk(clk2), .Q(register_24_q));  // open: clr
  assign nand_5_out = ~(register_17_q & bit_extender_5_out);  // NAND_Gate nand_5, 10 bits wide
  assign nand_6_out = ~(register_18_q & bit_extender_6_out);  // NAND_Gate nand_6, 10 bits wide
  assign not_13_out = ~adder_5_out;  // NOT_Gate not_13, 10 bits wide
  D_Flip_Flop #(.trigger("high")) d_ff_5 (.D(adder_5_cout), .clk(clk1), .Qn(d_ff_5_qn));  // open: Q, preset, reset
  Adder #(.width(10)) adder_6 (.a(register_23_q), .b(register_22_q), .out(adder_6_out), .cin(d_ff_5_qn));  // open: cout
  Register #(.trigger("high"), .width(10)) register_25 (
    .D(not_14_out), .en(clk2), .clk(clk2), .Q(register_25_q));  // open: clr
  assign not_14_out = ~adder_6_out;  // NOT_Gate not_14, 10 bits wide
  assign not_15_out = ~register_25_q;  // NOT_Gate not_15, 10 bits wide
  sr_bit_10 sr_bit_10_4 (.val(not_13_out), .clk1(clk1), .clk2(clk2), .valout(sr_bit_10_4_valout));
  sr_bit_10 sr_bit_10_5 (.val(sr_bit_10_48_valout), .clk1(clk1), .clk2(clk2), .valout(sr_bit_10_5_valout));
  sr_bit_10 sr_bit_10_6 (.val(not_15_out), .clk1(clk1), .clk2(clk2), .valout(sr_bit_10_6_valout));
  sr_bit_10 sr_bit_10_7 (.val(sr_bit_10_49_valout), .clk1(clk1), .clk2(clk2), .valout(sr_bit_10_7_valout));
  pg_dbg pg_dbg_1 (.clk1(clk1), .clk2(clk2), .load(d_ff_1_qn), .val(sr_bit_10_45_valout), .valout(dbg_bit));
  sr_bit_10 sr_bit_10_8 (.val(sr_bit_10_4_valout), .clk1(clk1), .clk2(clk2), .valout(sr_bit_10_8_valout));
  sr_bit_10 sr_bit_10_9 (.val(sr_bit_10_5_valout), .clk1(clk1), .clk2(clk2), .valout(sr_bit_10_9_valout));
  sr_bit_10 sr_bit_10_10 (.val(sr_bit_10_6_valout), .clk1(clk1), .clk2(clk2), .valout(sr_bit_10_10_valout));
  sr_bit_10 sr_bit_10_11 (.val(sr_bit_10_7_valout), .clk1(clk1), .clk2(clk2), .valout(sr_bit_10_11_valout));
  sr_bit_10 sr_bit_10_12 (.val(sr_bit_10_8_valout), .clk1(clk1), .clk2(clk2), .valout(sr_bit_10_12_valout));
  sr_bit_10 sr_bit_10_13 (.val(sr_bit_10_9_valout), .clk1(clk1), .clk2(clk2), .valout(sr_bit_10_13_valout));
  sr_bit_10 sr_bit_10_14 (.val(sr_bit_10_10_valout), .clk1(clk1), .clk2(clk2), .valout(sr_bit_10_14_valout));
  sr_bit_10 sr_bit_10_15 (.val(sr_bit_10_11_valout), .clk1(clk1), .clk2(clk2), .valout(sr_bit_10_15_valout));
  sr_bit_10 sr_bit_10_16 (.val(sr_bit_10_12_valout), .clk1(clk1), .clk2(clk2), .valout(sr_bit_10_16_valout));
  sr_bit_10 sr_bit_10_17 (.val(sr_bit_10_13_valout), .clk1(clk1), .clk2(clk2), .valout(sr_bit_10_17_valout));
  sr_bit_10 sr_bit_10_18 (.val(sr_bit_10_14_valout), .clk1(clk1), .clk2(clk2), .valout(sr_bit_10_18_valout));
  sr_bit_10 sr_bit_10_19 (.val(sr_bit_10_15_valout), .clk1(clk1), .clk2(clk2), .valout(sr_bit_10_19_valout));
  sr_bit_10 sr_bit_10_20 (.val(sr_bit_10_16_valout), .clk1(clk1), .clk2(clk2), .valout(sr_bit_10_20_valout));
  sr_bit_10 sr_bit_10_21 (.val(sr_bit_10_17_valout), .clk1(clk1), .clk2(clk2), .valout(sr_bit_10_21_valout));
  sr_bit_10 sr_bit_10_22 (.val(sr_bit_10_18_valout), .clk1(clk1), .clk2(clk2), .valout(sr_bit_10_22_valout));
  sr_bit_10 sr_bit_10_23 (.val(sr_bit_10_19_valout), .clk1(clk1), .clk2(clk2), .valout(sr_bit_10_23_valout));
  sr_bit_10 sr_bit_10_24 (.val(sr_bit_10_20_valout), .clk1(clk1), .clk2(clk2), .valout(sr_bit_10_24_valout));
  sr_bit_10 sr_bit_10_25 (.val(sr_bit_10_21_valout), .clk1(clk1), .clk2(clk2), .valout(sr_bit_10_25_valout));
  sr_bit_10 sr_bit_10_26 (.val(sr_bit_10_22_valout), .clk1(clk1), .clk2(clk2), .valout(sr_bit_10_26_valout));
  sr_bit_10 sr_bit_10_27 (.val(sr_bit_10_23_valout), .clk1(clk1), .clk2(clk2), .valout(sr_bit_10_27_valout));
  sr_bit_10 sr_bit_10_28 (.val(sr_bit_10_24_valout), .clk1(clk1), .clk2(clk2), .valout(sr_bit_10_28_valout));
  sr_bit_10 sr_bit_10_29 (.val(sr_bit_10_25_valout), .clk1(clk1), .clk2(clk2), .valout(sr_bit_10_29_valout));
  sr_bit_10 sr_bit_10_30 (.val(sr_bit_10_26_valout), .clk1(clk1), .clk2(clk2), .valout(sr_bit_10_30_valout));
  sr_bit_10 sr_bit_10_31 (.val(sr_bit_10_27_valout), .clk1(clk1), .clk2(clk2), .valout(phase));
  sr_bit_10 sr_bit_10_32 (.val(sr_bit_10_28_valout), .clk1(clk1), .clk2(clk2), .valout(sr_bit_10_32_valout));
  sr_bit_10 sr_bit_10_33 (.val(sr_bit_10_29_valout), .clk1(clk1), .clk2(clk2), .valout(sr_bit_10_33_valout));
  sr_bit_10 sr_bit_10_34 (.val(sr_bit_10_30_valout), .clk1(clk1), .clk2(clk2), .valout(sr_bit_10_34_valout));
  sr_bit_10 sr_bit_10_35 (.val(phase), .clk1(clk1), .clk2(clk2), .valout(sr_bit_10_35_valout));
  sr_bit_10 sr_bit_10_36 (.val(sr_bit_10_32_valout), .clk1(clk1), .clk2(clk2), .valout(sr_bit_10_36_valout));
  sr_bit_10 sr_bit_10_37 (.val(sr_bit_10_33_valout), .clk1(clk1), .clk2(clk2), .valout(sr_bit_10_37_valout));
  sr_bit_10 sr_bit_10_38 (.val(sr_bit_10_34_valout), .clk1(clk1), .clk2(clk2), .valout(sr_bit_10_38_valout));
  sr_bit_10 sr_bit_10_39 (.val(sr_bit_10_35_valout), .clk1(clk1), .clk2(clk2), .valout(sr_bit_10_39_valout));
  sr_bit_10 sr_bit_10_40 (.val(sr_bit_10_36_valout), .clk1(clk1), .clk2(clk2), .valout(sr_bit_10_40_valout));
  sr_bit_10 sr_bit_10_41 (.val(sr_bit_10_37_valout), .clk1(clk1), .clk2(clk2), .valout(sr_bit_10_41_valout));
  sr_bit_10 sr_bit_10_42 (.val(sr_bit_10_38_valout), .clk1(clk1), .clk2(clk2), .valout(sr_bit_10_42_valout));
  sr_bit_10 sr_bit_10_43 (.val(sr_bit_10_39_valout), .clk1(clk1), .clk2(clk2), .valout(sr_bit_10_43_valout));
  sr_bit_10 sr_bit_10_44 (.val(sr_bit_10_40_valout), .clk1(clk1), .clk2(clk2), .valout(sr_bit_10_44_valout));
  sr_bit_10 sr_bit_10_45 (.val(sr_bit_10_41_valout), .clk1(clk1), .clk2(clk2), .valout(sr_bit_10_45_valout));
  sr_bit_10 sr_bit_10_46 (.val(sr_bit_10_42_valout), .clk1(clk1), .clk2(clk2), .valout(sr_bit_10_46_valout));
  sr_bit_10 sr_bit_10_47 (.val(sr_bit_10_43_valout), .clk1(clk1), .clk2(clk2), .valout(sr_bit_10_47_valout));
  sr_bit_10 sr_bit_10_48 (.val(sr_bit_10_44_valout), .clk1(clk1), .clk2(clk2), .valout(sr_bit_10_48_valout));
  sr_bit_10 sr_bit_10_49 (.val(sr_bit_10_46_valout), .clk1(clk1), .clk2(clk2), .valout(sr_bit_10_49_valout));
endmodule

module pg_fnum_block (
  input  clk1,
  input  clk2,
  input  [11:0] fnum_lfo,
  input  [2:0] blk,
  output [16:0] fnum_block
);

  wire d_ff_1_qn, d_ff_2_qn, d_ff_3_qn, d_ff_4_qn, d_ff_5_qn, d_ff_6_qn, nand_1_out, nand_2_out, nand_3_out,
       nand_4_out, not_1_out, not_2_out, not_3_out, sr_bit_1_valout;
  wire [15:0] and_1_out, and_2_out, bit_extender_1_out, bit_extender_2_out, controlled_buffer_1_out;

  assign controlled_buffer_1_out = d_ff_3_qn ? {3'b000, fnum_lfo, 1'b0} : 16'bz;  // Controlled_Buffer controlled_buffer_1
  assign controlled_buffer_1_out = d_ff_4_qn ? {2'b00, fnum_lfo, 2'b00} : 16'bz;  // Controlled_Buffer controlled_buffer_2
  assign controlled_buffer_1_out = d_ff_5_qn ? {1'b0, fnum_lfo, 3'b000} : 16'bz;  // Controlled_Buffer controlled_buffer_3
  D_Flip_Flop #(.trigger("high")) d_ff_1 (.D(blk[0]), .clk(clk2), .Qn(d_ff_1_qn));  // open: Q, preset, reset
  D_Flip_Flop #(.trigger("high")) d_ff_2 (.D(blk[1]), .clk(clk2), .Qn(d_ff_2_qn));  // open: Q, preset, reset
  sr_bit sr_bit_1 (.clk1(clk2), .clk2(clk1), .val(blk[2]), .valout(sr_bit_1_valout));  // open: nvalout
  assign controlled_buffer_1_out = d_ff_6_qn ? {fnum_lfo, 4'b0000} : 16'bz;  // Controlled_Buffer controlled_buffer_4
  not not_1 (not_1_out, d_ff_1_qn);
  not not_2 (not_2_out, d_ff_2_qn);
  not not_3 (not_3_out, sr_bit_1_valout);
  nand nand_1 (nand_1_out, not_1_out, not_2_out);
  nand nand_2 (nand_2_out, d_ff_1_qn, not_2_out);
  nand nand_3 (nand_3_out, not_1_out, d_ff_2_qn);
  nand nand_4 (nand_4_out, d_ff_1_qn, d_ff_2_qn);
  assign bit_extender_1_out = {{15{not_3_out}}, not_3_out};  // Bit_Extender bit_extender_1
  assign bit_extender_2_out = {{15{sr_bit_1_valout}}, sr_bit_1_valout};  // Bit_Extender bit_extender_2
  D_Flip_Flop #(.trigger("high")) d_ff_3 (.D(nand_1_out), .clk(clk1), .Qn(d_ff_3_qn));  // open: Q, preset, reset
  D_Flip_Flop #(.trigger("high")) d_ff_4 (.D(nand_2_out), .clk(clk1), .Qn(d_ff_4_qn));  // open: Q, preset, reset
  D_Flip_Flop #(.trigger("high")) d_ff_5 (.D(nand_3_out), .clk(clk1), .Qn(d_ff_5_qn));  // open: Q, preset, reset
  D_Flip_Flop #(.trigger("high")) d_ff_6 (.D(nand_4_out), .clk(clk1), .Qn(d_ff_6_qn));  // open: Q, preset, reset
  assign and_1_out = controlled_buffer_1_out & bit_extender_1_out;  // AND_Gate and_1, 16 bits wide
  assign and_2_out = {4'b0000, controlled_buffer_1_out[15:4]} & bit_extender_2_out;  // AND_Gate and_2, 16 bits wide
  nand nand_5 (fnum_block[0], sr_bit_1_valout, controlled_buffer_1_out[3]);
  assign fnum_block[16:1] = ~(and_1_out | and_2_out);  // NOR_Gate nor_1, 16 bits wide
endmodule

module pg_detune (
  input  clk1,
  input  clk2,
  input  [2:0] blk,
  input  [1:0] note,
  input  [2:0] detune,
  output dt_sign,
  output [4:0] dt_value
);

  wire adder_1_cout, and_1_out, and_2_out, and_3_out, and_4_out, and_5_out, and_6_out, and_7_out, and_8_out,
       and_9_out, and_10_out, d_ff_7_q, nand_1_out, nand_2_out, nand_3_out, nor_1_out, nor_2_out, nor_3_out,
       nor_4_out, nor_5_out, nor_6_out, nor_7_out, nor_8_out, nor_9_out, nor_10_out, nor_11_out, nor_12_out,
       nor_13_out, nor_14_out, not_1_out, not_2_out, not_3_out, not_4_out, or_1_out, or_2_out, or_3_out,
       or_4_out, sr_bit_1_nvalout, sr_bit_2_nvalout, sr_bit_3_nvalout, sr_bit_4_valout, sr_bit_5_valout;
  wire [1:0] d_ff_5_q;
  wire [3:0] adder_1_out, d_ff_1_q, not_5_out, not_6_out, register_1_q;
  wire [4:0] bit_extender_1_out, nor_15_out;

  nand nand_1 (nand_1_out, detune[0], detune[1]);
  nor nor_1 (nor_1_out, detune[0], detune[1]);
  not not_1 (not_1_out, detune[1]);
  nor nor_2 (nor_2_out, blk[0], blk[1], blk[2]);
  sr_bit sr_bit_1 (.clk1(clk2), .clk2(clk1), .val(nor_2_out), .nvalout(sr_bit_1_nvalout));  // open: valout
  sr_bit sr_bit_2 (.clk1(clk2), .clk2(clk1), .val(note[0]), .nvalout(sr_bit_2_nvalout));  // open: valout
  sr_bit sr_bit_3 (.clk1(clk2), .clk2(clk1), .val(note[1]), .nvalout(sr_bit_3_nvalout));  // open: valout
  nand nand_2 (nand_2_out, sr_bit_1_nvalout, sr_bit_2_nvalout);
  nand nand_3 (nand_3_out, sr_bit_1_nvalout, sr_bit_3_nvalout);
  not not_2 (not_2_out, nand_2_out);
  not not_3 (not_3_out, nand_3_out);
  D_Flip_Flop #(.trigger("high")) d_ff_1 (.D(blk[0]), .clk(clk2), .Q(d_ff_1_q[0]));  // open: Qn, preset, reset
  D_Flip_Flop #(.trigger("high")) d_ff_2 (.D(blk[1]), .clk(clk2), .Q(d_ff_1_q[1]));  // open: Qn, preset, reset
  D_Flip_Flop #(.trigger("high")) d_ff_3 (.D(blk[2]), .clk(clk2), .Q(d_ff_1_q[2]));  // open: Qn, preset, reset
  D_Flip_Flop #(.trigger("high")) d_ff_4 (.D(nor_1_out), .clk(clk2), .Q(d_ff_1_q[3]));  // open: Qn, preset, reset
  D_Flip_Flop #(.trigger("high")) d_ff_5 (.D(nand_1_out), .clk(clk2), .Q(d_ff_5_q[0]));  // open: Qn, preset, reset
  D_Flip_Flop #(.trigger("high")) d_ff_6 (.D(not_1_out), .clk(clk2), .Q(d_ff_5_q[1]));  // open: Qn, preset, reset
  sr_bit sr_bit_4 (.clk1(clk2), .clk2(clk1), .val(nor_1_out), .valout(sr_bit_4_valout));  // open: nvalout
  nor nor_3 (nor_3_out, nand_2_out, not_3_out, register_1_q[0]);
  nor nor_4 (nor_4_out, not_2_out, nand_3_out, register_1_q[0]);
  nor nor_5 (nor_5_out, nand_2_out, nand_3_out, register_1_q[0]);
  nor nor_6 (nor_6_out, not_2_out, not_3_out, not_6_out[0]);
  nor nor_7 (nor_7_out, nand_2_out, not_3_out, not_6_out[0]);
  nor nor_8 (nor_8_out, not_2_out, nand_3_out, not_6_out[0]);
  nor nor_9 (nor_9_out, nand_2_out, nand_3_out, not_6_out[0]);
  not not_4 (not_4_out, 1'b1);
  Adder #(.width(4)) adder_1 (
    .a(d_ff_1_q), .b({2'b11, d_ff_5_q}), .out(adder_1_out), .cin(not_4_out), .cout(adder_1_cout));
  Register #(.trigger("high"), .width(4)) register_1 (
    .D(not_5_out), .en(clk1), .clk(clk1), .Q(register_1_q));  // open: clr
  assign not_5_out = ~adder_1_out;  // NOT_Gate not_5, 4 bits wide
  or or_1 (or_1_out, nor_3_out, nor_4_out, nor_8_out, nor_9_out);
  or or_2 (or_2_out, nor_4_out, nor_6_out, nor_8_out);
  or or_3 (or_3_out, nor_5_out, nor_6_out, nor_9_out);
  or or_4 (or_4_out, nor_7_out, nor_8_out, nor_9_out);
  D_Flip_Flop #(.trigger("high")) d_ff_7 (.D(adder_1_cout), .clk(clk1), .Q(d_ff_7_q));  // open: Qn, preset, reset
  assign not_6_out = ~register_1_q;  // NOT_Gate not_6, 4 bits wide
  not not_7 (register_1_q[1], d_ff_7_q);
  sr_bit sr_bit_5 (.clk1(clk2), .clk2(clk1), .val(detune[2]), .valout(sr_bit_5_valout));  // open: nvalout
  nor nor_10 (nor_10_out, sr_bit_4_valout, not_6_out[1], register_1_q[2], register_1_q[3], d_ff_7_q);
  nor nor_11 (nor_11_out, sr_bit_4_valout, register_1_q[1], register_1_q[2], register_1_q[3], d_ff_7_q);
  nor nor_12 (nor_12_out, sr_bit_4_valout, not_6_out[1], not_6_out[2], not_6_out[3], register_1_q[1]);
  nor nor_13 (nor_13_out, sr_bit_4_valout, register_1_q[1], not_6_out[2], not_6_out[3], register_1_q[1]);
  nor nor_14 (nor_14_out, sr_bit_4_valout, not_6_out[1], register_1_q[2], not_6_out[3], register_1_q[1]);
  and and_1 (and_1_out, or_1_out, nor_10_out);
  and and_2 (and_2_out, or_2_out, nor_10_out);
  and and_3 (and_3_out, or_3_out, nor_10_out);
  and and_4 (and_4_out, or_4_out, nor_10_out);
  and and_5 (and_5_out, or_2_out, nor_11_out);
  and and_6 (and_6_out, or_3_out, nor_11_out);
  and and_7 (and_7_out, or_4_out, nor_11_out);
  and and_8 (and_8_out, or_3_out, nor_12_out);
  and and_9 (and_9_out, or_4_out, nor_12_out);
  and and_10 (and_10_out, or_4_out, nor_13_out);
  not not_8 (dt_sign, sr_bit_5_valout);
  nor nor_15 (nor_15_out[0], and_1_out, and_5_out, and_8_out, and_10_out, nor_14_out);
  nor nor_16 (nor_15_out[1], and_2_out, and_6_out, and_9_out, nor_13_out);
  nor nor_17 (nor_15_out[2], and_3_out, and_7_out, nor_12_out);
  nor nor_18 (nor_15_out[3], and_4_out, nor_11_out);
  not not_9 (nor_15_out[4], nor_10_out);
  assign bit_extender_1_out = {{4{sr_bit_5_valout}}, sr_bit_5_valout};  // Bit_Extender bit_extender_1
  assign dt_value = bit_extender_1_out ^ nor_15_out;  // XOR_Gate xor_1, 5 bits wide
endmodule

module pg_freq_detune (
  input  clk1,
  input  clk2,
  input  [16:0] freq,
  input  dt_sign,
  input  [4:0] dt_value,
  output [16:0] freq_dt
);

  wire adder_1_cout, d_ff_1_q, d_ff_2_qn, d_ff_3_q, not_1_out;
  wire [7:0] adder_2_out, bit_extender_1_out, not_3_out, not_4_out, register_3_q, register_4_q, register_5_q,
       register_6_q;
  wire [8:0] adder_1_out, not_2_out, register_1_q, register_2_q;

  D_Flip_Flop #(.trigger("high")) d_ff_1 (.D(dt_sign), .clk(clk2), .Q(d_ff_1_q));  // open: Qn, preset, reset
  Register #(.trigger("high"), .width(9)) register_1 (
    .D({{4{dt_sign}}, dt_value}), .en(clk2), .clk(clk2), .Q(register_1_q));  // open: clr
  Register #(.trigger("high"), .width(9)) register_2 (
    .D(freq[8:0]), .en(clk2), .clk(clk2), .Q(register_2_q));  // open: clr
  D_Flip_Flop #(.trigger("high")) d_ff_2 (.D(dt_sign), .clk(clk2), .Qn(d_ff_2_qn));  // open: Q, preset, reset
  Register #(.trigger("high")) register_3 (.D(freq[16:9]), .en(clk2), .clk(clk2), .Q(register_3_q));  // open: clr
  not not_1 (not_1_out, adder_1_cout);
  Register #(.trigger("high")) register_4 (
    .D(bit_extender_1_out), .en(clk1), .clk(clk1), .Q(register_4_q));  // open: clr
  assign bit_extender_1_out = {{7{d_ff_2_qn}}, d_ff_2_qn};  // Bit_Extender bit_extender_1
  Register #(.trigger("high")) register_5 (.D(register_3_q), .en(clk1), .clk(clk1), .Q(register_5_q));  // open: clr
  Adder #(.width(9)) adder_1 (
    .a(register_1_q), .b(register_2_q), .out(adder_1_out), .cin(d_ff_1_q), .cout(adder_1_cout));
  D_Flip_Flop #(.trigger("high")) d_ff_3 (.D(not_1_out), .clk(clk1), .Q(d_ff_3_q));  // open: Qn, preset, reset
  assign not_2_out = ~adder_1_out;  // NOT_Gate not_2, 9 bits wide
  Adder adder_2 (.a(register_4_q), .b(not_3_out), .out(adder_2_out), .cin(d_ff_3_q));  // open: cout
  assign not_3_out = ~register_5_q;  // NOT_Gate not_3, 8 bits wide
  assign not_4_out = ~adder_2_out;  // NOT_Gate not_4, 8 bits wide
  Register #(.trigger("high")) register_6 (.D(not_4_out), .en(clk2), .clk(clk2), .Q(register_6_q));  // open: clr
  sr_bit_9 sr_bit_9_1 (.val(not_2_out), .clk1(clk1), .clk2(clk2), .valout(freq_dt[8:0]));
  assign freq_dt[16:9] = ~register_6_q;  // NOT_Gate not_5, 8 bits wide
endmodule

module sr_bit_9 (
  input  [8:0] val,
  input  clk1,
  input  clk2,
  output [8:0] valout
);

  wire [8:0] register_1_q;

  Register #(.trigger("high"), .width(9)) register_1 (.D(val), .en(clk1), .clk(clk1), .Q(register_1_q));  // open: clr
  Register #(.trigger("high"), .width(9)) register_2 (
    .D(register_1_q), .en(clk2), .clk(clk2), .Q(valout));  // open: clr
endmodule

module pg_multi_decoder (
  input  clk1,
  input  clk2,
  input  [3:0] multi,
  input  pg_reset,
  output [2:0] multi_sel1,
  output [4:0] multi_sel2,
  output multi_sel3,
  output multi_sel4,
  output pg_res_l1,
  output pg_res_l2
);

  wire d_ff_1_qn, d_ff_10_qn, nand_1_out, nor_1_out, nor_2_out, nor_3_out, nor_4_out, nor_5_out, nor_6_out,
       nor_7_out, nor_8_out, nor_9_out, nor_10_out, nor_11_out, nor_12_out, nor_13_out, nor_14_out,
       nor_15_out, nor_16_out, nor_17_out, nor_18_out, nor_19_out, nor_20_out, nor_21_out, nor_22_out,
       not_3_out, not_4_out, not_5_out, not_6_out, sr_bit_1_valout;
  wire [3:0] not_1_out, not_2_out, register_1_q;

  Register #(.trigger("high"), .width(4)) register_1 (.D(multi), .en(clk1), .clk(clk1), .Q(register_1_q));  // open: clr
  D_Flip_Flop #(.trigger("high")) d_ff_1 (.D(pg_reset), .clk(clk2), .Qn(d_ff_1_qn));  // open: Q, preset, reset
  assign not_1_out = ~register_1_q;  // NOT_Gate not_1, 4 bits wide
  assign not_2_out = ~not_1_out;  // NOT_Gate not_2, 4 bits wide
  nor nor_1 (nor_1_out, not_2_out[0], not_2_out[1], not_2_out[2], not_2_out[3]);
  nor nor_2 (nor_2_out, not_1_out[0], not_2_out[1], not_2_out[2], not_2_out[3]);
  nor nor_3 (nor_3_out, not_2_out[0], not_1_out[1], not_2_out[2], not_2_out[3]);
  nor nor_4 (nor_4_out, not_1_out[0], not_1_out[1], not_2_out[2], not_2_out[3]);
  nor nor_5 (nor_5_out, not_2_out[0], not_2_out[1], not_1_out[2], not_2_out[3]);
  nor nor_6 (nor_6_out, not_1_out[0], not_2_out[1], not_1_out[2], not_2_out[3]);
  nor nor_7 (nor_7_out, not_2_out[0], not_1_out[1], not_1_out[2], not_2_out[3]);
  nor nor_8 (nor_8_out, not_1_out[0], not_1_out[1], not_1_out[2], not_2_out[3]);
  nor nor_9 (nor_9_out, not_2_out[0], not_2_out[1], not_2_out[2], not_1_out[3]);
  nor nor_10 (nor_10_out, not_1_out[0], not_2_out[1], not_2_out[2], not_1_out[3]);
  nor nor_11 (nor_11_out, not_2_out[0], not_1_out[1], not_2_out[2], not_1_out[3]);
  nor nor_12 (nor_12_out, not_1_out[0], not_1_out[1], not_2_out[2], not_1_out[3]);
  nor nor_13 (nor_13_out, not_2_out[0], not_2_out[1], not_1_out[2], not_1_out[3]);
  nor nor_14 (nor_14_out, not_1_out[0], not_2_out[1], not_1_out[2], not_1_out[3]);
  nor nor_15 (nor_15_out, not_2_out[0], not_1_out[1], not_1_out[2], not_1_out[3]);
  nor nor_16 (nor_16_out, not_1_out[0], not_1_out[1], not_1_out[2], not_1_out[3]);
  not not_3 (not_3_out, nor_16_out);
  not not_4 (not_4_out, nor_15_out);
  nor nor_17 (nor_17_out, nor_3_out, nor_4_out, nor_7_out, nor_8_out, nor_11_out, nor_12_out);
  nor nor_18 (nor_18_out, nor_2_out, nor_4_out, nor_6_out, nor_8_out, nor_10_out, nor_12_out, nor_14_out);
  nor nor_19 (nor_19_out, nor_13_out, nor_14_out);
  not not_5 (not_5_out, nor_1_out);
  nor nor_20 (nor_20_out, nor_5_out, nor_6_out, nor_7_out, nor_8_out);
  nor nor_21 (nor_21_out, nor_9_out, nor_10_out, nor_11_out, nor_12_out, nor_13_out, nor_14_out);
  nor nor_22 (nor_22_out, nor_15_out, nor_16_out);
  D_Flip_Flop #(.trigger("high")) d_ff_2 (.D(not_3_out), .clk(clk2), .Qn(multi_sel2[1]));  // open: Q, preset, reset
  D_Flip_Flop #(.trigger("high")) d_ff_3 (.D(not_4_out), .clk(clk2), .Qn(multi_sel2[3]));  // open: Q, preset, reset
  D_Flip_Flop #(.trigger("high")) d_ff_4 (.D(nor_17_out), .clk(clk2), .Qn(multi_sel2[2]));  // open: Q, preset, reset
  D_Flip_Flop #(.trigger("high")) d_ff_5 (.D(nor_19_out), .clk(clk2), .Qn(multi_sel2[4]));  // open: Q, preset, reset
  D_Flip_Flop #(.trigger("high")) d_ff_6 (.D(not_5_out), .clk(clk2), .Qn(multi_sel2[0]));  // open: Q, preset, reset
  D_Flip_Flop #(.trigger("high")) d_ff_7 (.D(nor_20_out), .clk(clk2), .Qn(multi_sel1[2]));  // open: Q, preset, reset
  D_Flip_Flop #(.trigger("high")) d_ff_8 (.D(nor_21_out), .clk(clk2), .Qn(multi_sel1[1]));  // open: Q, preset, reset
  D_Flip_Flop #(.trigger("high")) d_ff_9 (.D(nor_22_out), .clk(clk2), .Qn(multi_sel1[0]));  // open: Q, preset, reset
  sr_bit sr_bit_1 (.clk1(clk2), .clk2(clk1), .val(nor_18_out), .valout(sr_bit_1_valout));  // open: nvalout
  D_Flip_Flop #(.trigger("high")) d_ff_10 (.D(sr_bit_1_valout), .clk(clk2), .Qn(d_ff_10_qn));  // open: Q, preset, reset
  nand nand_1 (nand_1_out, d_ff_1_qn, d_ff_10_qn);
  not not_6 (not_6_out, d_ff_1_qn);
  D_Flip_Flop #(.trigger("high")) d_ff_11 (.D(nand_1_out), .clk(clk1), .Qn(multi_sel4));  // open: Q, preset, reset
  D_Flip_Flop #(.trigger("high")) d_ff_12 (.D(not_6_out), .clk(clk1), .Qn(pg_res_l1));  // open: Q, preset, reset
  nor nor_23 (multi_sel3, multi_sel2[1], multi_sel2[3]);
  sr_bit sr_bit_2 (.clk1(clk2), .clk2(clk1), .val(pg_res_l1), .valout(pg_res_l2));  // open: nvalout
endmodule

module pg_multi_shifts (
  input  [16:0] freq,
  input  [2:0] mul_sel1,
  input  [4:0] mul_sel2,
  output [19:0] val1,
  output [19:0] val2,
  output [19:0] val3
);

  wire [17:0] and_1_out, and_2_out, and_3_out, bit_extender_1_out, bit_extender_2_out, bit_extender_3_out,
       not_1_out;
  wire [19:0] and_4_out, and_5_out, and_6_out, and_7_out, and_8_out, bit_extender_4_out, bit_extender_5_out,
       bit_extender_6_out, bit_extender_7_out, bit_extender_8_out;

  assign not_1_out = ~{1'b0, freq};  // NOT_Gate not_1, 18 bits wide
  assign bit_extender_1_out = {{17{mul_sel1[2]}}, mul_sel1[2]};  // Bit_Extender bit_extender_1
  assign bit_extender_2_out = {{17{mul_sel1[1]}}, mul_sel1[1]};  // Bit_Extender bit_extender_2
  assign bit_extender_3_out = {{17{mul_sel1[0]}}, mul_sel1[0]};  // Bit_Extender bit_extender_3
  assign and_1_out = {1'b0, freq} & bit_extender_1_out;  // AND_Gate and_1, 18 bits wide
  assign and_2_out = {freq, 1'b0} & bit_extender_2_out;  // AND_Gate and_2, 18 bits wide
  assign and_3_out = {freq[15:0], 2'b00} & bit_extender_3_out;  // AND_Gate and_3, 18 bits wide
  assign val1[19:2] = ~(and_1_out | and_2_out | and_3_out);  // NOR_Gate nor_1, 18 bits wide
  assign bit_extender_4_out = {{19{mul_sel2[0]}}, mul_sel2[0]};  // Bit_Extender bit_extender_4
  assign bit_extender_5_out = {{19{mul_sel2[1]}}, mul_sel2[1]};  // Bit_Extender bit_extender_5
  assign bit_extender_6_out = {{19{mul_sel2[2]}}, mul_sel2[2]};  // Bit_Extender bit_extender_6
  assign bit_extender_7_out = {{19{mul_sel2[3]}}, mul_sel2[3]};  // Bit_Extender bit_extender_7
  assign bit_extender_8_out = {{19{mul_sel2[4]}}, mul_sel2[4]};  // Bit_Extender bit_extender_8
  assign and_4_out = {4'b0000, freq[16:1]} & bit_extender_4_out;  // AND_Gate and_4, 20 bits wide
  assign and_5_out = {2'b11, not_1_out} & bit_extender_5_out;  // AND_Gate and_5, 20 bits wide
  assign and_6_out = {2'b00, freq, 1'b0} & bit_extender_6_out;  // AND_Gate and_6, 20 bits wide
  assign and_7_out = {1'b1, not_1_out, 1'b1} & bit_extender_7_out;  // AND_Gate and_7, 20 bits wide
  assign and_8_out = {1'b0, freq, 2'b00} & bit_extender_8_out;  // AND_Gate and_8, 20 bits wide
  assign val2 = ~(and_4_out | and_5_out | and_6_out | and_7_out | and_8_out);  // NOR_Gate nor_2, 20 bits wide

  assign val1[1:0] = 2'b11;
  assign val3 = {3'b000, freq};
endmodule

module sr_bit_10 (
  input  [9:0] val,
  input  clk1,
  input  clk2,
  output [9:0] valout
);

  wire [9:0] register_1_q;

  Register #(.trigger("high"), .width(10)) register_1 (.D(val), .en(clk1), .clk(clk1), .Q(register_1_q));  // open: clr
  Register #(.trigger("high"), .width(10)) register_2 (
    .D(register_1_q), .en(clk2), .clk(clk2), .Q(valout));  // open: clr
endmodule

module dbg_bit (
  input  clk1,
  input  clk2,
  input  val,
  input  load,
  input  prev,
  output valout
);

  wire and_1_out, d_ff_1_q, nor_1_out;

  and and_1 (and_1_out, val, load);
  D_Flip_Flop #(.trigger("high")) d_ff_1 (.D(prev), .clk(clk2), .Q(d_ff_1_q));  // open: Qn, preset, reset
  nor nor_1 (nor_1_out, and_1_out, d_ff_1_q);
  D_Flip_Flop #(.trigger("high")) d_ff_2 (.D(nor_1_out), .clk(clk1), .Qn(valout));  // open: Q, preset, reset
endmodule

module pg_dbg (
  input  clk1,
  input  clk2,
  input  load,
  input  [9:0] val,
  output valout
);

  wire dbg_bit_1_valout, dbg_bit_2_valout, dbg_bit_3_valout, dbg_bit_4_valout, dbg_bit_5_valout,
       dbg_bit_6_valout, dbg_bit_7_valout, dbg_bit_8_valout, dbg_bit_9_valout, dbg_bit_10_valout;

  dbg_bit dbg_bit_1 (.clk1(clk1), .clk2(clk2), .val(val[9]), .load(load), .prev(1'b0), .valout(dbg_bit_1_valout));
  dbg_bit dbg_bit_2 (
    .clk1(clk1), .clk2(clk2), .val(val[8]), .load(load), .prev(dbg_bit_1_valout), .valout(dbg_bit_2_valout));
  dbg_bit dbg_bit_3 (
    .clk1(clk1), .clk2(clk2), .val(val[7]), .load(load), .prev(dbg_bit_2_valout), .valout(dbg_bit_3_valout));
  dbg_bit dbg_bit_4 (
    .clk1(clk1), .clk2(clk2), .val(val[6]), .load(load), .prev(dbg_bit_3_valout), .valout(dbg_bit_4_valout));
  dbg_bit dbg_bit_5 (
    .clk1(clk1), .clk2(clk2), .val(val[5]), .load(load), .prev(dbg_bit_4_valout), .valout(dbg_bit_5_valout));
  dbg_bit dbg_bit_6 (
    .clk1(clk1), .clk2(clk2), .val(val[4]), .load(load), .prev(dbg_bit_5_valout), .valout(dbg_bit_6_valout));
  dbg_bit dbg_bit_7 (
    .clk1(clk1), .clk2(clk2), .val(val[3]), .load(load), .prev(dbg_bit_6_valout), .valout(dbg_bit_7_valout));
  dbg_bit dbg_bit_8 (
    .clk1(clk1), .clk2(clk2), .val(val[2]), .load(load), .prev(dbg_bit_7_valout), .valout(dbg_bit_8_valout));
  dbg_bit dbg_bit_9 (
    .clk1(clk1), .clk2(clk2), .val(val[1]), .load(load), .prev(dbg_bit_8_valout), .valout(dbg_bit_9_valout));
  dbg_bit dbg_bit_10 (
    .clk1(clk1), .clk2(clk2), .val(val[0]), .load(load), .prev(dbg_bit_9_valout), .valout(dbg_bit_10_valout));
  not not_1 (valout, dbg_bit_10_valout);
endmodule
